// Logisim project computer.circ as structural Verilog: 28 circuits, main circuit main_expanded
module main_expanded (
  input  [1:0] in_1,
  input  [1:0] in_2,
  input  MANUAL_CLK,
  input  CLK_SWITCH,
  input  [1:0] in_5,
  input  in_6,
  input  in_7,
  input  in_8,
  input  in_9,
  input  in_10
);

  wire ALU_CARRY_IN0, ALU_LOGIC, and_2_out, and_3_out, and_4_out, and_5_out, and_6_out, and_9_out,
       and_10_out, and_11_out, and_12_out, and_13_out, and_14_out, and_15_out, AUTO_CLK, CLK, CLK16,
       clock_1_out, decoder_1_out0, decoder_1_out1, decoder_1_out2, decoder_1_out3, decoder_1_out4,
       decoder_1_out5, decoder_1_out6, decoder_1_out7, decoder_1_out9, decoder_1_out10, decoder_1_out11,
       decoder_1_out15, EQUAL, FAST_CLK, IR2_pin12, IR2_pin13, IR2_pin14, IR2_pin15, IR2_pin16, IR2_pin17,
       IR2_pin18, IR2_pin19, keyboard_1_avail, MAR_CNT, MEM_WRITE, n7400_2_pin11, n7404_1_pin10,
       n7404_1_pin11, n7408_1_pin1, n7419_1_pin1, n7419_1_pin2, n7424_1_pin3, n7424_1_pin6, n7424_1_pin12,
       n7432_1_pin3, n7432_1_pin6, n7432_1_pin8, n7432_1_pin11, n7432_2_pin3, n7432_2_pin4, n7432_3_pin4,
       n7432_3_pin6, n7432_4_pin3, n74138_1_pin4, n74138_1_pin5, n74138_1_pin6, n74138_1_pin7, n74138_1_pin9,
       n74138_2_pin5, n74138_2_pin6, n74138_3_pin5, n74138_3_pin6, n74138_4_pin4, n74138_5_pin4,
       n74138_6_pin4, n74138_6_pin5, n74138_6_pin6, n74138_6_pin7, n74138_6_pin9, n74138_6_pin10,
       n74138_6_pin11, n74138_6_pin12, n74138_6_pin13, n74138_6_pin14, n74138_6_pin15, n74139_1_pin1,
       n74139_1_pin15, n74151_1_pin4, n74151_1_pin7, n74157_1_pin15, n74161_1_pin3, n74161_1_pin4,
       n74161_1_pin5, n74161_1_pin6, n74161_1_pin7, n74161_1_pin10, n74161_2_pin7, n74161_2_pin10,
       n74161_3_pin7, n74161_3_pin10, n74161_4_pin7, n74161_4_pin10, n74161_5_pin7, n74161_5_pin10,
       n74161_6_pin7, n74161_6_pin10, n74161_7_pin7, n74161_7_pin10, n74161_8_pin7, n74161_9_pin7,
       n74181_2_p1, n74181_2_p2, n74181_2_p19, n74181_3_p1, n74245_1_pin1, n74245_2_pin1, n74245_3_pin1,
       n74245_4_pin1, n74245_5_pin1, n74245_6_pin1, n74245_7_pin1, n74245_8_pin1, n74245_9_pin1,
       n74245_10_pin1, n74245_11_pin1, n74245_12_pin1, n74299_1_pin11, n74299_1_pin18, n74377_3_pin14,
       n74377_3_pin17, n74377_3_pin18, nA_BOUT_EN, nA_WRITE, nA_ZERO, nABUS_MSB, nABUS_TO_BUS_HIGH,
       nABUS_TO_BUS_LOW, nALU_CARRY_IN0, nALU_S0, nB_BOUT_EN, nB_WRITE, nCARRY, nCLK, nF_BOUT_EN, nFAST_CLK,
       nFLAG_BOUT, nFLAG_REG_WRITE, nFLAG_WRITE_BUS, nHALT, nIR2_WRITE, nIR_WRITE, nKEYB_BOUT, nMAR_AOUT,
       nMAR_CNT, nMAR_LOAD_HIGH, nMAR_LOAD_LOW, nMEM_READ, nMEM_WRITE, not_2_out, not_6_out, not_7_out,
       not_8_out, not_9_out, not_10_out, not_11_out, not_12_out, not_13_out, not_14_out, not_15_out,
       not_16_out, not_17_out, not_18_out, not_19_out, not_20_out, not_21_out, not_22_out, not_23_out,
       not_24_out, not_25_out, not_26_out, not_27_out, not_28_out, nPC_AOUT, nPC_LOAD_EN, nPC_LOAD_HIGH,
       nPC_LOAD_HIGH_ROM, nPC_LOAD_LOW, nPC_LOAD_LOW_ROM, nRAM_WE, nRESET, nRESET_MICRO, nSP_AOUT, nSP_CNT,
       nSP_CNTDOWN, nSP_CNTUP, nSP_LOAD_HIGH, nSP_LOAD_LOW, nSWITCH_CLK, nVRAM_READ, nVRAM_WRITE, nX_BOUT,
       nX_SHIFT_LEFT, nX_SHIFT_RIGHT, nX_WRITE, nY_BOUT, nY_SHIFT_LEFT, nY_SHIFT_RIGHT, nY_WRITE, nZ_BOUT,
       nZ_WRITE, or_1_out, or_2_out, or_3_out, or_4_out, or_5_out, or_6_out, or_7_out, or_8_out, or_9_out,
       or_10_out, or_11_out, or_12_out, or_13_out, or_14_out, PC_CNT, PC_LOAD_EN, ROM_nCE,
       t74hc191_1_max_min, t74hc191_1_nrco, t74hc191_2_max_min, t74hc191_2_nrco, t74hc191_3_max_min,
       t74hc191_3_nrco, t74hc191_4_max_min, t74hc191_4_nrco, X_LEFT_FLAG, X_pin11, X_pin18, X_RIGHT_FLAG,
       X_S0, X_S1, xor_1_out, Y_pin11, Y_pin18, Y_S0, Y_S1, Z_WRITE;
  wire [2:0] FLAG_SELECT;
  wire [3:0] ALU_S, FLG_BUS_MUX_OUT, PC_Q0, PC_Q1, PC_Q2, PC_Q3, UCODE_REG0_0, UCODE_REG0_1, UCODE_REG1_0;
  wire [6:0] keyboard_1_data;
  wire [7:0] ALU_A, ALU_B, BBUS, bit_extender_1_out, dipswitch_1_sw8, F, IR, Q_FLAGS, UCODE_ROM0, UCODE_ROM1;
  wire [9:0] synced_cpu_vga_1_x, synced_cpu_vga_1_y;
  wire [15:0] ABUS, dipswitch_2_sw16, MAR_ADDR, SP_ADDR, synced_cpu_vga_1_color;
  wire [16:1] UCODE_ADDR;

  Button #(.press("passive")) RE (.out(nRESET));
  _74138 #(.ShowInternalStructure("true")) u_74138_1 (
    .pin1(FLAG_SELECT[0]), .pin2(FLAG_SELECT[1]), .pin3(FLAG_SELECT[2]), .pin4(n74138_1_pin4),
    .pin5(n74138_1_pin5), .pin6(n74138_1_pin6), .pin7(n74138_1_pin7), .pin15(nX_SHIFT_LEFT),
    .pin14(nX_SHIFT_RIGHT), .pin13(nY_SHIFT_LEFT), .pin12(nY_SHIFT_RIGHT), .pin11(nVRAM_WRITE),
    .pin10(nVRAM_READ), .pin9(n74138_1_pin9));
  _74139 #(.ShowInternalStructure("true")) u_74139_1 (
    .pin1(n74139_1_pin1), .pin2(UCODE_REG1_0[0]), .pin3(UCODE_REG1_0[1]), .pin5(nPC_AOUT), .pin6(nMAR_AOUT),
    .pin7(nSP_AOUT), .pin15(n74139_1_pin15), .pin14(UCODE_REG1_0[2]), .pin13(UCODE_REG1_0[3]),
    .pin11(nFLAG_REG_WRITE), .pin10(nRESET_MICRO), .pin9(n74138_1_pin5));  // open: pin4, pin12
  _7419 #(.ShowInternalStructure("true")) u_7419_1 (
    .pin1(n7419_1_pin1), .pin2(n7419_1_pin2), .pin3(n7419_1_pin2), .pin4(nCLK), .pin5(nCLK), .pin6(CLK),
    .pin13(CLK_SWITCH), .pin12(nSWITCH_CLK), .pin11(FAST_CLK), .pin10(nFAST_CLK), .pin9(nFAST_CLK),
    .pin8(n7419_1_pin1));
  _74138 #(.ShowInternalStructure("true")) u_74138_2 (
    .pin1(UCODE_REG0_1[0]), .pin2(UCODE_REG0_1[1]), .pin3(UCODE_REG0_1[2]), .pin4(UCODE_REG0_1[3]),
    .pin5(n74138_2_pin5), .pin6(n74138_2_pin6), .pin7(nZ_WRITE), .pin14(nIR2_WRITE), .pin13(nSP_LOAD_HIGH),
    .pin12(nSP_LOAD_LOW), .pin11(nMAR_LOAD_HIGH), .pin10(nMAR_LOAD_LOW), .pin9(nMEM_WRITE));  // open: pin15
  _7419 #(.ShowInternalStructure("true")) u_7419_2 (
    .pin1(nZ_WRITE), .pin2(Z_WRITE));  // open: pin3, pin4, pin5, pin6, pin13, pin12, pin11, pin10, pin9, pin8
  _7424 #(.ShowInternalStructure("true")) u_7424_1 (
    .pin1(CLK_SWITCH), .pin2(MANUAL_CLK), .pin3(n7424_1_pin3), .pin4(nSWITCH_CLK), .pin5(AUTO_CLK),
    .pin6(n7424_1_pin6), .pin13(nHALT), .pin12(n7424_1_pin12), .pin11(FAST_CLK), .pin10(n7424_1_pin3),
    .pin9(n7424_1_pin6), .pin8(n7424_1_pin12));
  _74161 #(.ShowInternalStructure("true")) u_74161_1 (
    .pin1(nRESET), .pin2(CLK), .pin3(n74161_1_pin3), .pin4(n74161_1_pin4), .pin5(n74161_1_pin5),
    .pin6(n74161_1_pin6), .pin7(n74161_1_pin7), .pin14(UCODE_ADDR[13]), .pin13(UCODE_ADDR[14]),
    .pin12(UCODE_ADDR[15]), .pin11(UCODE_ADDR[16]), .pin10(n74161_1_pin10), .pin9(nRESET_MICRO));  // open: pin15
  Decoder #(.select(4)) decoder_1 (
    .out0(decoder_1_out0), .out1(decoder_1_out1), .out2(decoder_1_out2), .out3(decoder_1_out3),
    .out4(decoder_1_out4), .out5(decoder_1_out5), .out6(decoder_1_out6), .out7(decoder_1_out7),
    .out9(decoder_1_out9), .out10(decoder_1_out10), .out11(decoder_1_out11), .out15(decoder_1_out15),
    .sel({IR[7], ALU_LOGIC, ALU_S[3], IR[4]}));  // open: out8, out12, out13, out14, en
  // Probe on {IR[7], ALU_LOGIC, ALU_S[3], IR[4]}
  SST39SF010A sst39sf010a_1 (
    .nOE(1'b0), .nCE(1'b0), .ROM_SELECT(in_1), .A0(CLK16), .A1(UCODE_ADDR[1]), .A2(UCODE_ADDR[2]),
    .A3(UCODE_ADDR[3]), .A4(UCODE_ADDR[4]), .A5(IR[3]), .A6(IR[2]), .A7(IR[1]), .A8(IR[4]), .A9(ALU_S[3]),
    .A10(IR[7]), .A11(ALU_LOGIC), .A12(IR[0]), .A13(UCODE_ADDR[13]), .A14(UCODE_ADDR[14]),
    .A15(UCODE_ADDR[15]), .A16(UCODE_ADDR[16]), .O0(UCODE_ROM1[0]), .O1(UCODE_ROM1[1]), .O2(UCODE_ROM1[2]),
    .O3(UCODE_ROM1[3]), .O4(UCODE_ROM1[4]), .O5(UCODE_ROM1[5]), .O6(UCODE_ROM1[6]), .O7(UCODE_ROM1[7]));
  _74138 #(.ShowInternalStructure("true")) u_74138_3 (
    .pin1(UCODE_REG0_0[0]), .pin2(UCODE_REG0_0[1]), .pin3(UCODE_REG0_0[2]), .pin4(UCODE_REG0_0[3]),
    .pin5(n74138_3_pin5), .pin6(n74138_3_pin6), .pin7(nSP_CNTDOWN), .pin14(nMEM_READ),
    .pin13(nABUS_TO_BUS_LOW), .pin12(nABUS_TO_BUS_HIGH), .pin11(nMAR_CNT), .pin10(nHALT), .pin9(nSP_CNTUP));  // open: pin15
  // LedBar #(.inputtype("row")) ledbar_1: pin names not known; wires that end beside it: BBUS
  DipSwitch dipswitch_1 (
    .sw1(dipswitch_1_sw8[7]), .sw2(dipswitch_1_sw8[6]), .sw3(dipswitch_1_sw8[5]), .sw4(dipswitch_1_sw8[4]),
    .sw5(dipswitch_1_sw8[3]), .sw6(dipswitch_1_sw8[2]), .sw7(dipswitch_1_sw8[1]), .sw8(dipswitch_1_sw8[0]));
  // Probe on BBUS
  // Probe on BBUS
  SST39SF010A sst39sf010a_2 (
    .nOE(1'b0), .nCE(1'b0), .ROM_SELECT(in_2), .A0(CLK16), .A1(UCODE_ADDR[1]), .A2(UCODE_ADDR[2]),
    .A3(UCODE_ADDR[3]), .A4(UCODE_ADDR[4]), .A5(IR[3]), .A6(IR[2]), .A7(IR[1]), .A8(IR[4]), .A9(ALU_S[3]),
    .A10(IR[7]), .A11(ALU_LOGIC), .A12(IR[0]), .A13(UCODE_ADDR[13]), .A14(UCODE_ADDR[14]),
    .A15(UCODE_ADDR[15]), .A16(UCODE_ADDR[16]), .O0(UCODE_ROM0[0]), .O1(UCODE_ROM0[1]), .O2(UCODE_ROM0[2]),
    .O3(UCODE_ROM0[3]), .O4(UCODE_ROM0[4]), .O5(UCODE_ROM0[5]), .O6(UCODE_ROM0[6]), .O7(UCODE_ROM0[7]));
  _74273 #(.ShowInternalStructure("true")) u_74273_1 (
    .pin1(nRESET), .pin2(UCODE_REG1_0[0]), .pin3(UCODE_ROM1[0]), .pin4(UCODE_ROM1[1]),
    .pin5(UCODE_REG1_0[1]), .pin6(UCODE_REG1_0[2]), .pin7(UCODE_ROM1[2]), .pin8(UCODE_ROM1[3]),
    .pin9(UCODE_REG1_0[3]), .pin19(PC_CNT), .pin18(UCODE_ROM1[7]), .pin17(UCODE_ROM1[6]),
    .pin16(FLAG_SELECT[2]), .pin15(FLAG_SELECT[1]), .pin14(UCODE_ROM1[5]), .pin13(UCODE_ROM1[4]),
    .pin12(FLAG_SELECT[0]), .pin11(nCLK));
  assign BBUS = in_6 ? dipswitch_1_sw8 : 8'bz;  // Controlled_Buffer controlled_buffer_1
  DipSwitch #(.number(16)) dipswitch_2 (
    .sw1(dipswitch_2_sw16[15]), .sw2(dipswitch_2_sw16[14]), .sw3(dipswitch_2_sw16[13]),
    .sw4(dipswitch_2_sw16[12]), .sw5(dipswitch_2_sw16[11]), .sw6(dipswitch_2_sw16[10]),
    .sw7(dipswitch_2_sw16[9]), .sw8(dipswitch_2_sw16[8]), .sw9(dipswitch_2_sw16[7]),
    .sw10(dipswitch_2_sw16[6]), .sw11(dipswitch_2_sw16[5]), .sw12(dipswitch_2_sw16[4]),
    .sw13(dipswitch_2_sw16[3]), .sw14(dipswitch_2_sw16[2]), .sw15(dipswitch_2_sw16[1]),
    .sw16(dipswitch_2_sw16[0]));
  not not_1 (ALU_CARRY_IN0, or_1_out);
  or or_1 (or_1_out, or_2_out, and_6_out);
  and and_1 (ALU_CARRY_IN0, not_2_out, and_2_out);
  Pull_Resistor pull_resistor_1 (.node(BBUS));
  // LedBar #(.inputtype("row"), .matrixcols(16)) ledbar_2: pin names not known; wires that end beside it: ABUS
  or or_2 (or_2_out, in_9, and_5_out);
  not not_2 (not_2_out, in_9);
  and and_2 (and_2_out, or_12_out, or_13_out);
  // NOT_Gate not_3 has open pins: in=or_3_out, out=open
  or or_3 (or_3_out, not_6_out, not_7_out);
  and and_3 (and_3_out, not_8_out, not_9_out);
  and and_4 (and_4_out, or_11_out, not_10_out);
  and and_5 (and_5_out, in_8, IR[4]);
  and and_6 (and_6_out, in_10, not_11_out);
  // NOT_Gate not_4 has open pins: in=xor_1_out, out=open
  xor xor_1 (xor_1_out, in_9, not_12_out);
  // NOT_Gate not_5 has open pins: in=or_4_out, out=open
  or or_4 (or_4_out, and_9_out, and_10_out);
  // AND_Gate and_7 has open pins: in0=or_5_out, in1=or_6_out, out=open
  not not_6 (not_6_out, or_7_out);
  not not_7 (not_7_out, or_8_out);
  // AND_Gate and_8 has open pins: in0=or_9_out, in1=or_10_out, out=open
  not not_8 (not_8_out, and_11_out);
  not not_9 (not_9_out, and_12_out);
  not not_10 (not_10_out, and_13_out);
  not not_11 (not_11_out, IR[4]);
  not not_12 (not_12_out, in_8);
  and and_9 (and_9_out, in_9, not_19_out);
  and and_10 (and_10_out, not_20_out, in_8);
  or or_5 (or_5_out, in_9, not_21_out);
  or or_6 (or_6_out, not_22_out, in_8);
  or or_7 (or_7_out, or_14_out, not_13_out);
  not not_13 (not_13_out, in_8);
  not not_14 (not_14_out, or_14_out);
  or or_8 (or_8_out, not_14_out, in_8);
  or or_9 (or_9_out, and_14_out, not_15_out);
  not not_15 (not_15_out, in_8);
  not not_16 (not_16_out, and_14_out);
  or or_10 (or_10_out, not_16_out, in_8);
  and and_11 (and_11_out, and_15_out, not_17_out);
  not not_17 (not_17_out, in_8);
  not not_18 (not_18_out, and_15_out);
  and and_12 (and_12_out, not_18_out, in_8);
  or or_11 (or_11_out, not_23_out, in_8);
  and and_13 (and_13_out, not_23_out, in_8);
  _74377 #(.ShowInternalStructure("true")) u_IR (
    .pin1(nIR_WRITE), .pin2(IR[0]), .pin3(BBUS[0]), .pin4(BBUS[1]), .pin5(IR[1]), .pin6(IR[2]),
    .pin7(BBUS[2]), .pin8(BBUS[3]), .pin9(IR[3]), .pin19(IR[4]), .pin18(BBUS[4]), .pin17(BBUS[5]),
    .pin16(ALU_S[3]), .pin15(ALU_LOGIC), .pin14(BBUS[6]), .pin13(BBUS[7]), .pin12(IR[7]), .pin11(CLK));
  Pull_Resistor pull_resistor_2 (.node(ABUS));
  assign ABUS = in_7 ? dipswitch_2_sw16 : 16'bz;  // Controlled_Buffer controlled_buffer_2
  or or_12 (or_12_out, not_24_out, not_25_out);
  or or_13 (or_13_out, not_26_out, in_8);
  not not_19 (not_19_out, in_8);
  not not_20 (not_20_out, in_9);
  not not_21 (not_21_out, in_8);
  not not_22 (not_22_out, in_9);
  not not_23 (not_23_out, ALU_S[3]);
  // Probe on {PC_Q3, PC_Q2, PC_Q1, PC_Q0}
  // Probe on {PC_Q3, PC_Q2, PC_Q1, PC_Q0}
  not not_24 (not_24_out, in_8);
  not not_25 (not_25_out, IR[4]);
  not not_26 (not_26_out, in_10);
  _74273 #(.ShowInternalStructure("true")) u_74273_2 (
    .pin1(nRESET), .pin2(UCODE_REG0_0[0]), .pin3(UCODE_ROM0[0]), .pin4(UCODE_ROM0[1]),
    .pin5(UCODE_REG0_0[1]), .pin6(UCODE_REG0_0[2]), .pin7(UCODE_ROM0[2]), .pin8(UCODE_ROM0[3]),
    .pin9(UCODE_REG0_0[3]), .pin19(UCODE_REG0_1[3]), .pin18(UCODE_ROM0[7]), .pin17(UCODE_ROM0[6]),
    .pin16(UCODE_REG0_1[2]), .pin15(UCODE_REG0_1[1]), .pin14(UCODE_ROM0[5]), .pin13(UCODE_ROM0[4]),
    .pin12(UCODE_REG0_1[0]), .pin11(nCLK));
  or or_14 (or_14_out, not_27_out, not_28_out);
  and and_14 (and_14_out, in_9, in_10);
  and and_15 (and_15_out, in_9, in_10);
  // NoConnect on IR2_pin19
  // NoConnect on IR2_pin18
  _74377 #(.ShowInternalStructure("true")) IR2 (
    .pin1(nIR2_WRITE), .pin2(UCODE_ADDR[4]), .pin3(BBUS[0]), .pin4(BBUS[1]), .pin5(UCODE_ADDR[3]),
    .pin6(UCODE_ADDR[2]), .pin7(BBUS[2]), .pin8(BBUS[3]), .pin9(UCODE_ADDR[1]), .pin19(IR2_pin19),
    .pin18(IR2_pin18), .pin17(IR2_pin17), .pin16(IR2_pin16), .pin15(IR2_pin15), .pin14(IR2_pin14),
    .pin13(IR2_pin13), .pin12(IR2_pin12), .pin11(CLK));
  not not_27 (not_27_out, in_9);
  not not_28 (not_28_out, in_10);
  // NoConnect on IR2_pin17
  // NoConnect on IR2_pin16
  // NoConnect on IR2_pin15
  // NoConnect on IR2_pin14
  // Probe on {IR[7], ALU_LOGIC, ALU_S[3], IR[4:0]}
  // NoConnect on IR2_pin13
  // NoConnect on IR2_pin12
  _74299 #(.ShowInternalStructure("true")) X (
    .pin1(X_S0), .pin2(nX_BOUT), .pin3(nX_BOUT), .pin4(BBUS[6]), .pin5(BBUS[4]), .pin6(BBUS[2]),
    .pin7(BBUS[0]), .pin8(X_LEFT_FLAG), .pin9(nRESET), .pin19(X_S1), .pin18(X_pin18), .pin17(X_RIGHT_FLAG),
    .pin16(BBUS[7]), .pin15(BBUS[5]), .pin14(BBUS[3]), .pin13(BBUS[1]), .pin12(CLK), .pin11(X_pin11));
  _74138 #(.ShowInternalStructure("true")) u_74138_4 (
    .pin1(UCODE_REG0_1[0]), .pin2(UCODE_REG0_1[1]), .pin3(UCODE_REG0_1[2]), .pin4(n74138_4_pin4),
    .pin5(n74138_4_pin4), .pin6(UCODE_REG0_1[3]), .pin7(nIR_WRITE), .pin15(nA_WRITE), .pin14(nB_WRITE),
    .pin13(nPC_LOAD_HIGH_ROM), .pin12(nPC_LOAD_LOW_ROM), .pin11(nFLAG_WRITE_BUS), .pin10(nX_WRITE),
    .pin9(nY_WRITE));
  _74299 #(.ShowInternalStructure("true")) Y (
    .pin1(Y_S0), .pin2(nY_BOUT), .pin3(nY_BOUT), .pin4(BBUS[6]), .pin5(BBUS[4]), .pin6(BBUS[2]),
    .pin7(BBUS[0]), .pin9(nRESET), .pin19(Y_S1), .pin18(Y_pin18), .pin16(BBUS[7]), .pin15(BBUS[5]),
    .pin14(BBUS[3]), .pin13(BBUS[1]), .pin12(CLK), .pin11(Y_pin11));  // open: pin8, pin17
  _74138 #(.ShowInternalStructure("true")) u_74138_5 (
    .pin1(UCODE_REG0_0[0]), .pin2(UCODE_REG0_0[1]), .pin3(UCODE_REG0_0[2]), .pin4(n74138_5_pin4),
    .pin5(n74138_5_pin4), .pin6(UCODE_REG0_0[3]), .pin7(nZ_BOUT), .pin15(nA_BOUT_EN), .pin14(nB_BOUT_EN),
    .pin13(nKEYB_BOUT), .pin12(nF_BOUT_EN), .pin11(nFLAG_BOUT), .pin10(nX_BOUT), .pin9(nY_BOUT));
  LedBar ledbar_3 (
    .led0(UCODE_REG0_1[3]), .led1(UCODE_REG0_1[2]), .led2(UCODE_REG0_1[1]), .led3(UCODE_REG0_1[0]),
    .led4(UCODE_REG0_0[3]), .led5(UCODE_REG0_0[2]), .led6(UCODE_REG0_0[1]), .led7(UCODE_REG0_0[0]));
  _7400 #(.ShowInternalStructure("true")) u_7400_1 (
    .pin1(nY_SHIFT_RIGHT), .pin2(nY_WRITE), .pin3(Y_S0), .pin4(nY_SHIFT_LEFT), .pin5(nY_WRITE), .pin6(Y_S1),
    .pin13(nX_SHIFT_RIGHT), .pin12(nX_WRITE), .pin11(X_S0), .pin10(nX_SHIFT_LEFT), .pin9(nX_WRITE),
    .pin8(X_S1));
  _74299 #(.ShowInternalStructure("true")) u_74299_1 (
    .pin1(Z_WRITE), .pin2(nZ_BOUT), .pin3(nZ_BOUT), .pin4(BBUS[6]), .pin5(BBUS[4]), .pin6(BBUS[2]),
    .pin7(BBUS[0]), .pin9(nRESET), .pin19(Z_WRITE), .pin18(n74299_1_pin18), .pin16(BBUS[7]), .pin15(BBUS[5]),
    .pin14(BBUS[3]), .pin13(BBUS[1]), .pin12(CLK), .pin11(n74299_1_pin11));  // open: pin8, pin17
  Hex_Digit_Display hex_digit_display_1 (.value(ALU_A[7:4]));  // open: dp
  Hex_Digit_Display hex_digit_display_2 (.value(ALU_B[7:4]));  // open: dp
  // Probe on MAR_ADDR
  // Probe on MAR_ADDR
  // Probe on SP_ADDR
  // Probe on SP_ADDR
  Hex_Digit_Display hex_digit_display_3 (.value(ALU_A[3:0]));  // open: dp
  Hex_Digit_Display hex_digit_display_4 (.value(ALU_B[3:0]));  // open: dp
  _74245 #(.ShowInternalStructure("true")) u_74245_1 (
    .pin1(n74245_1_pin1), .pin2(ALU_A[7]), .pin3(ALU_A[6]), .pin4(ALU_A[5]), .pin5(ALU_A[4]),
    .pin6(ALU_A[3]), .pin7(ALU_A[2]), .pin8(ALU_A[1]), .pin9(ALU_A[0]), .pin19(nA_BOUT_EN), .pin18(BBUS[7]),
    .pin17(BBUS[6]), .pin16(BBUS[5]), .pin15(BBUS[4]), .pin14(BBUS[3]), .pin13(BBUS[2]), .pin12(BBUS[1]),
    .pin11(BBUS[0]));
  Hex_Digit_Display L_F1 (.value(F[7:4]));  // open: dp
  _74245 #(.ShowInternalStructure("true")) u_74245_2 (
    .pin1(n74245_2_pin1), .pin2(ALU_B[7]), .pin3(ALU_B[6]), .pin4(ALU_B[5]), .pin5(ALU_B[4]),
    .pin6(ALU_B[3]), .pin7(ALU_B[2]), .pin8(ALU_B[1]), .pin9(ALU_B[0]), .pin19(nB_BOUT_EN), .pin18(BBUS[7]),
    .pin17(BBUS[6]), .pin16(BBUS[5]), .pin15(BBUS[4]), .pin14(BBUS[3]), .pin13(BBUS[2]), .pin12(BBUS[1]),
    .pin11(BBUS[0]));
  Hex_Digit_Display L_F0 (.value(F[3:0]));  // open: dp
  _74245 #(.ShowInternalStructure("true")) u_74245_3 (
    .pin1(n74245_3_pin1), .pin2(F[7]), .pin3(F[6]), .pin4(F[5]), .pin5(F[4]), .pin6(F[3]), .pin7(F[2]),
    .pin8(F[1]), .pin9(F[0]), .pin19(nF_BOUT_EN), .pin18(BBUS[7]), .pin17(BBUS[6]), .pin16(BBUS[5]),
    .pin15(BBUS[4]), .pin14(BBUS[3]), .pin13(BBUS[2]), .pin12(BBUS[1]), .pin11(BBUS[0]));
  _74377 #(.ShowInternalStructure("true")) u_74377_1 (
    .pin1(nA_WRITE), .pin2(ALU_A[0]), .pin3(BBUS[0]), .pin4(BBUS[1]), .pin5(ALU_A[1]), .pin6(ALU_A[2]),
    .pin7(BBUS[2]), .pin8(BBUS[3]), .pin9(ALU_A[3]), .pin19(ALU_A[7]), .pin18(BBUS[7]), .pin17(BBUS[6]),
    .pin16(ALU_A[6]), .pin15(ALU_A[5]), .pin14(BBUS[5]), .pin13(BBUS[4]), .pin12(ALU_A[4]), .pin11(CLK));
  _74377 #(.ShowInternalStructure("true")) u_74377_2 (
    .pin1(nB_WRITE), .pin2(ALU_B[0]), .pin3(BBUS[0]), .pin4(BBUS[1]), .pin5(ALU_B[1]), .pin6(ALU_B[2]),
    .pin7(BBUS[2]), .pin8(BBUS[3]), .pin9(ALU_B[3]), .pin19(ALU_B[7]), .pin18(BBUS[7]), .pin17(BBUS[6]),
    .pin16(ALU_B[6]), .pin15(ALU_B[5]), .pin14(BBUS[5]), .pin13(BBUS[4]), .pin12(ALU_B[4]), .pin11(CLK));
  T74HC191 t74hc191_1 (
    .A(BBUS[4]), .B(BBUS[5]), .C(BBUS[6]), .D(BBUS[7]), .nCLKEN(t74hc191_2_nrco), .D_nU(nSP_CNTUP),
    .CLK(CLK), .nLOAD(nSP_LOAD_HIGH), .Qa(SP_ADDR[12]), .Qb(SP_ADDR[13]), .Qc(SP_ADDR[14]), .Qd(SP_ADDR[15]),
    .MAX_MIN(t74hc191_1_max_min), .nRCO(t74hc191_1_nrco));
  // _74181 #(.ShowInternalStructure("true")) 74181_1: pin names not known; wires that end beside it: ALU_B[0], ALU_A[1], ALU_A[0], ALU_B[1], ALU_A[2], ALU_B[2], ALU_A[3], ALU_B[3], nALU_CARRY_IN0, ALU_LOGIC
  _74161 #(.ShowInternalStructure("true")) u_74161_2 (
    .pin1(nRESET), .pin2(CLK), .pin3(BBUS[4]), .pin4(BBUS[5]), .pin5(BBUS[6]), .pin6(BBUS[7]),
    .pin7(n74161_2_pin7), .pin14(PC_Q3[0]), .pin13(PC_Q3[1]), .pin12(PC_Q3[2]), .pin11(PC_Q3[3]),
    .pin10(n74161_2_pin10), .pin9(nPC_LOAD_HIGH));  // open: pin15
  CY7C199 cy7c199_1 (
    .A0(ABUS[0]), .A1(ABUS[1]), .A2(ABUS[2]), .A3(ABUS[3]), .A4(ABUS[4]), .A5(ABUS[5]), .A6(ABUS[6]),
    .A7(ABUS[7]), .A8(ABUS[8]), .A9(ABUS[9]), .A10(ABUS[10]), .A11(ABUS[11]), .A12(ABUS[12]), .A13(ABUS[13]),
    .A14(ABUS[14]), .I0(BBUS[0]), .I1(BBUS[1]), .I2(BBUS[2]), .I3(BBUS[3]), .I4(BBUS[4]), .I5(BBUS[5]),
    .I6(BBUS[6]), .I7(BBUS[7]), .nWE(nRAM_WE), .nOE(nMEM_READ), .nCE(nABUS_MSB), .O0(BBUS[0]), .O1(BBUS[1]),
    .O2(BBUS[2]), .O3(BBUS[3]), .O4(BBUS[4]), .O5(BBUS[5]), .O6(BBUS[6]), .O7(BBUS[7]));
  _74161 #(.ShowInternalStructure("true")) u_74161_3 (
    .pin1(nRESET), .pin2(CLK), .pin3(BBUS[4]), .pin4(BBUS[5]), .pin5(BBUS[6]), .pin6(BBUS[7]),
    .pin7(n74161_3_pin7), .pin14(MAR_ADDR[12]), .pin13(MAR_ADDR[13]), .pin12(MAR_ADDR[14]),
    .pin11(MAR_ADDR[15]), .pin10(n74161_3_pin10), .pin9(nMAR_LOAD_HIGH));  // open: pin15
  T74HC191 t74hc191_2 (
    .A(BBUS[0]), .B(BBUS[1]), .C(BBUS[2]), .D(BBUS[3]), .nCLKEN(t74hc191_3_nrco), .D_nU(nSP_CNTUP),
    .CLK(CLK), .nLOAD(nSP_LOAD_HIGH), .Qa(SP_ADDR[8]), .Qb(SP_ADDR[9]), .Qc(SP_ADDR[10]), .Qd(SP_ADDR[11]),
    .MAX_MIN(t74hc191_2_max_min), .nRCO(t74hc191_2_nrco));
  // NoConnect on nothing
  // NoConnect on nothing
  _74245 #(.ShowInternalStructure("true")) u_74245_4 (
    .pin1(n74245_4_pin1), .pin2(ABUS[15]), .pin3(ABUS[14]), .pin4(ABUS[13]), .pin5(ABUS[12]),
    .pin6(ABUS[11]), .pin7(ABUS[10]), .pin8(ABUS[9]), .pin9(ABUS[8]), .pin19(nABUS_TO_BUS_HIGH),
    .pin18(BBUS[7]), .pin17(BBUS[6]), .pin16(BBUS[5]), .pin15(BBUS[4]), .pin14(BBUS[3]), .pin13(BBUS[2]),
    .pin12(BBUS[1]), .pin11(BBUS[0]));
  _74161 #(.ShowInternalStructure("true")) u_74161_4 (
    .pin1(nRESET), .pin2(CLK), .pin3(BBUS[0]), .pin4(BBUS[1]), .pin5(BBUS[2]), .pin6(BBUS[3]),
    .pin7(n74161_4_pin7), .pin15(n74161_2_pin10), .pin14(PC_Q2[0]), .pin13(PC_Q2[1]), .pin12(PC_Q2[2]),
    .pin11(PC_Q2[3]), .pin10(n74161_4_pin10), .pin9(nPC_LOAD_HIGH));
  _74245 #(.ShowInternalStructure("true")) u_74245_5 (
    .pin1(n74245_5_pin1), .pin2(PC_Q3[3]), .pin3(PC_Q3[2]), .pin4(PC_Q3[1]), .pin5(PC_Q3[0]),
    .pin6(PC_Q2[3]), .pin7(PC_Q2[2]), .pin8(PC_Q2[1]), .pin9(PC_Q2[0]), .pin19(nPC_AOUT), .pin18(ABUS[15]),
    .pin17(ABUS[14]), .pin16(ABUS[13]), .pin15(ABUS[12]), .pin14(ABUS[11]), .pin13(ABUS[10]),
    .pin12(ABUS[9]), .pin11(ABUS[8]));
  _74161 #(.ShowInternalStructure("true")) u_74161_5 (
    .pin1(nRESET), .pin2(CLK), .pin3(BBUS[0]), .pin4(BBUS[1]), .pin5(BBUS[2]), .pin6(BBUS[3]),
    .pin7(n74161_5_pin7), .pin15(n74161_3_pin10), .pin14(MAR_ADDR[8]), .pin13(MAR_ADDR[9]),
    .pin12(MAR_ADDR[10]), .pin11(MAR_ADDR[11]), .pin10(n74161_5_pin10), .pin9(nMAR_LOAD_HIGH));
  _74245 #(.ShowInternalStructure("true")) u_74245_6 (
    .pin1(n74245_6_pin1), .pin2(MAR_ADDR[15]), .pin3(MAR_ADDR[14]), .pin4(MAR_ADDR[13]), .pin5(MAR_ADDR[12]),
    .pin6(MAR_ADDR[11]), .pin7(MAR_ADDR[10]), .pin8(MAR_ADDR[9]), .pin9(MAR_ADDR[8]), .pin19(nMAR_AOUT),
    .pin18(ABUS[15]), .pin17(ABUS[14]), .pin16(ABUS[13]), .pin15(ABUS[12]), .pin14(ABUS[11]),
    .pin13(ABUS[10]), .pin12(ABUS[9]), .pin11(ABUS[8]));
  _74245 #(.ShowInternalStructure("true")) u_74245_7 (
    .pin1(n74245_7_pin1), .pin2(SP_ADDR[15]), .pin3(SP_ADDR[14]), .pin4(SP_ADDR[13]), .pin5(SP_ADDR[12]),
    .pin6(SP_ADDR[11]), .pin7(SP_ADDR[10]), .pin8(SP_ADDR[9]), .pin9(SP_ADDR[8]), .pin19(nSP_AOUT),
    .pin18(ABUS[15]), .pin17(ABUS[14]), .pin16(ABUS[13]), .pin15(ABUS[12]), .pin14(ABUS[11]),
    .pin13(ABUS[10]), .pin12(ABUS[9]), .pin11(ABUS[8]));
  // _74181 #(.ShowInternalStructure("true")) 74181_2: pin names not known; wires that end beside it: n74181_2_p1, n74181_2_p2, F[3], ALU_B[4], ALU_A[5], ALU_A[4], ALU_B[5], ALU_S[3], ALU_A[6], ALU_S[2], ALU_B[6], ALU_S[1], ALU_A[7], ALU_S[0], ALU_B[7], n74181_2_p1, ALU_LOGIC, nCARRY, n74181_2_p19, F[7]
  _74157 #(.ShowInternalStructure("true")) u_74157_1 (
    .pin1(nFLAG_WRITE_BUS), .pin2(BBUS[0]), .pin3(nCARRY), .pin4(FLG_BUS_MUX_OUT[0]), .pin5(BBUS[1]),
    .pin6(EQUAL), .pin7(FLG_BUS_MUX_OUT[1]), .pin15(n74157_1_pin15), .pin14(BBUS[3]), .pin13(X_LEFT_FLAG),
    .pin12(FLG_BUS_MUX_OUT[3]), .pin11(BBUS[2]), .pin10(nA_ZERO), .pin9(FLG_BUS_MUX_OUT[2]));
  _74245 #(.ShowInternalStructure("true")) u_74245_8 (
    .pin1(n74245_8_pin1), .pin2(ABUS[7]), .pin3(ABUS[6]), .pin4(ABUS[5]), .pin5(ABUS[4]), .pin6(ABUS[3]),
    .pin7(ABUS[2]), .pin8(ABUS[1]), .pin9(ABUS[0]), .pin19(nABUS_TO_BUS_LOW), .pin18(BBUS[7]),
    .pin17(BBUS[6]), .pin16(BBUS[5]), .pin15(BBUS[4]), .pin14(BBUS[3]), .pin13(BBUS[2]), .pin12(BBUS[1]),
    .pin11(BBUS[0]));
  _7432 #(.ShowInternalStructure("true")) u_7432_1 (
    .pin1(ALU_A[4]), .pin2(ALU_A[5]), .pin3(n7432_1_pin3), .pin4(ALU_A[6]), .pin5(ALU_A[7]),
    .pin6(n7432_1_pin6), .pin13(ALU_A[0]), .pin12(ALU_A[1]), .pin11(n7432_1_pin11), .pin10(ALU_A[2]),
    .pin9(ALU_A[3]), .pin8(n7432_1_pin8));
  _74245 #(.ShowInternalStructure("true")) u_74245_9 (
    .pin1(n74245_9_pin1), .pin2(PC_Q1[3]), .pin3(PC_Q1[2]), .pin4(PC_Q1[1]), .pin5(PC_Q1[0]),
    .pin6(PC_Q0[3]), .pin7(PC_Q0[2]), .pin8(PC_Q0[1]), .pin9(PC_Q0[0]), .pin19(nPC_AOUT), .pin18(ABUS[7]),
    .pin17(ABUS[6]), .pin16(ABUS[5]), .pin15(ABUS[4]), .pin14(ABUS[3]), .pin13(ABUS[2]), .pin12(ABUS[1]),
    .pin11(ABUS[0]));
  _7432 #(.ShowInternalStructure("true")) u_7432_2 (
    .pin1(n7432_1_pin6), .pin2(n7432_1_pin3), .pin3(n7432_2_pin3), .pin4(n7432_2_pin4), .pin5(n7432_2_pin3),
    .pin6(nA_ZERO), .pin13(n7432_1_pin8), .pin12(n7432_1_pin11), .pin11(n7432_2_pin4));  // open: pin10, pin9, pin8
  // NoConnect on nothing
  // NoConnect on nothing
  _74245 #(.ShowInternalStructure("true")) u_74245_10 (
    .pin1(n74245_10_pin1), .pin2(MAR_ADDR[7]), .pin3(MAR_ADDR[6]), .pin4(MAR_ADDR[5]), .pin5(MAR_ADDR[4]),
    .pin6(MAR_ADDR[3]), .pin7(MAR_ADDR[2]), .pin8(MAR_ADDR[1]), .pin9(MAR_ADDR[0]), .pin19(nMAR_AOUT),
    .pin18(ABUS[7]), .pin17(ABUS[6]), .pin16(ABUS[5]), .pin15(ABUS[4]), .pin14(ABUS[3]), .pin13(ABUS[2]),
    .pin12(ABUS[1]), .pin11(ABUS[0]));
  _74245 #(.ShowInternalStructure("true")) u_74245_11 (
    .pin1(n74245_11_pin1), .pin2(SP_ADDR[7]), .pin3(SP_ADDR[6]), .pin4(SP_ADDR[5]), .pin5(SP_ADDR[4]),
    .pin6(SP_ADDR[3]), .pin7(SP_ADDR[2]), .pin8(SP_ADDR[1]), .pin9(SP_ADDR[0]), .pin19(nSP_AOUT),
    .pin18(ABUS[7]), .pin17(ABUS[6]), .pin16(ABUS[5]), .pin15(ABUS[4]), .pin14(ABUS[3]), .pin13(ABUS[2]),
    .pin12(ABUS[1]), .pin11(ABUS[0]));
  _74138 #(.ShowInternalStructure("true")) u_74138_6 (
    .pin1(IR[4]), .pin2(ALU_S[3]), .pin3(ALU_LOGIC), .pin4(n74138_6_pin4), .pin5(n74138_6_pin5),
    .pin6(n74138_6_pin6), .pin7(n74138_6_pin7), .pin15(n74138_6_pin15), .pin14(n74138_6_pin14),
    .pin13(n74138_6_pin13), .pin12(n74138_6_pin12), .pin11(n74138_6_pin11), .pin10(n74138_6_pin10),
    .pin9(n74138_6_pin9));
  SST39SF010A sst39sf010a_3 (
    .nOE(1'b0), .nCE(ROM_nCE), .ROM_SELECT(in_5), .A0(ABUS[0]), .A1(ABUS[1]), .A2(ABUS[2]), .A3(ABUS[3]),
    .A4(ABUS[4]), .A5(ABUS[5]), .A6(ABUS[6]), .A7(ABUS[7]), .A8(ABUS[8]), .A9(ABUS[9]), .A10(ABUS[10]),
    .A11(ABUS[11]), .A12(ABUS[12]), .A13(ABUS[13]), .A14(ABUS[14]), .A15(ABUS[15]), .A16(1'b0), .O0(BBUS[0]),
    .O1(BBUS[1]), .O2(BBUS[2]), .O3(BBUS[3]), .O4(BBUS[4]), .O5(BBUS[5]), .O6(BBUS[6]), .O7(BBUS[7]));
  and and_16 (EQUAL, n74181_2_p2, n74181_2_p19);
  // NoConnect on n74138_6_pin15
  // NoConnect on n74138_6_pin14
  // NoConnect on n74138_6_pin10
  // NoConnect on n74138_6_pin9
  _7408 #(.ShowInternalStructure("true")) u_7408_1 (
    .pin1(n7408_1_pin1), .pin2(n74138_6_pin7), .pin3(nALU_S0), .pin4(n74138_6_pin7), .pin5(ALU_S[1]),
    .pin6(ALU_S[2]), .pin13(n74138_6_pin13), .pin12(n74138_6_pin12), .pin11(n7408_1_pin1),
    .pin10(n7408_1_pin1), .pin9(n74138_6_pin11), .pin8(ALU_S[1]));
  T74HC191 t74hc191_3 (
    .A(BBUS[4]), .B(BBUS[5]), .C(BBUS[6]), .D(BBUS[7]), .nCLKEN(t74hc191_4_nrco), .D_nU(nSP_CNTUP),
    .CLK(CLK), .nLOAD(nSP_LOAD_LOW), .Qa(SP_ADDR[4]), .Qb(SP_ADDR[5]), .Qc(SP_ADDR[6]), .Qd(SP_ADDR[7]),
    .MAX_MIN(t74hc191_3_max_min), .nRCO(t74hc191_3_nrco));
  _74377 #(.ShowInternalStructure("true")) u_74377_3 (
    .pin1(nFLAG_REG_WRITE), .pin2(Q_FLAGS[0]), .pin3(FLG_BUS_MUX_OUT[0]), .pin4(FLG_BUS_MUX_OUT[1]),
    .pin5(Q_FLAGS[1]), .pin6(Q_FLAGS[2]), .pin7(FLG_BUS_MUX_OUT[2]), .pin8(FLG_BUS_MUX_OUT[3]),
    .pin9(Q_FLAGS[3]), .pin19(Q_FLAGS[7]), .pin18(n74377_3_pin18), .pin17(n74377_3_pin17),
    .pin16(Q_FLAGS[6]), .pin15(Q_FLAGS[5]), .pin14(n74377_3_pin14), .pin13(X_RIGHT_FLAG), .pin12(Q_FLAGS[4]),
    .pin11(CLK));
  _74161 #(.ShowInternalStructure("true")) u_74161_6 (
    .pin1(nRESET), .pin2(CLK), .pin3(BBUS[4]), .pin4(BBUS[5]), .pin5(BBUS[6]), .pin6(BBUS[7]),
    .pin7(n74161_6_pin7), .pin15(n74161_4_pin10), .pin14(PC_Q1[0]), .pin13(PC_Q1[1]), .pin12(PC_Q1[2]),
    .pin11(PC_Q1[3]), .pin10(n74161_6_pin10), .pin9(nPC_LOAD_LOW));
  _74161 #(.ShowInternalStructure("true")) u_74161_7 (
    .pin1(nRESET), .pin2(CLK), .pin3(BBUS[4]), .pin4(BBUS[5]), .pin5(BBUS[6]), .pin6(BBUS[7]),
    .pin7(n74161_7_pin7), .pin15(n74161_5_pin10), .pin14(MAR_ADDR[4]), .pin13(MAR_ADDR[5]),
    .pin12(MAR_ADDR[6]), .pin11(MAR_ADDR[7]), .pin10(n74161_7_pin10), .pin9(nMAR_LOAD_LOW));
  T74HC191 t74hc191_4 (
    .A(BBUS[0]), .B(BBUS[1]), .C(BBUS[2]), .D(BBUS[3]), .nCLKEN(nSP_CNT), .D_nU(nSP_CNTUP), .CLK(CLK),
    .nLOAD(nSP_LOAD_LOW), .Qa(SP_ADDR[0]), .Qb(SP_ADDR[1]), .Qc(SP_ADDR[2]), .Qd(SP_ADDR[3]),
    .MAX_MIN(t74hc191_4_max_min), .nRCO(t74hc191_4_nrco));
  _74161 #(.ShowInternalStructure("true")) u_74161_8 (
    .pin1(nRESET), .pin2(CLK), .pin3(BBUS[0]), .pin4(BBUS[1]), .pin5(BBUS[2]), .pin6(BBUS[3]),
    .pin7(n74161_8_pin7), .pin15(n74161_6_pin10), .pin14(PC_Q0[0]), .pin13(PC_Q0[1]), .pin12(PC_Q0[2]),
    .pin11(PC_Q0[3]), .pin10(PC_CNT), .pin9(nPC_LOAD_LOW));
  _74161 #(.ShowInternalStructure("true")) u_74161_9 (
    .pin1(nRESET), .pin2(CLK), .pin3(BBUS[0]), .pin4(BBUS[1]), .pin5(BBUS[2]), .pin6(BBUS[3]),
    .pin7(n74161_9_pin7), .pin15(n74161_7_pin10), .pin14(MAR_ADDR[0]), .pin13(MAR_ADDR[1]),
    .pin12(MAR_ADDR[2]), .pin11(MAR_ADDR[3]), .pin10(MAR_CNT), .pin9(nMAR_LOAD_LOW));
  _7432 #(.ShowInternalStructure("true")) u_7432_3 (
    .pin4(n7432_3_pin4), .pin5(PC_LOAD_EN), .pin6(n7432_3_pin6));  // open: pin1, pin2, pin3, pin13, pin12, pin11, pin10, pin9, pin8
  _74245 #(.ShowInternalStructure("true")) u_74245_12 (
    .pin1(n74245_12_pin1), .pin2(Q_FLAGS[7]), .pin3(Q_FLAGS[6]), .pin4(Q_FLAGS[5]), .pin5(Q_FLAGS[4]),
    .pin6(Q_FLAGS[3]), .pin7(Q_FLAGS[2]), .pin8(Q_FLAGS[1]), .pin9(Q_FLAGS[0]), .pin19(nFLAG_BOUT),
    .pin18(BBUS[7]), .pin17(BBUS[6]), .pin16(BBUS[5]), .pin15(BBUS[4]), .pin14(BBUS[3]), .pin13(BBUS[2]),
    .pin12(BBUS[1]), .pin11(BBUS[0]));
  Keyboard #(.trigger("falling")) keyboard_1 (
    .clk(CLK), .re(1'b1), .clr(1'b0), .avail(keyboard_1_avail), .data(keyboard_1_data));
  _7404 #(.ShowInternalStructure("true")) u_7404_1 (
    .pin1(nALU_S0), .pin2(ALU_S[0]), .pin13(ALU_S[3]), .pin12(n7432_3_pin4), .pin11(n7404_1_pin11),
    .pin10(n7404_1_pin10));  // open: pin3, pin4, pin5, pin6, pin9, pin8
  _7432 #(.ShowInternalStructure("true")) u_7432_4 (
    .pin1(ABUS[15]), .pin2(MEM_WRITE), .pin3(n7432_4_pin3), .pin4(n7432_4_pin3), .pin5(nMEM_READ),
    .pin6(ROM_nCE), .pin13(nPC_LOAD_HIGH_ROM), .pin12(nPC_LOAD_EN), .pin11(nPC_LOAD_HIGH),
    .pin10(nPC_LOAD_LOW_ROM), .pin9(nPC_LOAD_EN), .pin8(nPC_LOAD_LOW));
  _7400 #(.ShowInternalStructure("true")) u_7400_2 (
    .pin1(MEM_WRITE), .pin2(FAST_CLK), .pin3(nRAM_WE), .pin13(nSP_CNTDOWN), .pin12(nSP_CNTUP),
    .pin11(n7400_2_pin11), .pin10(n7400_2_pin11), .pin9(n7400_2_pin11), .pin8(nSP_CNT));  // open: pin4, pin5, pin6
  _7404 #(.ShowInternalStructure("true")) u_7404_2 (
    .pin1(nMAR_CNT), .pin2(MAR_CNT), .pin3(MAR_CNT), .pin13(ABUS[15]), .pin12(nABUS_MSB), .pin9(nMEM_WRITE),
    .pin8(MEM_WRITE));  // open: pin4, pin5, pin6, pin11, pin10
  _7408 #(.ShowInternalStructure("true")) u_7408_2 (
    .pin1(n7432_3_pin4), .pin2(PC_LOAD_EN), .pin3(n7404_1_pin11), .pin4(n7404_1_pin10), .pin5(n7432_3_pin6),
    .pin6(nALU_CARRY_IN0));  // open: pin13, pin12, pin11, pin10, pin9, pin8
  assign bit_extender_1_out = {{1{1'b0}}, keyboard_1_data};  // Bit_Extender bit_extender_1
  _74151 #(.ShowInternalStructure("true")) u_74151_1 (
    .pin1(Q_FLAGS[2]), .pin2(Q_FLAGS[1]), .pin3(Q_FLAGS[0]), .pin4(n74151_1_pin4), .pin5(PC_LOAD_EN),
    .pin6(nPC_LOAD_EN), .pin7(n74151_1_pin7), .pin15(Q_FLAGS[3]), .pin14(Q_FLAGS[4]), .pin13(Q_FLAGS[5]),
    .pin12(Q_FLAGS[6]), .pin11(FLAG_SELECT[0]), .pin10(FLAG_SELECT[1]), .pin9(FLAG_SELECT[2]));
  // gp_register gp_register_1: pin names not known; wires that end beside it: CLK, bit_extender_1_out, keyboard_1_avail, nRESET, nKEYB_BOUT, BBUS
  _74245 #(.ShowInternalStructure("true")) u_74245_13 ();  // open: pin1, pin2, pin3, pin4, pin5, pin6, pin7, pin8, pin9, pin19, pin18, pin17, pin16, pin15, pin14, pin13, pin12, pin11
  _74377 #(.ShowInternalStructure("true")) u_74377_4 ();  // open: pin1, pin2, pin3, pin4, pin5, pin6, pin7, pin8, pin9, pin19, pin18, pin17, pin16, pin15, pin14, pin13, pin12, pin11
  _74245 #(.ShowInternalStructure("true")) u_74245_14 ();  // open: pin1, pin2, pin3, pin4, pin5, pin6, pin7, pin8, pin9, pin19, pin18, pin17, pin16, pin15, pin14, pin13, pin12, pin11
  _74377 #(.ShowInternalStructure("true")) u_74377_5 ();  // open: pin1, pin2, pin3, pin4, pin5, pin6, pin7, pin8, pin9, pin19, pin18, pin17, pin16, pin15, pin14, pin13, pin12, pin11
  // _74181 #(.ShowInternalStructure("true")) 74181_3: pin names not known; wires that end beside it: n74181_3_p1, n74181_3_p1
  Clock clock_1 (.out(clock_1_out));
  _7432 #(.ShowInternalStructure("true")) u_7432_5 ();  // open: pin1, pin2, pin3, pin4, pin5, pin6, pin13, pin12, pin11, pin10, pin9, pin8
  // _74181 #(.ShowInternalStructure("true")) 74181_4: pin names not known
  _74245 #(.ShowInternalStructure("true")) u_74245_15 ();  // open: pin1, pin2, pin3, pin4, pin5, pin6, pin7, pin8, pin9, pin19, pin18, pin17, pin16, pin15, pin14, pin13, pin12, pin11
  _7432 #(.ShowInternalStructure("true")) u_7432_6 ();  // open: pin1, pin2, pin3, pin4, pin5, pin6, pin13, pin12, pin11, pin10, pin9, pin8
  synced_cpu_vga synced_cpu_vga_1 (
    .CLK1(clock_1_out), .BIN(BBUS), .AIN(ABUS), .nRAM_WRITE_EN(nVRAM_WRITE), .nRAM_READ_EN(nVRAM_READ),
    .CLK8_OUT(AUTO_CLK), .CLK16_OUT(CLK16), .BOUT(BBUS), .X(synced_cpu_vga_1_x), .Y(synced_cpu_vga_1_y),
    .COLOR(synced_cpu_vga_1_color));  // open: CLK2_OUT, CLK4_OUT, nCLK2_OUT, nCLK4_OUT, nCLK8_OUT, nCLK1_OUT, nCLK16_OUT
  _74377 #(.ShowInternalStructure("true")) u_74377_6 ();  // open: pin1, pin2, pin3, pin4, pin5, pin6, pin7, pin8, pin9, pin19, pin18, pin17, pin16, pin15, pin14, pin13, pin12, pin11
  _7404 #(.ShowInternalStructure("true")) u_7404_3 ();  // open: pin1, pin2, pin3, pin4, pin5, pin6, pin13, pin12, pin11, pin10, pin9, pin8
  _7408 #(.ShowInternalStructure("true")) u_7408_3 ();  // open: pin1, pin2, pin3, pin4, pin5, pin6, pin13, pin12, pin11, pin10, pin9, pin8
  _74245 #(.ShowInternalStructure("true")) u_74245_16 ();  // open: pin1, pin2, pin3, pin4, pin5, pin6, pin7, pin8, pin9, pin19, pin18, pin17, pin16, pin15, pin14, pin13, pin12, pin11
  // RGB_Video #(.height(530), .scale(1), .width(803)) rgb_video_1: pin names not known; wires that end beside it: 1'b0, clock_1_out, 1'b1, synced_cpu_vga_1_x, synced_cpu_vga_1_y, synced_cpu_vga_1_color
  _7408 #(.ShowInternalStructure("true")) u_7408_4 ();  // open: pin1, pin2, pin3, pin4, pin5, pin6, pin13, pin12, pin11, pin10, pin9, pin8
  _74245 #(.ShowInternalStructure("true")) u_74245_17 ();  // open: pin1, pin2, pin3, pin4, pin5, pin6, pin7, pin8, pin9, pin19, pin18, pin17, pin16, pin15, pin14, pin13, pin12, pin11
  _74138 #(.ShowInternalStructure("true")) u_74138_7 ();  // open: pin1, pin2, pin3, pin4, pin5, pin6, pin7, pin15, pin14, pin13, pin12, pin11, pin10, pin9
  _74164 #(.ShowInternalStructure("true")) u_74164_1 ();  // open: pin1, pin2, pin3, pin4, pin5, pin6, pin13, pin12, pin11, pin10, pin9, pin8
  _74151 #(.ShowInternalStructure("true")) u_74151_2 ();  // open: pin1, pin2, pin3, pin4, pin5, pin6, pin7, pin15, pin14, pin13, pin12, pin11, pin10, pin9
  // also tied to GND on the sheet: {n74138_1_pin4, n74139_1_pin1, n74139_1_pin15, n74138_2_pin5, n74161_1_pin3, n74161_1_pin4, n74161_1_pin5, n74161_1_pin6, n74138_3_pin5, X_pin18, n74138_4_pin4, X_pin11, Y_pin18, Y_pin11, n74138_5_pin4, n74299_1_pin18, n74299_1_pin11, n74245_2_pin1, n74245_1_pin1, n74157_1_pin15, n74138_6_pin4, n74138_6_pin5, n74377_3_pin18, n74377_3_pin17, n74377_3_pin14, n74151_1_pin7}
  // also tied to VCC on the sheet: {n74138_1_pin6, n74138_2_pin6, n74138_3_pin6, n74161_1_pin10, n74161_1_pin7, n74245_3_pin1, n74161_2_pin7, n74161_3_pin7, n74161_4_pin7, n74161_5_pin7, n74245_4_pin1, n74245_5_pin1, n74245_6_pin1, n74245_7_pin1, n74245_8_pin1, n74245_9_pin1, n74245_10_pin1, n74245_11_pin1, n74161_6_pin7, n74138_6_pin6, n74161_7_pin7, n74161_8_pin7, n74161_9_pin7, n74245_12_pin1, n74151_1_pin4}

  // Other names for the same wires on the sheet: ABUS_MSB = ABUS[15]; ALU_CARRY_IN = in_8; BBUS_1 = BBUS[1];
  //   BBUS_5 = BBUS[5]; UCODE_REG1_1[3:0] = {PC_CNT, FLAG_SELECT}; fSUB = in_9; fSUB_WITH_CARRY = in_10;
  //   UCODE_ADDR (some bits) = {IR[0], ALU_LOGIC, IR[7], ALU_S[3], IR[4], IR[1], IR[2], IR[3], CLK16};
  //   IR_ISTR_WORD[3:0] = {IR[7], ALU_LOGIC, ALU_S[3], IR[4]}; SEL0 = IR[4]; IR[6:5] = {ALU_LOGIC, ALU_S[3]};
  //   MAR_Q0[3:0] = MAR_ADDR[3:0]; MAR_Q1[3:0] = MAR_ADDR[7:4]; MAR_Q2[3:0] = MAR_ADDR[11:8];
  //   MAR_Q3[3:0] = MAR_ADDR[15:12]; SP_Q0[3:0] = SP_ADDR[3:0]; SP_Q1[3:0] = SP_ADDR[7:4]; SP_Q2[3:0] = SP_ADDR[11:8];
  //   SP_Q3[3:0] = SP_ADDR[15:12]; SWITCH_CLK = CLK_SWITCH

  // Notes on the sheet:
  //   in_1: initial=0x1
  //   in_5: initial=0x2
  //   one more ic here
  //   TODO: pass these clocks through Schmitt trigger inverters
  //   two unused!
  //   clock
  //   extended other line
  //   (only usable when not jumping)
  //   WRITE 1
  //   BOUT 0
  //   TODO: pull up resistors on all OE 245 to avoid bus contention on startup
  //   move
  //   cmp
  //   store
  //   sub
  //   adc
  //   add
  //   and
  //   push
  //   pop
  //   jmp
  //   keyb
  //   load
  //   WRITE 0
  //   can switch ir2 for 4 bit reg instead for smaller profile
  //   wire-and
  //   actual is implemented with shift register + 245, fits with a reg
  //   NOTE: Q_FLAGS msb is not selectable
  //   TODO: and the vram with high clock
  //   bus leds?
endmodule

module async_cpu_vga (
  input  in_1,
  input  RAM_WRITE_EN,
  input  [1:0] in_3,
  output [9:0] X,
  output [9:0] Y,
  output [15:0] COLOR
);

  wire CHAR_REG_pin10, CHAR_REG_pin15, CLK1, CLK2, CLK4, CLK8, CLK16, COLOR_REG_pin1, COLOR_REG_pin2,
       COLOR_REG_pin5, COLOR_REG_pin6, COLOR_REG_pin9, COLOR_REG_pin11, COLOR_REG_pin12, COLOR_REG_pin15,
       COLOR_REG_pin16, COLOR_REG_pin19, FG_ACTIVE, n74157_1_pin15, n74163_1_pin1, n74163_1_pin3,
       n74163_1_pin4, n74163_1_pin5, n74163_1_pin6, n74163_1_pin7, n74163_1_pin10, n74163_1_pin15, nCLK1,
       nCLK2, nCLK4, nCLK8, nCLK16, nCOLORS_LATCH, not_1_out, not_2_out, not_9_out, not_10_out, not_11_out,
       not_12_out, not_13_out, not_14_out, nROM_CNT_RESET, nX_CNT, nX_RESET, nY_CNT, nY_RESET, SHIFT_IN,
       t74hc590_1_nrco;
  wire [7:0] BBUS, NEW_COLOR_REG, VDATA_BUS;
  wire [7:7] VGA_ROM;
  wire [14:0] VBUS;
  wire [15:0] ABUS, divider_1_out, divider_1_rem, multiplier_1_out, VBUS_16, VGA_ROM_ADDR;

  T74HC574 t74hc574_1 (
    .D0(BBUS[7]), .D1(BBUS[6]), .D2(BBUS[5]), .D3(BBUS[4]), .D4(BBUS[3]), .D5(BBUS[2]), .D6(BBUS[1]),
    .D7(BBUS[0]), .nOE(CLK16), .CLK(CLK1), .O0(VDATA_BUS[7]), .O1(VDATA_BUS[6]), .O2(VDATA_BUS[5]),
    .O3(VDATA_BUS[4]), .O4(VDATA_BUS[3]), .O5(VDATA_BUS[2]), .O6(VDATA_BUS[1]), .O7(VDATA_BUS[0]));
  T74HC574 t74hc574_2 (
    .D0(ABUS[15]), .D1(ABUS[14]), .D2(ABUS[13]), .D3(ABUS[12]), .D4(ABUS[11]), .D5(ABUS[10]), .D6(ABUS[9]),
    .D7(ABUS[8]), .nOE(CLK16), .CLK(CLK1), .O1(VBUS[14]), .O2(VBUS[13]), .O3(VBUS[12]), .O4(VBUS[11]),
    .O5(VBUS[10]), .O6(VBUS[9]), .O7(VBUS[8]));  // open: O0
  T74HC574 t74hc574_3 (
    .D0(ABUS[7]), .D1(ABUS[6]), .D2(ABUS[5]), .D3(ABUS[4]), .D4(ABUS[3]), .D5(ABUS[2]), .D6(ABUS[1]),
    .D7(ABUS[0]), .nOE(CLK16), .CLK(CLK1), .O0(VBUS[7]), .O1(VBUS[6]), .O2(VBUS[5]), .O3(VBUS[4]),
    .O4(VBUS[3]), .O5(VBUS[2]), .O6(VBUS[1]), .O7(VBUS[0]));
  assign VBUS_16 = {{1{1'b0}}, VBUS};  // Bit_Extender bit_extender_1
  CY7C199 cy7c199_1 (
    .A0(VBUS_16[0]), .A1(VBUS_16[1]), .A2(VBUS_16[2]), .A3(VBUS_16[3]), .A4(VBUS_16[4]), .A5(VBUS_16[5]),
    .A6(VBUS_16[6]), .A7(VBUS_16[7]), .A8(VBUS_16[8]), .A9(VBUS_16[9]), .A10(VBUS_16[10]), .A11(VBUS_16[11]),
    .A12(VBUS_16[12]), .A13(VBUS_16[13]), .A14(VBUS_16[14]), .I0(VDATA_BUS[0]), .I1(VDATA_BUS[1]),
    .I2(VDATA_BUS[2]), .I3(VDATA_BUS[3]), .I4(VDATA_BUS[4]), .I5(VDATA_BUS[5]), .I6(VDATA_BUS[6]),
    .I7(VDATA_BUS[7]), .nWE(1'b1), .nOE(nCLK16), .nCE(1'b0), .O0(VDATA_BUS[0]), .O1(VDATA_BUS[1]),
    .O2(VDATA_BUS[2]), .O3(VDATA_BUS[3]), .O4(VDATA_BUS[4]), .O5(VDATA_BUS[5]), .O6(VDATA_BUS[6]),
    .O7(VDATA_BUS[7]));
  not not_1 (not_1_out, not_2_out);
  T74HC590 t74hc590_1 (
    .nOE(1'b0), .RCLK(CLK1), .nCLKEN(1'b0), .CCLK(nCLK16), .nCCLR(nROM_CNT_RESET), .Q_C(VGA_ROM_ADDR[2]),
    .Q_D(VGA_ROM_ADDR[3]), .Q_E(VGA_ROM_ADDR[4]), .Q_F(VGA_ROM_ADDR[5]), .Q_G(VGA_ROM_ADDR[6]),
    .Q_H(VGA_ROM_ADDR[7]), .Q_B(VGA_ROM_ADDR[1]), .Q_A(VGA_ROM_ADDR[0]), .nRCO(t74hc590_1_nrco));
  not not_2 (not_2_out, CLK16);
  // Probe on VBUS_16
  T74HC590 t74hc590_2 (
    .nOE(1'b0), .RCLK(CLK1), .nCLKEN(t74hc590_1_nrco), .CCLK(nCLK16), .nCCLR(nROM_CNT_RESET),
    .Q_C(VGA_ROM_ADDR[10]), .Q_D(VGA_ROM_ADDR[11]), .Q_E(VGA_ROM_ADDR[12]), .Q_F(VGA_ROM_ADDR[13]),
    .Q_G(VGA_ROM_ADDR[14]), .Q_H(VGA_ROM_ADDR[15]), .Q_B(VGA_ROM_ADDR[9]), .Q_A(VGA_ROM_ADDR[8]));  // open: nRCO
  // Probe on CLK16
  assign VBUS[14] = CLK16 ? CLK8 : 1'bz;  // Controlled_Buffer controlled_buffer_1
  T74HC590 Y_COUNTER (
    .nOE(nCLK16), .RCLK(CLK1), .nCLKEN(nY_CNT), .CCLK(nCLK16), .nCCLR(nY_RESET), .Q_C(VBUS[8]),
    .Q_D(VBUS[9]), .Q_E(VBUS[10]), .Q_F(VBUS[11]), .Q_G(VBUS[12]), .Q_H(VBUS[13]), .Q_B(VBUS[7]),
    .Q_A(VBUS[6]));  // open: nRCO
  _74165 #(.ShowInternalStructure("true")) CHAR_REG (
    .pin1(SHIFT_IN), .pin2(CLK2), .pin3(VDATA_BUS[4]), .pin4(VDATA_BUS[5]), .pin5(VDATA_BUS[6]),
    .pin6(VDATA_BUS[7]), .pin15(CHAR_REG_pin15), .pin14(VDATA_BUS[3]), .pin13(VDATA_BUS[2]),
    .pin12(VDATA_BUS[1]), .pin11(VDATA_BUS[0]), .pin10(CHAR_REG_pin10), .pin9(FG_ACTIVE));  // open: pin7
  Clock clock_1 (.out(CLK1));
  // Probe on CLK16
  // Probe on CLK8
  // Probe on CLK4
  // Probe on CLK2
  // NoConnect on n74163_1_pin15
  _74163 #(.ShowInternalStructure("true")) u_74163_1 (
    .pin1(n74163_1_pin1), .pin2(CLK1), .pin3(n74163_1_pin3), .pin4(n74163_1_pin4), .pin5(n74163_1_pin5),
    .pin6(n74163_1_pin6), .pin7(n74163_1_pin7), .pin15(n74163_1_pin15), .pin14(CLK2), .pin13(CLK4),
    .pin12(CLK8), .pin11(CLK16), .pin10(n74163_1_pin10), .pin9(n74163_1_pin10));
  // NoConnect on n74163_1_pin3
  T74HC590 X_COUNTER (
    .nOE(nCLK16), .RCLK(CLK1), .nCLKEN(nX_CNT), .CCLK(nCLK16), .nCCLR(nX_RESET), .Q_C(VBUS[2]),
    .Q_D(VBUS[3]), .Q_E(VBUS[4]), .Q_F(VBUS[5]), .Q_B(VBUS[1]), .Q_A(VBUS[0]));  // open: Q_G, Q_H, nRCO
  _74377 #(.ShowInternalStructure("true")) COLOR_REG (
    .pin1(COLOR_REG_pin1), .pin2(COLOR_REG_pin2), .pin3(NEW_COLOR_REG[5]), .pin4(NEW_COLOR_REG[1]),
    .pin5(COLOR_REG_pin5), .pin6(COLOR_REG_pin6), .pin7(NEW_COLOR_REG[4]), .pin8(NEW_COLOR_REG[0]),
    .pin9(COLOR_REG_pin9), .pin19(COLOR_REG_pin19), .pin18(NEW_COLOR_REG[2]), .pin17(NEW_COLOR_REG[6]),
    .pin16(COLOR_REG_pin16), .pin15(COLOR_REG_pin15), .pin14(NEW_COLOR_REG[3]), .pin13(NEW_COLOR_REG[7]),
    .pin12(COLOR_REG_pin12), .pin11(COLOR_REG_pin11));
  SST39SF010A sst39sf010a_1 (
    .nOE(1'b0), .nCE(1'b0), .ROM_SELECT(in_3), .A0(VGA_ROM_ADDR[0]), .A1(VGA_ROM_ADDR[1]),
    .A2(VGA_ROM_ADDR[2]), .A3(VGA_ROM_ADDR[3]), .A4(VGA_ROM_ADDR[4]), .A5(VGA_ROM_ADDR[5]),
    .A6(VGA_ROM_ADDR[6]), .A7(VGA_ROM_ADDR[7]), .A8(VGA_ROM_ADDR[8]), .A9(VGA_ROM_ADDR[9]),
    .A10(VGA_ROM_ADDR[10]), .A11(VGA_ROM_ADDR[11]), .A12(VGA_ROM_ADDR[12]), .A13(VGA_ROM_ADDR[13]),
    .A14(VGA_ROM_ADDR[14]), .A15(VGA_ROM_ADDR[15]), .A16(1'b0), .O0(COLOR[8]), .O1(COLOR[13]), .O2(nX_CNT),
    .O3(nY_CNT), .O4(nX_RESET), .O5(nY_RESET), .O6(nROM_CNT_RESET), .O7(VGA_ROM[7]));
  // NoConnect on n74163_1_pin4
  // NoConnect on n74163_1_pin5
  // NoConnect on n74163_1_pin6
  // Probe on VBUS[14:8]
  not not_3 (nCLK1, CLK1);
  not not_4 (nCLK2, CLK2);
  not not_5 (nCLK4, CLK4);
  not not_6 (nCLK8, CLK8);
  not not_7 (nCLK16, CLK16);
  // Probe on VBUS
  // Probe on VBUS
  // Probe on VBUS[7:0]
  // Probe on VBUS[7:0]
  not not_8 (COLOR_REG_pin11, SHIFT_IN);
  _74157 #(.ShowInternalStructure("true")) u_74157_1 (
    .pin1(FG_ACTIVE), .pin2(COLOR_REG_pin9), .pin3(COLOR_REG_pin6), .pin4(COLOR[15]), .pin5(COLOR_REG_pin5),
    .pin6(COLOR_REG_pin2), .pin7(COLOR[10]), .pin15(n74157_1_pin15), .pin14(COLOR_REG_pin19),
    .pin13(COLOR_REG_pin16), .pin12(COLOR[4]), .pin11(COLOR_REG_pin15), .pin10(COLOR_REG_pin12),
    .pin9(COLOR[14]));
  // Probe on NEW_COLOR_REG
  not not_9 (not_9_out, CLK2);
  not not_10 (not_10_out, CLK4);
  not not_11 (not_11_out, CLK8);
  not not_12 (not_12_out, CLK16);
  // Probe on nCOLORS_LATCH
  not not_13 (not_13_out, CLK4);
  not not_14 (not_14_out, CLK16);
  // Probe on SHIFT_IN
  or or_1 (SHIFT_IN, 1'b0, not_9_out, not_10_out, not_11_out, not_12_out);
  or or_2 (nCOLORS_LATCH, not_13_out, CLK8, not_14_out);
  _74377 #(.ShowInternalStructure("true")) u_74377_1 (
    .pin1(nCOLORS_LATCH), .pin2(NEW_COLOR_REG[7]), .pin3(VDATA_BUS[7]), .pin4(VDATA_BUS[6]),
    .pin5(NEW_COLOR_REG[6]), .pin6(NEW_COLOR_REG[3]), .pin7(VDATA_BUS[3]), .pin8(VDATA_BUS[2]),
    .pin9(NEW_COLOR_REG[2]), .pin19(NEW_COLOR_REG[5]), .pin18(VDATA_BUS[5]), .pin17(VDATA_BUS[4]),
    .pin16(NEW_COLOR_REG[4]), .pin15(NEW_COLOR_REG[1]), .pin14(VDATA_BUS[1]), .pin13(VDATA_BUS[0]),
    .pin12(NEW_COLOR_REG[0]), .pin11(CLK2));
  // Probe on VGA_ROM_ADDR
  Divider #(.width(16)) divider_1 (
    .a(VGA_ROM_ADDR), .b(16'h32), .out(divider_1_out), .rem(divider_1_rem));  // open: upper
  // Probe on divider_1_rem
  Bit_Extender #(.in_width(16), .out_width(10)) bit_extender_2 (.in(divider_1_out), .out(Y));
  Multiplier #(.width(16)) multiplier_1 (.a(divider_1_rem), .b(16'h10), .out(multiplier_1_out));  // open: cin, cout
  Counter #(.max('h31f), .width(10)) counter_1 (.count(1'b1), .Q(X), .clk(CLK1));  // open: load, D, carry, up, clr
  // Probe on multiplier_1_out
  // Probe on X
  // RGB_Video #(.height(530), .scale(1), .width(801)) rgb_video_1: pin names not known; wires that end beside it: 1'b0, CLK1, 1'b1, X, Y, {COLOR[15:13], {2{COLOR[13]}}, COLOR[10], COLOR[14], {4{COLOR[8]}}, COLOR[4], COLOR[14], 3'b000}
  // Probe on X
  // Probe on Y
  // Probe on {COLOR[15:13], {2{COLOR[13]}}, COLOR[10], COLOR[14], {4{COLOR[8]}}, COLOR[4], COLOR[14], 3'b000}

  assign {COLOR[12:11], COLOR[9], COLOR[7:5], COLOR[3:0]} = {{2{COLOR[13]}}, COLOR[14], {3{COLOR[8]}}, COLOR[14], 3'b000};
  // also tied to GND on the sheet: {CHAR_REG_pin15, CHAR_REG_pin10, COLOR_REG_pin1, n74157_1_pin15}
  // also tied to VCC on the sheet: {n74163_1_pin1, n74163_1_pin10, n74163_1_pin7}

  // Other names for the same wires on the sheet: BLUE = COLOR[4]; ROM_VSYNC = COLOR[8];
  //   VGA_ROM[6:0] = {nROM_CNT_RESET, nY_RESET, nX_RESET, nY_CNT, nX_CNT, COLOR[13], COLOR[8]}; GREEN = COLOR[10];
  //   ROM_HSYNC = COLOR[13]; WHITE = COLOR[14]; RED = COLOR[15]; nRAM_WE = CLK16; RAW_VGA_CLK = CLK1;
  //   VIDEO_Y[9:0] = Y

  // Notes on the sheet:
  //   in_3: initial=0x3
  //   actual circuit would have vbus facing down
  //   could replace with 32k ram
  //   25.175
  //   12
  //   6
  //   3
  //   1.5
  //   TODO: need to clock into a register to avoid reseting constantly
endmodule

module synced_cpu_vga (
  input  CLK1,
  input  [7:0] BIN,
  input  [15:0] AIN,
  input  nRAM_WRITE_EN,
  input  nRAM_READ_EN,
  output CLK2_OUT,
  output CLK4_OUT,
  output CLK8_OUT,
  output CLK16_OUT,
  output nCLK2_OUT,
  output nCLK4_OUT,
  output nCLK8_OUT,
  output nCLK1_OUT,
  output nCLK16_OUT,
  output [7:0] BOUT,
  output [9:0] X,
  output [9:0] Y,
  output [15:0] COLOR
);

  wire and_2_out, CHAR_REG_pin10, CHAR_REG_pin15, COLOR_REG_pin1, COLOR_REG_pin2, COLOR_REG_pin5,
       COLOR_REG_pin6, COLOR_REG_pin9, COLOR_REG_pin11, COLOR_REG_pin12, COLOR_REG_pin15, COLOR_REG_pin16,
       COLOR_REG_pin19, FG_ACTIVE, n74157_1_pin15, n74163_1_pin1, n74163_1_pin3, n74163_1_pin4,
       n74163_1_pin5, n74163_1_pin6, n74163_1_pin7, n74163_1_pin10, n74163_1_pin11, n74163_1_pin12,
       n74163_1_pin13, n74163_1_pin14, n74163_1_pin15, n74245_2_pin1, n74245_3_pin1, nBUS_OE, nCOLORS_LATCH,
       not_1_out, not_2_out, not_3_out, not_6_out, not_7_out, not_8_out, not_9_out, not_10_out, not_11_out,
       nRAM_OE, nRAM_WE, nROM_CNT_RESET, nX_CNT, nX_RESET, nY_CNT, nY_RESET, or_1_out, or_4_out, or_5_out,
       or_6_out, or_9_out, SHIFT_IN, t74hc590_1_nrco;
  wire [7:0] controlled_buffer_2_out, NEW_COLOR_REG, VDATA_BUS;
  wire [7:7] VGA_ROM;
  wire [15:0] divider_1_out, divider_1_rem, multiplier_1_out, VBUS_16, VGA_ROM_ADDR;

  and and_1 (nRAM_OE, nCLK16_OUT, nRAM_READ_EN);
  and and_2 (and_2_out, nRAM_READ_EN, nRAM_WRITE_EN);
  not not_1 (not_1_out, nRAM_READ_EN);
  not not_2 (not_2_out, nRAM_WRITE_EN);
  or or_1 (or_1_out, CLK16_OUT, nRAM_WRITE_EN);
  assign BOUT = not_1_out ? controlled_buffer_2_out : 8'bz;  // Controlled_Buffer controlled_buffer_1
  assign controlled_buffer_2_out = not_2_out ? BIN : 8'bz;  // Controlled_Buffer controlled_buffer_2
  _74245 #(.ShowInternalStructure("true")) u_74245_1 (
    .pin1(nRAM_WRITE_EN), .pin2(VDATA_BUS[7]), .pin3(VDATA_BUS[6]), .pin4(VDATA_BUS[5]), .pin5(VDATA_BUS[4]),
    .pin6(VDATA_BUS[3]), .pin7(VDATA_BUS[2]), .pin8(VDATA_BUS[1]), .pin9(VDATA_BUS[0]), .pin19(nBUS_OE),
    .pin18(controlled_buffer_2_out[7]), .pin17(controlled_buffer_2_out[6]),
    .pin16(controlled_buffer_2_out[5]), .pin15(controlled_buffer_2_out[4]),
    .pin14(controlled_buffer_2_out[3]), .pin13(controlled_buffer_2_out[2]),
    .pin12(controlled_buffer_2_out[1]), .pin11(controlled_buffer_2_out[0]));
  or or_2 (nBUS_OE, CLK16_OUT, and_2_out);
  or or_3 (nRAM_WE, or_1_out, nCLK8_OUT);
  _74245 #(.ShowInternalStructure("true")) u_74245_2 (
    .pin1(n74245_2_pin1), .pin2(VBUS_16[15]), .pin3(VBUS_16[14]), .pin4(VBUS_16[13]), .pin5(VBUS_16[12]),
    .pin6(VBUS_16[11]), .pin7(VBUS_16[10]), .pin8(VBUS_16[9]), .pin9(VBUS_16[8]), .pin19(nBUS_OE),
    .pin18(AIN[15]), .pin17(AIN[14]), .pin16(AIN[13]), .pin15(AIN[12]), .pin14(AIN[11]), .pin13(AIN[10]),
    .pin12(AIN[9]), .pin11(AIN[8]));
  // Probe on VDATA_BUS
  _74245 #(.ShowInternalStructure("true")) u_74245_3 (
    .pin1(n74245_3_pin1), .pin2(VBUS_16[7]), .pin3(VBUS_16[6]), .pin4(VBUS_16[5]), .pin5(VBUS_16[4]),
    .pin6(VBUS_16[3]), .pin7(VBUS_16[2]), .pin8(VBUS_16[1]), .pin9(VBUS_16[0]), .pin19(nBUS_OE),
    .pin18(AIN[7]), .pin17(AIN[6]), .pin16(AIN[5]), .pin15(AIN[4]), .pin14(AIN[3]), .pin13(AIN[2]),
    .pin12(AIN[1]), .pin11(AIN[0]));
  T74HC590 t74hc590_1 (
    .nOE(1'b0), .RCLK(CLK1), .nCLKEN(1'b0), .CCLK(nCLK16_OUT), .nCCLR(nROM_CNT_RESET), .Q_C(VGA_ROM_ADDR[2]),
    .Q_D(VGA_ROM_ADDR[3]), .Q_E(VGA_ROM_ADDR[4]), .Q_F(VGA_ROM_ADDR[5]), .Q_G(VGA_ROM_ADDR[6]),
    .Q_H(VGA_ROM_ADDR[7]), .Q_B(VGA_ROM_ADDR[1]), .Q_A(VGA_ROM_ADDR[0]), .nRCO(t74hc590_1_nrco));
  // Probe on AIN
  CY7C199 cy7c199_1 (
    .A0(VBUS_16[0]), .A1(VBUS_16[1]), .A2(VBUS_16[2]), .A3(VBUS_16[3]), .A4(VBUS_16[4]), .A5(VBUS_16[5]),
    .A6(VBUS_16[6]), .A7(VBUS_16[7]), .A8(VBUS_16[8]), .A9(VBUS_16[9]), .A10(VBUS_16[10]), .A11(VBUS_16[11]),
    .A12(VBUS_16[12]), .A13(VBUS_16[13]), .A14(VBUS_16[14]), .I0(VDATA_BUS[0]), .I1(VDATA_BUS[1]),
    .I2(VDATA_BUS[2]), .I3(VDATA_BUS[3]), .I4(VDATA_BUS[4]), .I5(VDATA_BUS[5]), .I6(VDATA_BUS[6]),
    .I7(VDATA_BUS[7]), .nWE(nRAM_WE), .nOE(nRAM_OE), .nCE(1'b0), .O0(VDATA_BUS[0]), .O1(VDATA_BUS[1]),
    .O2(VDATA_BUS[2]), .O3(VDATA_BUS[3]), .O4(VDATA_BUS[4]), .O5(VDATA_BUS[5]), .O6(VDATA_BUS[6]),
    .O7(VDATA_BUS[7]));
  // Probe on VBUS_16
  T74HC590 t74hc590_2 (
    .nOE(1'b0), .RCLK(CLK1), .nCLKEN(t74hc590_1_nrco), .CCLK(nCLK16_OUT), .nCCLR(nROM_CNT_RESET),
    .Q_C(VGA_ROM_ADDR[10]), .Q_D(VGA_ROM_ADDR[11]), .Q_E(VGA_ROM_ADDR[12]), .Q_F(VGA_ROM_ADDR[13]),
    .Q_G(VGA_ROM_ADDR[14]), .Q_H(VGA_ROM_ADDR[15]), .Q_B(VGA_ROM_ADDR[9]), .Q_A(VGA_ROM_ADDR[8]));  // open: nRCO
  xor xor_1 (CLK2_OUT, not_3_out, n74163_1_pin14);
  xor xor_2 (CLK4_OUT, not_3_out, n74163_1_pin13);
  xor xor_3 (CLK8_OUT, not_3_out, n74163_1_pin12);
  xor xor_4 (CLK16_OUT, not_3_out, n74163_1_pin11);
  assign VBUS_16[15] = CLK16_OUT ? 1'b0 : 1'bz;  // Controlled_Buffer controlled_buffer_3
  assign VBUS_16[14] = CLK16_OUT ? CLK8_OUT : 1'bz;  // Controlled_Buffer controlled_buffer_4
  T74HC590 Y_COUNTER (
    .nOE(nCLK16_OUT), .RCLK(CLK1), .nCLKEN(nY_CNT), .CCLK(nCLK16_OUT), .nCCLR(nY_RESET), .Q_C(VBUS_16[8]),
    .Q_D(VBUS_16[9]), .Q_E(VBUS_16[10]), .Q_F(VBUS_16[11]), .Q_G(VBUS_16[12]), .Q_H(VBUS_16[13]),
    .Q_B(VBUS_16[7]), .Q_A(VBUS_16[6]));  // open: nRCO
  not not_3 (not_3_out, 1'b0);
  _74165 #(.ShowInternalStructure("true")) CHAR_REG (
    .pin1(SHIFT_IN), .pin2(CLK2_OUT), .pin3(VDATA_BUS[4]), .pin4(VDATA_BUS[5]), .pin5(VDATA_BUS[6]),
    .pin6(VDATA_BUS[7]), .pin15(CHAR_REG_pin15), .pin14(VDATA_BUS[3]), .pin13(VDATA_BUS[2]),
    .pin12(VDATA_BUS[1]), .pin11(VDATA_BUS[0]), .pin10(CHAR_REG_pin10), .pin9(FG_ACTIVE));  // open: pin7
  // Probe on n74163_1_pin11
  // Probe on n74163_1_pin12
  // Probe on n74163_1_pin13
  // Probe on n74163_1_pin14
  // NoConnect on n74163_1_pin15
  _74163 #(.ShowInternalStructure("true")) u_74163_1 (
    .pin1(n74163_1_pin1), .pin2(CLK1), .pin3(n74163_1_pin3), .pin4(n74163_1_pin4), .pin5(n74163_1_pin5),
    .pin6(n74163_1_pin6), .pin7(n74163_1_pin7), .pin15(n74163_1_pin15), .pin14(n74163_1_pin14),
    .pin13(n74163_1_pin13), .pin12(n74163_1_pin12), .pin11(n74163_1_pin11), .pin10(n74163_1_pin10),
    .pin9(n74163_1_pin10));
  // Probe on VBUS_16[15:8]
  Clock clock_1 ();  // open: out
  // NoConnect on n74163_1_pin3
  // NoConnect on n74163_1_pin4
  // NoConnect on n74163_1_pin5
  // NoConnect on n74163_1_pin6
  T74HC590 X_COUNTER (
    .nOE(nCLK16_OUT), .RCLK(CLK1), .nCLKEN(nX_CNT), .CCLK(nCLK16_OUT), .nCCLR(nX_RESET), .Q_C(VBUS_16[2]),
    .Q_D(VBUS_16[3]), .Q_E(VBUS_16[4]), .Q_F(VBUS_16[5]), .Q_B(VBUS_16[1]), .Q_A(VBUS_16[0]));  // open: Q_G, Q_H, nRCO
  _74377 #(.ShowInternalStructure("true")) COLOR_REG (
    .pin1(COLOR_REG_pin1), .pin2(COLOR_REG_pin2), .pin3(NEW_COLOR_REG[5]), .pin4(NEW_COLOR_REG[1]),
    .pin5(COLOR_REG_pin5), .pin6(COLOR_REG_pin6), .pin7(NEW_COLOR_REG[4]), .pin8(NEW_COLOR_REG[0]),
    .pin9(COLOR_REG_pin9), .pin19(COLOR_REG_pin19), .pin18(NEW_COLOR_REG[2]), .pin17(NEW_COLOR_REG[6]),
    .pin16(COLOR_REG_pin16), .pin15(COLOR_REG_pin15), .pin14(NEW_COLOR_REG[3]), .pin13(NEW_COLOR_REG[7]),
    .pin12(COLOR_REG_pin12), .pin11(COLOR_REG_pin11));
  SST39SF010A sst39sf010a_1 (
    .nOE(1'b0), .nCE(1'b0), .ROM_SELECT(2'b11), .A0(VGA_ROM_ADDR[0]), .A1(VGA_ROM_ADDR[1]),
    .A2(VGA_ROM_ADDR[2]), .A3(VGA_ROM_ADDR[3]), .A4(VGA_ROM_ADDR[4]), .A5(VGA_ROM_ADDR[5]),
    .A6(VGA_ROM_ADDR[6]), .A7(VGA_ROM_ADDR[7]), .A8(VGA_ROM_ADDR[8]), .A9(VGA_ROM_ADDR[9]),
    .A10(VGA_ROM_ADDR[10]), .A11(VGA_ROM_ADDR[11]), .A12(VGA_ROM_ADDR[12]), .A13(VGA_ROM_ADDR[13]),
    .A14(VGA_ROM_ADDR[14]), .A15(VGA_ROM_ADDR[15]), .A16(1'b0), .O0(COLOR[8]), .O1(COLOR[13]), .O2(nX_CNT),
    .O3(nY_CNT), .O4(nX_RESET), .O5(nY_RESET), .O6(nROM_CNT_RESET), .O7(VGA_ROM[7]));
  not not_4 (nCLK1_OUT, CLK1);
  // Probe on VBUS_16
  // Probe on VBUS_16
  // Probe on VBUS_16[7:0]
  // Probe on VBUS_16[7:0]
  not not_5 (COLOR_REG_pin11, SHIFT_IN);
  _74157 #(.ShowInternalStructure("true")) u_74157_1 (
    .pin1(FG_ACTIVE), .pin2(COLOR_REG_pin9), .pin3(COLOR_REG_pin6), .pin4(COLOR[15]), .pin5(COLOR_REG_pin5),
    .pin6(COLOR_REG_pin2), .pin7(COLOR[10]), .pin15(n74157_1_pin15), .pin14(COLOR_REG_pin19),
    .pin13(COLOR_REG_pin16), .pin12(COLOR[4]), .pin11(COLOR_REG_pin15), .pin10(COLOR_REG_pin12),
    .pin9(COLOR[14]));
  xor xor_5 (nCLK2_OUT, 1'b0, n74163_1_pin14);
  xor xor_6 (nCLK4_OUT, 1'b0, n74163_1_pin13);
  xor xor_7 (nCLK8_OUT, 1'b0, n74163_1_pin12);
  xor xor_8 (nCLK16_OUT, 1'b0, n74163_1_pin11);
  // Probe on NEW_COLOR_REG
  not not_6 (not_6_out, CLK2_OUT);
  not not_7 (not_7_out, CLK4_OUT);
  not not_8 (not_8_out, CLK8_OUT);
  not not_9 (not_9_out, CLK16_OUT);
  // Probe on or_6_out
  not not_10 (not_10_out, CLK4_OUT);
  not not_11 (not_11_out, CLK16_OUT);
  or or_4 (or_4_out, nCLK16_OUT, nCLK4_OUT);
  // Probe on or_5_out
  or or_5 (or_5_out, not_6_out, not_7_out, not_8_out, not_9_out);
  or or_6 (or_6_out, not_10_out, CLK8_OUT, not_11_out);
  or or_7 (nCOLORS_LATCH, or_4_out, CLK8_OUT);
  or or_8 (SHIFT_IN, or_4_out, or_9_out);
  or or_9 (or_9_out, nCLK2_OUT, nCLK8_OUT);
  _74377 #(.ShowInternalStructure("true")) u_74377_1 (
    .pin1(nCOLORS_LATCH), .pin2(NEW_COLOR_REG[7]), .pin3(VDATA_BUS[7]), .pin4(VDATA_BUS[6]),
    .pin5(NEW_COLOR_REG[6]), .pin6(NEW_COLOR_REG[3]), .pin7(VDATA_BUS[3]), .pin8(VDATA_BUS[2]),
    .pin9(NEW_COLOR_REG[2]), .pin19(NEW_COLOR_REG[5]), .pin18(VDATA_BUS[5]), .pin17(VDATA_BUS[4]),
    .pin16(NEW_COLOR_REG[4]), .pin15(NEW_COLOR_REG[1]), .pin14(VDATA_BUS[1]), .pin13(VDATA_BUS[0]),
    .pin12(NEW_COLOR_REG[0]), .pin11(CLK2_OUT));
  // Probe on VGA_ROM_ADDR
  Bit_Extender #(.in_width(16), .out_width(10)) bit_extender_1 (.in(divider_1_out), .out(Y));
  Divider #(.width(16)) divider_1 (
    .a(VGA_ROM_ADDR), .b(16'h32), .out(divider_1_out), .rem(divider_1_rem));  // open: upper
  // Probe on divider_1_rem
  Counter #(.max('h31f), .width(10)) counter_1 (.count(1'b1), .Q(X), .clk(CLK1));  // open: load, D, carry, up, clr
  // Probe on multiplier_1_out
  Multiplier #(.width(16)) multiplier_1 (.a(divider_1_rem), .b(16'h10), .out(multiplier_1_out));  // open: cin, cout
  // Probe on X
  // Probe on X
  // Probe on Y
  // RGB_Video #(.height(530), .scale(1), .width(803)) rgb_video_1: pin names not known; wires that end beside it: 1'b0, CLK1, 1'b1, X, Y, {COLOR[15:13], {2{COLOR[13]}}, COLOR[10], COLOR[14], {4{COLOR[8]}}, COLOR[4], COLOR[14], 3'b000}
  // Probe on {COLOR[15:13], {2{COLOR[13]}}, COLOR[10], COLOR[14], {4{COLOR[8]}}, COLOR[4], COLOR[14], 3'b000}

  assign {COLOR[12:11], COLOR[9], COLOR[7:5], COLOR[3:0]} = {{2{COLOR[13]}}, COLOR[14], {3{COLOR[8]}}, COLOR[14], 3'b000};
  // also tied to GND on the sheet: {n74245_2_pin1, n74245_3_pin1, CHAR_REG_pin15, CHAR_REG_pin10, COLOR_REG_pin1, n74157_1_pin15}
  // also tied to VCC on the sheet: {n74163_1_pin1, n74163_1_pin10, n74163_1_pin7}

  // Other names for the same wires on the sheet: CLK2 = CLK2_OUT; CLK4 = CLK4_OUT; CLK8 = CLK8_OUT; CLK16 = CLK16_OUT;
  //   BLUE = COLOR[4]; ROM_VSYNC = COLOR[8];
  //   VGA_ROM[6:0] = {nROM_CNT_RESET, nY_RESET, nX_RESET, nY_CNT, nX_CNT, COLOR[13], COLOR[8]}; GREEN = COLOR[10];
  //   ROM_HSYNC = COLOR[13]; WHITE = COLOR[14]; RED = COLOR[15]; nCLK1 = nCLK1_OUT; nCLK2 = nCLK2_OUT;
  //   nCLK4 = nCLK4_OUT; nCLK8 = nCLK8_OUT; nCLK16 = nCLK16_OUT; VIDEO_Y[9:0] = Y

  // Notes on the sheet:
  //   nRAM_WRITE_EN: initial=0x1
  //   nRAM_READ_EN: initial=0x1
  //   might already have in form of vram enable
  //   assumes cpu runs with clk = clk8
  //   12
  //   6
  //   3
  //   1.5
  //   actual circuit would have vbus facing down
  //   could replace with 32k ram
  //   25.175
  //   TODO: need to clock into a register to avoid reseting constantly
  //   12
  //   6
  //   3
  //   1.5
  //   TODO: might accidentally latch on counter transitions causing cut off characters
  //   might be fine with hardware, maybe not
endmodule

module main (
  input  RESET,
  input  in_2,
  input  in_3,
  output [2:0] IR,
  output [7:0] IR2,
  output [2:0] out_6,
  output [13:0] out_7
);

  wire A_ZERO, ALU_CARRY_IN, CLK, decoder_1_out1, decoder_1_out2, decoder_1_out3, decoder_1_out4,
       decoder_1_out5, decoder_1_out6, decoder_1_out7, decoder_1_out9, decoder_1_out10, decoder_1_out11,
       decoder_1_out12, decoder_1_out13, decoder_1_out14, decoder_1_out15, decoder_2_out0, decoder_2_out1,
       decoder_2_out2, decoder_2_out3, decoder_3_out0, decoder_3_out1, decoder_3_out2, decoder_3_out6,
       decoder_3_out7, decoder_3_out11, decoder_3_out12, decoder_3_out13, decoder_3_out14, decoder_4_out0,
       decoder_4_out1, decoder_4_out2, decoder_4_out3, DIRECT_CLK, FAST_CLK, FAST_INV_CLK, FLAG_BIN_EN,
       INV_CLK, keyboard_1_avail, MAR_CNT, MEM_READ, MEM_WRITE, n74151_1_pin4, n74151_1_pin5, n74151_1_pin6,
       n74151_1_pin7, n74151_1_pin12, n74151_1_pin13, n74151_1_pin14, n74151_1_pin15, n74157_1_pin4,
       n74157_1_pin7, n74157_1_pin9, n74157_1_pin12, n74157_1_pin14, n74157_1_pin15, n74245_1_pin1,
       n74245_1_pin6, n74245_1_pin7, n74245_1_pin8, n74245_1_pin9, nA_BOUT_EN, nA_WRITE, nABUS_TO_BUS_HIGH,
       nABUS_TO_BUS_LOW, nB_BOUT_EN, nB_WRITE, nF_BOUT_EN, nFLAG_BOUT, nHALT, nIR2_WRITE, nIR_WRITE,
       nKEYB_BOUT, nMAR_AOUT, nMAR_LOAD_HIGH, nMAR_LOAD_LOW, not_26_out, not_27_out, not_30_out, not_31_out,
       nPC_AOUT, nPC_LOAD_HIGH, nPC_LOAD_LOW, nRESET, nRESET_MICRO, nSP_AOUT, nSP_LOAD_HIGH, nSP_LOAD_LOW,
       nX_BOUT, nY_BOUT, nZ_BOUT, or_1_out, PC_CNT, PC_LOAD_HIGH, PC_LOAD_LOW, SP_CNTDOWN, SP_CNTUP, X_WRITE,
       Y_WRITE, Z_WRITE;
  wire [1:0] ADDR_CONTROL_DEC, ALU_FLAGS;
  wire [2:0] OTHER_DEC;
  wire [3:0] BUS_CONTROL_DEC, BUS_WRITE_DEC;
  wire [3:1] Q_FLAGS;
  wire [3:3] INTRUCTION_CNTR_q;
  wire [6:0] keyboard_1_data;
  wire [7:0] BBUS, bit_extender_1_out, dipswitch_1_sw8;
  wire [7:3] IR2_q;
  wire [15:0] ABUS, dipswitch_2_sw16, rom_1_data;
  wire [15:13] register_1_q;

  not not_1 (nRESET, RESET);
  Decoder #(.select(4)) decoder_1 (
    .out1(decoder_1_out1), .out2(decoder_1_out2), .out3(decoder_1_out3), .out4(decoder_1_out4),
    .out5(decoder_1_out5), .out6(decoder_1_out6), .out7(decoder_1_out7), .out8(MEM_READ),
    .out9(decoder_1_out9), .out10(decoder_1_out10), .out11(decoder_1_out11), .out12(decoder_1_out12),
    .out13(decoder_1_out13), .out14(decoder_1_out14), .out15(decoder_1_out15), .sel(BUS_CONTROL_DEC),
    .en(1'b1));  // open: out0
  Decoder #(.select(2)) decoder_2 (
    .out0(decoder_2_out0), .out1(decoder_2_out1), .out2(decoder_2_out2), .out3(decoder_2_out3),
    .sel(ADDR_CONTROL_DEC), .en(1'b1));
  Decoder #(.select(4)) decoder_3 (
    .out0(decoder_3_out0), .out1(decoder_3_out1), .out2(decoder_3_out2), .out3(X_WRITE), .out4(Y_WRITE),
    .out5(Z_WRITE), .out6(decoder_3_out6), .out7(decoder_3_out7), .out8(MEM_WRITE), .out9(PC_LOAD_LOW),
    .out10(PC_LOAD_HIGH), .out11(decoder_3_out11), .out12(decoder_3_out12), .out13(decoder_3_out13),
    .out14(decoder_3_out14), .out15(FLAG_BIN_EN), .sel(BUS_WRITE_DEC), .en(FAST_CLK));
  Decoder #(.select(3)) decoder_4 (
    .out0(decoder_4_out0), .out1(decoder_4_out1), .out2(decoder_4_out2), .out3(decoder_4_out3),
    .out4(PC_CNT), .out5(MAR_CNT), .out6(SP_CNTUP), .out7(SP_CNTDOWN), .sel(OTHER_DEC), .en(FAST_CLK));
  not not_2 (nA_BOUT_EN, decoder_1_out1);
  not not_3 (nB_BOUT_EN, decoder_1_out2);
  not not_4 (nX_BOUT, decoder_1_out3);
  not not_5 (nY_BOUT, decoder_1_out4);
  not not_6 (nZ_BOUT, decoder_1_out5);
  not not_7 (nABUS_TO_BUS_LOW, decoder_1_out6);
  not not_8 (nABUS_TO_BUS_HIGH, decoder_1_out7);
  not not_9 (nF_BOUT_EN, decoder_1_out9);
  not not_10 (nFLAG_BOUT, decoder_1_out10);
  not not_11 (nKEYB_BOUT, decoder_1_out12);
  not not_12 (nHALT, decoder_1_out14);
  not not_13 (nRESET_MICRO, decoder_1_out15);
  not not_14 (nPC_AOUT, decoder_2_out1);
  not not_15 (nMAR_AOUT, decoder_2_out2);
  not not_16 (nSP_AOUT, decoder_2_out3);
  not not_17 (nA_WRITE, decoder_3_out1);
  not not_18 (nB_WRITE, decoder_3_out2);
  not not_19 (nMAR_LOAD_LOW, decoder_3_out6);
  not not_20 (nMAR_LOAD_HIGH, decoder_3_out7);
  not not_21 (nSP_LOAD_LOW, decoder_3_out11);
  not not_22 (nSP_LOAD_HIGH, decoder_3_out12);
  not not_23 (nIR_WRITE, decoder_3_out13);
  not not_24 (nIR2_WRITE, decoder_3_out14);
  and and_1 (FAST_CLK, DIRECT_CLK, nHALT);
  Clock clock_1 (.out(DIRECT_CLK));
  not not_25 (FAST_INV_CLK, FAST_CLK);
  not not_26 (not_26_out, FAST_INV_CLK);
  not not_27 (not_27_out, not_26_out);
  not not_28 (CLK, not_27_out);
  generic_8bit_register u_IR2 (.nWE(nIR2_WRITE), .D(BBUS), .CLOCK(CLK), .Q({IR2_q, out_6}));
  generic_8bit_register generic_8bit_register_1 (.nWE(nIR_WRITE), .D(BBUS), .CLOCK(CLK), .Q(IR2));
  counter4 INTRUCTION_CNTR (
    .nCLEAR(nRESET_MICRO), .CNT_EN(1'b1), .nLOAD_EN(1'b1), .CLOCK(FAST_INV_CLK),
    .Q({INTRUCTION_CNTR_q[3], IR}));  // open: D
  not not_29 (INV_CLK, CLK);
  ROM #(.addrWidth(14), .dataWidth(16)) rom_1 (.addr({out_6, IR2, IR}), .data(rom_1_data));
  // Probe on rom_1_data
  // Probe on {register_1_q, OTHER_DEC, BUS_WRITE_DEC, ADDR_CONTROL_DEC, BUS_CONTROL_DEC}
  Register #(.width(16)) register_1 (
    .D(rom_1_data), .en(1'b1), .clk(INV_CLK),
    .Q({register_1_q, OTHER_DEC, BUS_WRITE_DEC, ADDR_CONTROL_DEC, BUS_CONTROL_DEC}), .clr(RESET));
  ram_assembly ram_assembly_1 (
    .MEM_READ(MEM_READ), .MEM_WRITE(MEM_WRITE), .nSP_CNTDOWN(SP_CNTDOWN), .nSP_LOAD_LOW(nSP_LOAD_LOW),
    .nSP_LOAD_HIGH(nSP_LOAD_HIGH), .nPC_AOUT(nPC_AOUT), .PC_CNT(PC_CNT), .nPC_LOAD_LOW(nPC_LOAD_LOW),
    .nPC_LOAD_HIGH(nPC_LOAD_HIGH), .nMAR_AOUT(nMAR_AOUT), .MAR_CNT(MAR_CNT), .nMAR_LOAD_LOW(nMAR_LOAD_LOW),
    .nMAR_LOAD_HIGH(nMAR_LOAD_HIGH), .nSP_AOUT(nSP_AOUT), .nSP_CNTUP(SP_CNTUP),
    .nLOW_ATOB_EN(nABUS_TO_BUS_LOW), .nHIGH_ATOB_EN(nABUS_TO_BUS_HIGH), .nRESET(nRESET), .CLOCK(CLK),
    .AIN(ABUS), .BIN(BBUS), .AOUT(ABUS), .BOUT(BBUS));
  // LedBar #(.inputtype("row"), .matrixcols(4)) ledbar_1: pin names not known; wires that end beside it: BUS_CONTROL_DEC
  // LedBar #(.inputtype("row"), .matrixcols(2)) ledbar_2: pin names not known; wires that end beside it: ADDR_CONTROL_DEC
  // LedBar #(.inputtype("row"), .matrixcols(3)) ledbar_3: pin names not known; wires that end beside it: OTHER_DEC
  // LedBar #(.inputtype("row"), .matrixcols(4)) ledbar_4: pin names not known; wires that end beside it: BUS_WRITE_DEC
  // LedBar #(.inputtype("row"), .matrixcols(16)) ledbar_5: pin names not known; wires that end beside it: {register_1_q, OTHER_DEC, BUS_WRITE_DEC, ADDR_CONTROL_DEC, BUS_CONTROL_DEC}
  Keyboard #(.trigger("falling")) keyboard_1 (
    .clk(CLK), .re(1'b1), .clr(1'b0), .avail(keyboard_1_avail), .data(keyboard_1_data));
  DipSwitch dipswitch_1 (
    .sw1(dipswitch_1_sw8[7]), .sw2(dipswitch_1_sw8[6]), .sw3(dipswitch_1_sw8[5]), .sw4(dipswitch_1_sw8[4]),
    .sw5(dipswitch_1_sw8[3]), .sw6(dipswitch_1_sw8[2]), .sw7(dipswitch_1_sw8[1]), .sw8(dipswitch_1_sw8[0]));
  // LedBar #(.inputtype("row")) ledbar_6: pin names not known; wires that end beside it: BBUS
  assign BBUS = in_2 ? dipswitch_1_sw8 : 8'bz;  // Controlled_Buffer controlled_buffer_1
  _74157 #(.ShowInternalStructure("true")) u_74157_1 (
    .pin1(FLAG_BIN_EN), .pin2(ALU_FLAGS[0]), .pin3(BBUS[0]), .pin4(n74157_1_pin4), .pin5(ALU_FLAGS[1]),
    .pin6(BBUS[1]), .pin7(n74157_1_pin7), .pin15(n74157_1_pin15), .pin14(n74157_1_pin14), .pin13(BBUS[3]),
    .pin12(n74157_1_pin12), .pin11(A_ZERO), .pin10(BBUS[2]), .pin9(n74157_1_pin9));
  assign bit_extender_1_out = {{1{1'b0}}, keyboard_1_data};  // Bit_Extender bit_extender_1
  Pull_Resistor pull_resistor_1 (.node(BBUS));
  DipSwitch #(.number(16)) dipswitch_2 (
    .sw1(dipswitch_2_sw16[15]), .sw2(dipswitch_2_sw16[14]), .sw3(dipswitch_2_sw16[13]),
    .sw4(dipswitch_2_sw16[12]), .sw5(dipswitch_2_sw16[11]), .sw6(dipswitch_2_sw16[10]),
    .sw7(dipswitch_2_sw16[9]), .sw8(dipswitch_2_sw16[8]), .sw9(dipswitch_2_sw16[7]),
    .sw10(dipswitch_2_sw16[6]), .sw11(dipswitch_2_sw16[5]), .sw12(dipswitch_2_sw16[4]),
    .sw13(dipswitch_2_sw16[3]), .sw14(dipswitch_2_sw16[2]), .sw15(dipswitch_2_sw16[1]),
    .sw16(dipswitch_2_sw16[0]));
  // LedBar #(.inputtype("row"), .matrixcols(16)) ledbar_7: pin names not known; wires that end beside it: ABUS
  T74HC173 t74hc173_1 (
    .M(1'b0), .N(1'b0), .CLK(CLK), .nCLR(nRESET), .D1(n74157_1_pin4), .D2(n74157_1_pin7), .D3(n74157_1_pin9),
    .D4(n74157_1_pin12), .nG2(not_30_out), .nG1(not_30_out), .Q1(ALU_CARRY_IN), .Q2(Q_FLAGS[1]),
    .Q3(Q_FLAGS[2]), .Q4(Q_FLAGS[3]));
  XYZ_regs xyz_regs_1 (
    .X_WE(X_WRITE), .nX_BOUT(nX_BOUT), .Y_WE(Y_WRITE), .nY_BOUT(nY_BOUT), .Z_WE(Z_WRITE), .nZ_BOUT(nZ_BOUT),
    .nRESET(nRESET), .CLOCK(CLK), .BIN(BBUS), .BOUT(BBUS));
  // gp_register gp_register_1: pin names not known; wires that end beside it: CLK, bit_extender_1_out, keyboard_1_avail, nRESET, nKEYB_BOUT, BBUS
  Pull_Resistor pull_resistor_2 (.node(ABUS));
  assign ABUS = in_3 ? dipswitch_2_sw16 : 16'bz;  // Controlled_Buffer controlled_buffer_2
  ALU_assembly alu_assembly_1 (
    .B_WE(nB_WRITE), .nA_BOUT_EN(nA_BOUT_EN), .nB_BOUT_EN(nB_BOUT_EN), .nF_BOUT_EN(nF_BOUT_EN),
    .A_WE(nA_WRITE), .CLOCK(CLK), .BIN(BBUS), .ALU_CARRY_IN(ALU_CARRY_IN), .S0(IR2[4]), .S1(IR2[5]),
    .S2(IR2[6]), .S3(IR2[7]), .CARRY_OUT(ALU_FLAGS[0]), .EQUAL(ALU_FLAGS[1]), .A_ZERO(A_ZERO), .BOUT(BBUS));
  not not_30 (not_30_out, or_1_out);
  _74245 u_74245_1 (
    .pin1(n74245_1_pin1), .pin2(ALU_CARRY_IN), .pin3(Q_FLAGS[1]), .pin4(Q_FLAGS[2]), .pin5(Q_FLAGS[3]),
    .pin6(n74245_1_pin6), .pin7(n74245_1_pin7), .pin8(n74245_1_pin8), .pin9(n74245_1_pin9),
    .pin19(nFLAG_BOUT), .pin18(BBUS[0]), .pin17(BBUS[1]), .pin16(BBUS[2]), .pin15(BBUS[3]));  // open: pin14, pin13, pin12, pin11
  not not_31 (not_31_out, nF_BOUT_EN);
  or or_1 (or_1_out, not_31_out, FLAG_BIN_EN);
  _74151 #(.ShowInternalStructure("true")) u_74151_1 (
    .pin1(Q_FLAGS[2]), .pin2(Q_FLAGS[1]), .pin3(ALU_CARRY_IN), .pin4(n74151_1_pin4), .pin5(n74151_1_pin5),
    .pin6(n74151_1_pin6), .pin7(n74151_1_pin7), .pin15(n74151_1_pin15), .pin14(n74151_1_pin14),
    .pin13(n74151_1_pin13), .pin12(n74151_1_pin12), .pin11(OTHER_DEC[0]), .pin10(OTHER_DEC[1]),
    .pin9(OTHER_DEC[2]));
  // NoConnect on n74151_1_pin6
  nand nand_1 (nPC_LOAD_LOW, PC_LOAD_LOW, n74151_1_pin5);
  nand nand_2 (nPC_LOAD_HIGH, PC_LOAD_HIGH, n74151_1_pin5);

  assign out_7 = {out_6, IR2, IR};
  // also tied to GND on the sheet: {n74157_1_pin15, n74157_1_pin14, n74245_1_pin6, n74245_1_pin7, n74245_1_pin8, n74245_1_pin9, n74151_1_pin7}
  // also tied to VCC on the sheet: {n74245_1_pin1, n74151_1_pin15, n74151_1_pin14, n74151_1_pin13, n74151_1_pin4, n74151_1_pin12}

  // Other names for the same wires on the sheet: CARRY = ALU_FLAGS[0]; EQUAL = ALU_FLAGS[1]; ALU_FLAGS[2] = A_ZERO;
  //   FLAG_WRITE = FLAG_BIN_EN; IR_t[7:0] = IR2; IR_ISTR_WORD[3:0] = IR2[7:4]; Q_FLAGS[0] = ALU_CARRY_IN

  // Notes on the sheet:
  //   write from bus decoder
  //   other decoder
  //   out on bus decoder
  //   always want output on the bus
  //   always want output on the abus
  //   used for flag conditional jump
  //   might be weird to integrate with bout
  //   3 bits of micro instr
  //   contents of rom_1 (hex, n*v repeats v):
  //   358 400 398 441 4*f 358 400 398 481 4*f 358 400 398 4c1 4*f 358 400 398 501 4*f 358 400 398 541 4*f
  //   358 400 398 581 4*f 358 400 398 5c1 4*f 358 400 398 401 4*f 358 400 58 400 4*f 358 400 98 400 4*f
  //   358 400 d8 400 4*f 358 400 118 400 4*f 358 400 158 400 4*f 358 400 198 400 4*f 358 400 1d8 400 4*f
  //   358 400 18 400 4*f 358 68 400 5*f 358 a8 400 5*f 358 e8 400 5*f 358 128 400 5*f 358 168 400 5*f 358
  //   1a8 400 5*f 358 1e8 400 5*f 358 28 400 5*f 358 400 198 400 1d8 468 f f 358 400 198 400 1d8 4a8 f f
  //   358 400 198 400 1d8 4e8 f f 358 400 198 400 1d8 528 f f 358 400 198 400 1d8 568 f f 358 400 198 400
  //   1d8 5a8 f f 358 400 198 400 1d8 5e8 f f 358 400 198 400 1d8 428 f f 358 621 6*f 358 622 6*f 358 623
  //   6*f 358 624 6*f 358 625 6*f 358 626 6*f 358 627 6*f 358 620 6*f 358 400 198 400 1d8 621 f f 358 400
  //   198 400 1d8 622 f f 358 400 198 400 1d8 623 f f 358 400 198 400 1d8 624 f f 358 400 198 400 1d8 625
  //   f f 358 400 198 400 1d8 626 f f 358 400 198 400 1d8 627 f f 358 400 198 400 1d8 620 f f 358 631 1000
  //   5*f 358 632 1000 5*f 358 633 1000 5*f 358 634 1000 5*f 358 635 1000 5*f 358 636 1000 5*f 358 637
  //   1000 5*f 358 630 1000 5*f 358 400 398 63b 1000 f f f 358 400 398 63b 1000 f f f 358 400 398 63b 1000
  //   f f f 358 400 398 63b 1000 f f f 358 400 398 63b 1000 f f f 358 400 398 63b 1000 f f f 358 400 398
  //   63b 1000 f f f 358 400 398 63b 1000 f f f 358 439 c00 5*f 358 43a c00 5*f 358 43b c00 5*f 358 43c
  //   c00 5*f 358 43d c00 5*f 358 43e c00 5*f 358 43f c00 5*f 358 438 c00 5*f 358 439 c00 5*f 358 43a c00
  //   5*f 358 43b c00 5*f 358 43c c00 5*f 358 43d c00 5*f 358 43e c00 5*f 358 43f c00 5*f 358 438 c00 5*f
  //   358 400 198 400 1d8 400 f f 358 400 198 400 1d8 400 f f 358 400 198 400 1d8 400 f f 358 400 198 400
  //   1d8 400 f f 358 400 198 400 1d8 400 f f 358 400 198 400 1d8 400 f f 358 400 198 400 1d8 400 f f 358
  //   400 198 400 1d8 400 f f 358 400 198 400 1d8 400 f f 358 400 198 400 1d8 400 f f 358 400 198 400 1d8
  //   400 f f 358 400 198 400 1d8 400 f f 358 400 198 400 1d8 400 f f 358 400 198 400 1d8 400 f f 358 400
  //   198 400 1d8 400 f f 358 400 198 400 1d8 400 f f 358 400 1676 16b7 4*f 358 442 1676 16b7 4*f 358 443
  //   1676 16b7 4*f 358 444 1676 16b7 4*f 358 445 1676 16b7 4*f 358 466 1676 16b7 4*f 358 467 1676 16b7
  //   4*f 358 440 1676 16b7 4*f 358 276 2b7 5*f 358 276 2b7 5*f 358 276 2b7 5*f 358 276 2b7 5*f 358 276
  //   2b7 5*f 358 276 2b7 5*f 358 276 2b7 5*f 358 276 2b7 5*f 1152*ffff 358 400 398 442 4*f 358 400 398
  //   482 4*f 358 400 398 4c2 4*f 358 400 398 502 4*f 358 400 398 542 4*f 358 400 398 582 4*f 358 400 398
  //   5c2 4*f 358 400 398 402 4*f 358 400 58 400 4*f 358 400 98 400 4*f 358 400 d8 400 4*f 358 400 118 400
  //   4*f 358 400 158 400 4*f 358 400 198 400 4*f 358 400 1d8 400 4*f 358 400 18 400 4*f 358 68 400 5*f
  //   358 a8 400 5*f 358 e8 400 5*f 358 128 400 5*f 358 168 400 5*f 358 1a8 400 5*f 358 1e8 400 5*f 358 28
  //   400 5*f 358 400 198 400 1d8 468 f f 358 400 198 400 1d8 4a8 f f 358 400 198 400 1d8 4e8 f f 358 400
  //   198 400 1d8 528 f f 358 400 198 400 1d8 568 f f 358 400 198 400 1d8 5a8 f f 358 400 198 400 1d8 5e8
  //   f f 358 400 198 400 1d8 428 f f 358 621 6*f 358 622 6*f 358 623 6*f 358 624 6*f 358 625 6*f 358 626
  //   6*f 358 627 6*f 358 620 6*f 358 400 198 400 1d8 621 f f 358 400 198 400 1d8 622 f f 358 400 198 400
  //   1d8 623 f f 358 400 198 400 1d8 624 f f 358 400 198 400 1d8 625 f f 358 400 198 400 1d8 626 f f 358
  //   400 198 400 1d8 627 f f 358 400 198 400 1d8 620 f f 358 631 1000 5*f 358 632 1000 5*f 358 633 1000
  //   5*f 358 634 1000 5*f 358 635 1000 5*f 358 636 1000 5*f 358 637 1000 5*f 358 630 1000 5*f 358 400 398
  //   63b 1000 f f f 358 400 398 63b 1000 f f f 358 400 398 63b 1000 f f f 358 400 398 63b 1000 f f f 358
  //   400 398 63b 1000 f f f 358 400 398 63b 1000 f f f 358 400 398 63b 1000 f f f 358 400 398 63b 1000 f
  //   f f 358 439 c00 5*f 358 43a c00 5*f 358 43b c00 5*f 358 43c c00 5*f 358 43d c00 5*f 358 43e c00 5*f
  //   358 43f c00 5*f 358 438 c00 5*f 358 439 c00 5*f 358 43a c00 5*f 358 43b c00 5*f 358 43c c00 5*f 358
  //   43d c00 5*f 358 43e c00 5*f 358 43f c00 5*f 358 438 c00 5*f 358 400 198 400 1d8 400 f f 358 400 198
  //   400 1d8 400 f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
  //   used to select alu math mode
  //   STEP
  //   TODO: output only on fast clk?
  //   4-8 options are direct
endmodule

module alu (
  input  [7:0] A,
  input  [7:0] B,
  input  sel0,
  input  sel1,
  input  sel2,
  input  sel3,
  input  ALU_CARRY_IN,
  output [7:0] F,
  output CARRY_OUT,
  output EQ,
  output A_ZERO
);

  wire ALU_CARRY_IN0, ALU_CARRY_IN1, ALU_S0, ALU_S1, ALU_S2, and_1_out, and_2_out, and_4_out, fAND, ffOR,
       fNOT, fSUB, fSUB_CARRY_EN, fSUM, fSUM_CARRY_EN, fXOR, nand_1_out, not_1_out, not_2_out, not_3_out,
       not_4_out, not_5_out, not_6_out, not_7_out, not_8_out, not_12_out, not_13_out, not_14_out, not_15_out,
       not_18_out, or_1_out, or_2_out, or_3_out, or_4_out, or_5_out, or_6_out, or_7_out, or_8_out, or_9_out,
       or_10_out, or_11_out;

  // _74181 #(.ShowInternalStructure("true")) 74181_1: pin names not known; wires that end beside it: B[0], A[0], sel1, ALU_S2, ALU_S1, ALU_S0, ALU_CARRY_IN0, sel2, F[0], F[1], F[2], A[1], B[1], A[2], B[2], A[3], B[3], ALU_CARRY_IN1, EQ, F[3]
  or or_1 (or_1_out, A[0], A[1]);
  or or_2 (or_2_out, A[2], A[3]);
  or or_3 (or_3_out, A[4], A[5]);
  or or_4 (or_4_out, A[6], A[7]);
  not not_1 (not_1_out, A[0]);
  not not_2 (not_2_out, A[1]);
  not not_3 (not_3_out, A[2]);
  not not_4 (not_4_out, A[3]);
  not not_5 (not_5_out, A[4]);
  not not_6 (not_6_out, A[5]);
  not not_7 (not_7_out, A[6]);
  not not_8 (not_8_out, A[7]);
  or or_5 (or_5_out, or_1_out, or_2_out);
  or or_6 (or_6_out, or_5_out, or_7_out);
  or or_7 (or_7_out, or_3_out, or_4_out);
  nand nand_1 (nand_1_out, not_1_out, not_2_out, not_3_out, not_4_out, not_5_out, not_6_out, not_7_out, not_8_out);
  // NOT_Gate not_9 has open pins: in=nand_1_out, out=open
  not not_10 (A_ZERO, or_6_out);
  // _74181 #(.ShowInternalStructure("true")) 74181_2: pin names not known; wires that end beside it: B[4], A[4], sel1, ALU_S2, ALU_S1, ALU_S0, ALU_CARRY_IN1, sel2, F[4], F[5], F[6], A[5], B[5], A[6], B[6], A[7], B[7], CARRY_OUT, EQ, F[7]
  Decoder #(.enable("false"), .select(3)) decoder_1 (
    .out0(fSUB), .out1(fSUB_CARRY_EN), .out2(fSUM), .out3(fSUM_CARRY_EN), .out4(fNOT), .out5(fXOR),
    .out6(ffOR), .out7(fAND), .sel({sel2, sel1, sel0}));
  not not_11 (ALU_CARRY_IN0, or_8_out);
  or or_8 (or_8_out, fSUB, and_1_out);
  or or_9 (or_9_out, fSUM_CARRY_EN, fSUM);
  not not_12 (not_12_out, fSUM_CARRY_EN);
  not not_13 (not_13_out, fSUM);
  and and_1 (and_1_out, ALU_CARRY_IN, sel0);
  or or_10 (or_10_out, fNOT, or_9_out);
  not not_14 (not_14_out, fNOT);
  and and_2 (and_2_out, not_12_out, not_13_out);
  and and_3 (ALU_S1, not_14_out, and_2_out);
  not not_15 (not_15_out, fAND);
  or or_11 (or_11_out, or_10_out, fAND);
  not not_16 (ALU_S2, or_11_out);
  not not_17 (ALU_S1, or_10_out);
  or or_12 (ALU_S0, fAND, or_9_out);
  not not_18 (not_18_out, fAND);
  and and_4 (and_4_out, not_15_out, and_2_out);
  and and_5 (ALU_S2, ALU_S1, not_18_out);
  not not_19 (ALU_S0, and_4_out);

  // Other names for the same wires on the sheet: ALU_S3 = sel1; ALU_LOGIC = sel2; ALU_A[7:0] = A; ALU_A0 = A[0];
  //   ALU_A1 = A[1]; ALU_A2 = A[2]; ALU_A3 = A[3]; ALU_A4 = A[4]; ALU_A5 = A[5]; ALU_A6 = A[6]; ALU_A7 = A[7];
  //   ALU_B[7:0] = B; ALU_B0 = B[0]; ALU_B1 = B[1]; ALU_B2 = B[2]; ALU_B3 = B[3]; ALU_B4 = B[4]; ALU_B5 = B[5];
  //   ALU_B6 = B[6]; ALU_B7 = B[7]; ALU_CARRY_IN0_INPUT = ALU_CARRY_IN; ALU_CARRY_OUT0 = ALU_CARRY_IN1;
  //   ALU_CARRY_OUT1 = CARRY_OUT; ALU_EQ0 = EQ; ALU_EQ1 = EQ; ALU_F[7:0] = F; ALU_F0 = F[0]; ALU_F1 = F[1];
  //   ALU_F2 = F[2]; ALU_F3 = F[3]; ALU_F4 = F[4]; ALU_F5 = F[5]; ALU_F6 = F[6]; ALU_F7 = F[7]

  // Notes on the sheet:
  //   eq comp only works if carry in is high and subtract mode
  //   9 inverters, 1 nand, 3 ic's
  //   eq is open collector, can wire AND (?)
  //   7 or, 1 inv, 3 chips (unless inv is around)
  //   normal sub has carry
  //   1 or chip, 1 inv (could be used for other things as well), 1 dec -> 3 chips
  //   carry does not affect in logic modes, so can use sel0 as carry filter
  //   could have sel0 be direct and input carry into ucode rom
endmodule

module generic_8bit_register (
  input  CLOCK,
  input  nWE,
  input  [7:0] D,
  output [7:0] Q
);

  _74377 #(.ShowInternalStructure("true")) u_74377_1 (
    .pin1(nWE), .pin2(Q[0]), .pin3(D[0]), .pin4(D[1]), .pin5(Q[1]), .pin6(Q[2]), .pin7(D[2]), .pin8(D[3]),
    .pin9(Q[3]), .pin19(Q[7]), .pin18(D[7]), .pin17(D[6]), .pin16(Q[6]), .pin15(Q[5]), .pin14(D[5]),
    .pin13(D[4]), .pin12(Q[4]), .pin11(CLOCK));
  Hex_Digit_Display L1 (.value(Q[7:4]));  // open: dp
  Hex_Digit_Display L0 (.value(Q[3:0]));  // open: dp

  // Notes on the sheet:
  //   nWE: initial=0x1
  //   might replace with 74HC377
  //   or 74HC574 for OE - 3 state input
endmodule

module ALU_assembly (
  input  CLOCK,
  input  [7:0] BIN,
  input  A_WE,
  input  B_WE,
  input  nA_BOUT_EN,
  input  nB_BOUT_EN,
  input  nF_BOUT_EN,
  input  S0,
  input  S1,
  input  S2,
  input  S3,
  input  ALU_CARRY_IN,
  output [7:0] BOUT,
  output CARRY_OUT,
  output EQUAL,
  output A_ZERO
);

  wire [3:0] A_REG_q, A_REG_q_2, alu_1_f, alu_1_f_2;
  wire [7:0] B_REG_q;

  Hex_Digit_Display L_A1 (.value(A_REG_q_2));  // open: dp
  Hex_Digit_Display L_A0 (.value(A_REG_q));  // open: dp
  gp_register A_REG (
    .nWE(A_WE), .CLOCK(CLOCK), .BIN(BIN), .nBOUT_EN(nA_BOUT_EN), .BOUT(BOUT), .Q({A_REG_q_2, A_REG_q}));
  gp_register B_REG (.nWE(B_WE), .CLOCK(CLOCK), .BIN(BIN), .nBOUT_EN(nB_BOUT_EN), .BOUT(BOUT), .Q(B_REG_q));
  Hex_Digit_Display L_B1 (.value(A_REG_q_2));  // open: dp
  Hex_Digit_Display L_B0 (.value(A_REG_q));  // open: dp
  Hex_Digit_Display L_F1 (.value(alu_1_f_2));  // open: dp
  // Probe on {alu_1_f_2, alu_1_f}
  alu alu_1 (
    .A({A_REG_q_2, A_REG_q}), .B(B_REG_q), .sel0(S0), .sel1(S1), .sel2(S2), .sel3(S3),
    .ALU_CARRY_IN(ALU_CARRY_IN), .F({alu_1_f_2, alu_1_f}), .CARRY_OUT(CARRY_OUT), .EQ(EQUAL), .A_ZERO(A_ZERO));
  Hex_Digit_Display L_F0 (.value(alu_1_f));  // open: dp
  ttl_buffer ttl_buffer_1 (.N_ENABLE(nF_BOUT_EN), .inn({alu_1_f_2, alu_1_f}), .outt(BOUT));

  // Notes on the sheet:
  //   nA_BOUT_EN: initial=0x1
  //   nB_BOUT_EN: initial=0x1
  //   A
  //   B
  //   F
  //   equal cmp: nCARRY_IN = HI (inactive)
endmodule

module ttl_buffer (
  input  N_ENABLE,
  input  [7:0] inn,
  output [7:0] outt
);

  wire n74245_1_pin1, not_1_out;
  wire [7:0] n74245_1_pin2, n74245_1_pin18;

  _74245 #(.ShowInternalStructure("true")) u_74245_1 (
    .pin1(n74245_1_pin1), .pin2(n74245_1_pin2[0]), .pin3(n74245_1_pin2[1]), .pin4(n74245_1_pin2[2]),
    .pin5(n74245_1_pin2[3]), .pin6(n74245_1_pin2[4]), .pin7(n74245_1_pin2[5]), .pin8(n74245_1_pin2[6]),
    .pin9(n74245_1_pin2[7]), .pin19(N_ENABLE), .pin18(n74245_1_pin18[0]), .pin17(n74245_1_pin18[1]),
    .pin16(n74245_1_pin18[2]), .pin15(n74245_1_pin18[3]), .pin14(n74245_1_pin18[4]),
    .pin13(n74245_1_pin18[5]), .pin12(n74245_1_pin18[6]), .pin11(n74245_1_pin18[7]));
  not not_1 (not_1_out, N_ENABLE);
  assign outt = not_1_out ? inn : 8'bz;  // Controlled_Buffer controlled_buffer_1
  // also tied to VCC on the sheet: n74245_1_pin1
endmodule

module gp_register (
  input  CLOCK,
  input  [7:0] BIN,
  input  nWE,
  input  nBOUT_EN,
  output [7:0] BOUT,
  output [7:0] Q
);

  generic_8bit_register generic_8bit_register_1 (.nWE(nWE), .D(BIN), .CLOCK(CLOCK), .Q(Q));
  ttl_buffer ttl_buffer_1 (.N_ENABLE(nBOUT_EN), .inn(Q), .outt(BOUT));
endmodule

module ram_assembly (
  input  CLOCK,
  input  [7:0] BIN,
  input  [15:0] AIN,
  input  MEM_READ,
  input  MEM_WRITE,
  input  nPC_AOUT,
  input  PC_CNT,
  input  nPC_LOAD_LOW,
  input  nPC_LOAD_HIGH,
  input  nMAR_AOUT,
  input  MAR_CNT,
  input  nMAR_LOAD_LOW,
  input  nMAR_LOAD_HIGH,
  input  nSP_AOUT,
  input  nSP_CNTUP,
  input  nSP_CNTDOWN,
  input  nSP_LOAD_LOW,
  input  nSP_LOAD_HIGH,
  input  nLOW_ATOB_EN,
  input  nHIGH_ATOB_EN,
  input  nRESET,
  output [7:0] BOUT,
  output [15:0] AOUT
);

  wire and_1_out, and_2_out, MEMORY_INTERACT, not_1_out, not_2_out, not_3_out, not_4_out, not_5_out,
       not_6_out;
  wire [7:0] ram_1_data, rom_1_data;

  not not_1 (not_1_out, AIN[15]);
  or or_1 (MEMORY_INTERACT, MEM_READ, MEM_WRITE);
  and and_1 (and_1_out, MEM_READ, not_1_out);
  and and_2 (and_2_out, MEMORY_INTERACT, AIN[15]);
  not not_2 (not_2_out, and_1_out);
  not not_3 (not_3_out, and_2_out);
  ROM #(.addrWidth(15)) rom_1 (.addr(AIN[14:0]), .data(rom_1_data));
  not not_4 (not_4_out, MEM_WRITE);
  addr_counter PC (
    .nCLEAR(nRESET), .CNT_EN(PC_CNT), .nLOAD_EN_LOW(nPC_LOAD_LOW), .nLOAD_EN_HIGH(nPC_LOAD_HIGH),
    .nBOUT_EN(nPC_AOUT), .CLOCK(CLOCK), .AIN({BIN, BIN}), .AOUT(AOUT));  // open: Q
  addr_counter MAR (
    .nCLEAR(nRESET), .CNT_EN(MAR_CNT), .nLOAD_EN_LOW(nMAR_LOAD_LOW), .nLOAD_EN_HIGH(nMAR_LOAD_HIGH),
    .nBOUT_EN(nMAR_AOUT), .CLOCK(CLOCK), .AIN({BIN, BIN}), .AOUT(AOUT));  // open: Q
  addr_counter SP (
    .nCLEAR(nRESET), .CNT_EN(nSP_CNTUP), .nLOAD_EN_LOW(nSP_LOAD_LOW), .nLOAD_EN_HIGH(nSP_LOAD_HIGH),
    .nBOUT_EN(nSP_AOUT), .CLOCK(CLOCK), .AIN({BIN, BIN}), .AOUT(AOUT));  // open: Q
  RAM #(.addrWidth(15), .databus("bidir")) ram_1 (
    .addr(AIN[14:0]), .we(not_5_out), .oe(not_6_out), .clk(CLOCK), .data(ram_1_data));
  not not_5 (not_5_out, not_4_out);
  not not_6 (not_6_out, MEM_WRITE);
  // Probe on rom_1_data
  ttl_buffer ttl_buffer_1 (.N_ENABLE(not_2_out), .inn(rom_1_data), .outt(BOUT));
  // Probe on BOUT
  double_buffer double_buffer_1 (
    .N_ENABLE(not_3_out), .A_TO_B(not_4_out), .A_IN(ram_1_data), .B_IN(BIN), .B_OUT(BOUT), .A_OUT(ram_1_data));
  ttl_buffer ttl_buffer_2 (.N_ENABLE(nLOW_ATOB_EN), .inn(AIN[7:0]), .outt(BOUT));
  ttl_buffer ttl_buffer_3 (.N_ENABLE(nHIGH_ATOB_EN), .inn(AIN[15:8]), .outt(BOUT));

  // Other names for the same wires on the sheet: MEMORY_READ = MEM_READ; MEMORY_WRITE = MEM_WRITE

  // Notes on the sheet:
  //   nSP_LOAD_LOW: initial=0x1
  //   nSP_LOAD_HIGH: initial=0x1
  //   nPC_AOUT: initial=0x1
  //   nPC_LOAD_LOW: initial=0x1
  //   nPC_LOAD_HIGH: initial=0x1
  //   nMAR_AOUT: initial=0x1
  //   nMAR_LOAD_LOW: initial=0x1
  //   nMAR_LOAD_HIGH: initial=0x1
  //   nSP_AOUT: initial=0x1
  //   nLOW_ATOB_EN: initial=0x1
  //   nHIGH_ATOB_EN: initial=0x1
  //   nRESET: initial=0x1
  //   need to implement
  //   only do anything if reading (rom)
  //   if either reading or writing
  //   implictly defined by write/interact?
  //   first 32k bytes
  //   second 32k bytes
  //   program counter
  //   memory address register
  //   contents of rom_1 (hex, n*v repeats v):
  //   8 67
  //   the actual chip has 3 state inputs with nCS (Chip select), so no buffers needed
  //   the actual chip has 3 state inputs with nCS (Chip select), so no buffers needed
  //   equivalent to CS in chip
  //   equivalent to CS in chip
  //   buffers from address to data bus
endmodule

module gp_counter (
  input  CLOCK,
  input  [7:0] BIN,
  input  nBIN_EN,
  input  nBOUT_EN,
  input  nCLEAR,
  input  CNT_EN,
  input  nLOAD_EN,
  output [7:0] BOUT,
  output [7:0] Q
);

  wire n74161_1_pin10, n74161_1_pin15, n74161_2_pin15;

  ttl_buffer ttl_buffer_1 (.N_ENABLE(nBIN_EN), .inn(BIN), .outt(BIN));
  ttl_buffer ttl_buffer_2 (.N_ENABLE(nBOUT_EN), .inn(Q), .outt(BOUT));
  _74161 #(.ShowInternalStructure("true")) u_74161_1 (
    .pin1(nCLEAR), .pin2(CLOCK), .pin3(BIN[0]), .pin4(BIN[1]), .pin5(BIN[2]), .pin6(BIN[3]), .pin7(CNT_EN),
    .pin15(n74161_1_pin15), .pin14(Q[0]), .pin13(Q[1]), .pin12(Q[2]), .pin11(Q[3]), .pin10(n74161_1_pin10),
    .pin9(nLOAD_EN));
  Hex_Digit_Display L1 (.value(Q[7:4]));  // open: dp
  Hex_Digit_Display L0 (.value(Q[3:0]));  // open: dp
  _74161 #(.ShowInternalStructure("true")) u_74161_2 (
    .pin1(nCLEAR), .pin2(CLOCK), .pin3(BIN[4]), .pin4(BIN[5]), .pin5(BIN[6]), .pin6(BIN[7]), .pin7(CNT_EN),
    .pin15(n74161_2_pin15), .pin14(Q[4]), .pin13(Q[5]), .pin12(Q[6]), .pin11(Q[7]), .pin10(n74161_1_pin15),
    .pin9(nLOAD_EN));
  // NoConnect on n74161_2_pin15
  // also tied to VCC on the sheet: n74161_1_pin10

  // Other names for the same wires on the sheet: D[7:0] = BIN; D0[3:0] = BIN[3:0]; D1[3:0] = BIN[7:4];
  //   Q0[3:0] = Q[3:0]; Q1[3:0] = Q[7:4]
endmodule

module addr_counter (
  input  CLOCK,
  input  [15:0] AIN,
  input  nBOUT_EN,
  input  nCLEAR,
  input  CNT_EN,
  input  nLOAD_EN_LOW,
  input  nLOAD_EN_HIGH,
  output [15:0] AOUT,
  output [15:0] Q
);

  wire n74161_1_pin10, n74161_1_pin15, n74161_2_pin15, n74161_3_pin15, n74161_4_pin15;

  _74161 #(.ShowInternalStructure("true")) u_74161_1 (
    .pin1(nCLEAR), .pin2(CLOCK), .pin3(AIN[0]), .pin4(AIN[1]), .pin5(AIN[2]), .pin6(AIN[3]), .pin7(CNT_EN),
    .pin15(n74161_1_pin15), .pin14(Q[0]), .pin13(Q[1]), .pin12(Q[2]), .pin11(Q[3]), .pin10(n74161_1_pin10),
    .pin9(nLOAD_EN_LOW));
  buffer_16 buffer_16_1 (.N_ENABLE(nBOUT_EN), .inn(Q), .outt(AOUT));
  Hex_Digit_Display L2 (.value(Q[11:8]));  // open: dp
  Hex_Digit_Display L3 (.value(Q[15:12]));  // open: dp
  _74161 #(.ShowInternalStructure("true")) u_74161_2 (
    .pin1(nCLEAR), .pin2(CLOCK), .pin3(AIN[4]), .pin4(AIN[5]), .pin5(AIN[6]), .pin6(AIN[7]), .pin7(CNT_EN),
    .pin15(n74161_2_pin15), .pin14(Q[4]), .pin13(Q[5]), .pin12(Q[6]), .pin11(Q[7]), .pin10(n74161_1_pin15),
    .pin9(nLOAD_EN_LOW));
  Hex_Digit_Display L1 (.value(Q[7:4]));  // open: dp
  Hex_Digit_Display L0 (.value(Q[3:0]));  // open: dp
  _74161 #(.ShowInternalStructure("true")) u_74161_3 (
    .pin1(nCLEAR), .pin2(CLOCK), .pin3(AIN[8]), .pin4(AIN[9]), .pin5(AIN[10]), .pin6(AIN[11]), .pin7(CNT_EN),
    .pin15(n74161_3_pin15), .pin14(Q[8]), .pin13(Q[9]), .pin12(Q[10]), .pin11(Q[11]), .pin10(n74161_2_pin15),
    .pin9(nLOAD_EN_HIGH));
  _74161 #(.ShowInternalStructure("true")) u_74161_4 (
    .pin1(nCLEAR), .pin2(CLOCK), .pin3(AIN[12]), .pin4(AIN[13]), .pin5(AIN[14]), .pin6(AIN[15]),
    .pin7(CNT_EN), .pin15(n74161_4_pin15), .pin14(Q[12]), .pin13(Q[13]), .pin12(Q[14]), .pin11(Q[15]),
    .pin10(n74161_3_pin15), .pin9(nLOAD_EN_HIGH));
  // NoConnect on n74161_4_pin15
  // also tied to VCC on the sheet: n74161_1_pin10

  // Other names for the same wires on the sheet: D[15:0] = AIN; D0[3:0] = AIN[3:0]; D1[3:0] = AIN[7:4];
  //   D2[3:0] = AIN[11:8]; D3[3:0] = AIN[15:12]; Q0[3:0] = Q[3:0]; Q1[3:0] = Q[7:4]; Q2[3:0] = Q[11:8];
  //   Q3[3:0] = Q[15:12]
endmodule

module buffer_16 (
  input  N_ENABLE,
  input  [15:0] inn,
  output [15:0] outt
);

  wire n74245_1_pin1, n74245_2_pin1;

  _74245 #(.ShowInternalStructure("true")) u_74245_1 (
    .pin1(n74245_1_pin1), .pin2(inn[0]), .pin3(inn[1]), .pin4(inn[2]), .pin5(inn[3]), .pin6(inn[4]),
    .pin7(inn[5]), .pin8(inn[6]), .pin9(inn[7]), .pin19(N_ENABLE), .pin18(outt[0]), .pin17(outt[1]),
    .pin16(outt[2]), .pin15(outt[3]), .pin14(outt[4]), .pin13(outt[5]), .pin12(outt[6]), .pin11(outt[7]));
  _74245 #(.ShowInternalStructure("true")) u_74245_2 (
    .pin1(n74245_2_pin1), .pin2(inn[8]), .pin3(inn[9]), .pin4(inn[10]), .pin5(inn[11]), .pin6(inn[12]),
    .pin7(inn[13]), .pin8(inn[14]), .pin9(inn[15]), .pin19(N_ENABLE), .pin18(outt[8]), .pin17(outt[9]),
    .pin16(outt[10]), .pin15(outt[11]), .pin14(outt[12]), .pin13(outt[13]), .pin12(outt[14]), .pin11(outt[15]));
  // also tied to VCC on the sheet: {n74245_1_pin1, n74245_2_pin1}

  // Notes on the sheet:
  //   N_ENABLE: initial=0x1
endmodule

module double_buffer (
  input  N_ENABLE,
  input  A_TO_B,
  input  [7:0] A_IN,
  input  [7:0] B_IN,
  output [7:0] B_OUT,
  output [7:0] A_OUT
);

  wire n74245_1_pin1, n74245_2_pin1, not_1_out, or_1_out, or_2_out;

  not not_1 (not_1_out, A_TO_B);
  or or_1 (or_1_out, N_ENABLE, not_1_out);
  or or_2 (or_2_out, N_ENABLE, A_TO_B);
  _74245 #(.ShowInternalStructure("true")) u_74245_1 (
    .pin1(n74245_1_pin1), .pin2(A_IN[0]), .pin3(A_IN[1]), .pin4(A_IN[2]), .pin5(A_IN[3]), .pin6(A_IN[4]),
    .pin7(A_IN[5]), .pin8(A_IN[6]), .pin9(A_IN[7]), .pin19(or_1_out), .pin18(B_OUT[0]), .pin17(B_OUT[1]),
    .pin16(B_OUT[2]), .pin15(B_OUT[3]), .pin14(B_OUT[4]), .pin13(B_OUT[5]), .pin12(B_OUT[6]), .pin11(B_OUT[7]));
  _74245 #(.ShowInternalStructure("true")) u_74245_2 (
    .pin1(n74245_2_pin1), .pin2(B_IN[0]), .pin3(B_IN[1]), .pin4(B_IN[2]), .pin5(B_IN[3]), .pin6(B_IN[4]),
    .pin7(B_IN[5]), .pin8(B_IN[6]), .pin9(B_IN[7]), .pin19(or_2_out), .pin18(A_OUT[0]), .pin17(A_OUT[1]),
    .pin16(A_OUT[2]), .pin15(A_OUT[3]), .pin14(A_OUT[4]), .pin13(A_OUT[5]), .pin12(A_OUT[6]), .pin11(A_OUT[7]));
  // also tied to VCC on the sheet: {n74245_2_pin1, n74245_1_pin1}

  // Notes on the sheet:
  //   N_ENABLE: initial=0x1
  //   A_TO_B: initial=0x1
endmodule

module counter8 (
  input  CLOCK,
  input  [7:0] D,
  input  nCLEAR,
  input  CNT_EN,
  input  nLOAD_EN,
  output [7:0] Q
);

  wire n74161_1_pin10, n74161_1_pin15, n74161_2_pin15;

  _74161 #(.ShowInternalStructure("true")) u_74161_1 (
    .pin1(nCLEAR), .pin2(CLOCK), .pin3(D[0]), .pin4(D[1]), .pin5(D[2]), .pin6(D[3]), .pin7(CNT_EN),
    .pin15(n74161_1_pin15), .pin14(Q[0]), .pin13(Q[1]), .pin12(Q[2]), .pin11(Q[3]), .pin10(n74161_1_pin10),
    .pin9(nLOAD_EN));
  Hex_Digit_Display L1 (.value(Q[7:4]));  // open: dp
  Hex_Digit_Display L0 (.value(Q[3:0]));  // open: dp
  _74161 #(.ShowInternalStructure("true")) u_74161_2 (
    .pin1(nCLEAR), .pin2(CLOCK), .pin3(D[4]), .pin4(D[5]), .pin5(D[6]), .pin6(D[7]), .pin7(CNT_EN),
    .pin15(n74161_2_pin15), .pin14(Q[4]), .pin13(Q[5]), .pin12(Q[6]), .pin11(Q[7]), .pin10(n74161_1_pin15),
    .pin9(nLOAD_EN));
  // NoConnect on n74161_2_pin15
  // also tied to VCC on the sheet: n74161_1_pin10

  // Other names for the same wires on the sheet: D0[3:0] = D[3:0]; D1[3:0] = D[7:4]; Q0[3:0] = Q[3:0];
  //   Q1[3:0] = Q[7:4]
endmodule

module counter4 (
  input  CLOCK,
  input  [3:0] D,
  input  nCLEAR,
  input  CNT_EN,
  input  nLOAD_EN,
  output [3:0] Q
);

  wire n74161_1_pin10, n74161_1_pin15;

  _74161 #(.ShowInternalStructure("true")) u_74161_1 (
    .pin1(nCLEAR), .pin2(CLOCK), .pin3(D[0]), .pin4(D[1]), .pin5(D[2]), .pin6(D[3]), .pin7(CNT_EN),
    .pin15(n74161_1_pin15), .pin14(Q[0]), .pin13(Q[1]), .pin12(Q[2]), .pin11(Q[3]), .pin10(n74161_1_pin10),
    .pin9(nLOAD_EN));
  // NoConnect on n74161_1_pin15
  Hex_Digit_Display #(.decimalPoint("false")) L_A1 (.value(Q));
  // also tied to VCC on the sheet: n74161_1_pin10
endmodule
module vga_display (
  input  in_1
);

  wire CLK1, CLK2, CLK4, MULT_nHRST, MULT_nVRST, MULT_VGA_H, MULT_VGA_V, multiplexer_4_out,
       multiplexer_7_out, n74161_1_pin3, n74161_1_pin4, n74161_1_pin5, n74161_1_pin6, n74161_1_pin7,
       n74161_1_pin9, n74161_1_pin10, n74161_1_pin15, n74161_2_pin3, n74161_2_pin4, n74161_2_pin5,
       n74161_2_pin6, n74161_2_pin7, n74161_2_pin9, n74161_3_pin3, n74161_3_pin4, n74161_3_pin5,
       n74161_3_pin6, n74161_3_pin7, n74161_3_pin9, n74161_3_pin15, n74161_4_pin3, n74161_4_pin4,
       n74161_4_pin5, n74161_4_pin6, n74161_4_pin7, n74161_4_pin9, n74161_4_pin15, n74161_5_pin3,
       n74161_5_pin4, n74161_5_pin5, n74161_5_pin6, n74161_5_pin7, n74161_5_pin9, n74163_1_pin1,
       n74163_1_pin3, n74163_1_pin4, n74163_1_pin5, n74163_1_pin6, n74163_1_pin7, n74163_1_pin10,
       n74163_1_pin11, n74163_1_pin12, n74163_1_pin15, n74273_1_pin1, n74273_1_pin2, n74273_1_pin3,
       n74273_2_pin1, n74273_2_pin2, n74273_2_pin3, n74273_2_pin4, n74273_2_pin5, n74273_2_pin6,
       n74273_2_pin7, n74273_2_pin8, n74273_2_pin9, nCLK4, nDRAWING, nHRST, not_2_out, not_3_out, not_6_out,
       not_7_out, nVRST, t74hc590_2_nrco, t74hc590_5_nrco, VGA_H, VGA_V;
  wire [1:0] BLUE, MULT_BLUE, MULT_RED, RED, Y;
  wire [2:0] GREEN, MULT_GREEN;
  wire [6:0] RAM_OUT;
  wire [9:0] X;
  wire [14:0] VBUS, VBUS1, VBUS2;

  // NoConnect on n74163_1_pin15
  _74163 #(.ShowInternalStructure("true")) u_74163_1 (
    .pin1(n74163_1_pin1), .pin2(CLK1), .pin3(n74163_1_pin3), .pin4(n74163_1_pin4), .pin5(n74163_1_pin5),
    .pin6(n74163_1_pin6), .pin7(n74163_1_pin7), .pin15(n74163_1_pin15), .pin14(CLK2), .pin13(CLK4),
    .pin12(n74163_1_pin12), .pin11(n74163_1_pin11), .pin10(n74163_1_pin10), .pin9(n74163_1_pin10));
  // Probe on VBUS
  // Probe on VBUS
  Clock clock_1 (.out(CLK1));
  not not_1 (nCLK4, CLK4);
  // NoConnect on n74163_1_pin12
  // NoConnect on n74163_1_pin11
  // NoConnect on n74163_1_pin3
  // NoConnect on n74163_1_pin4
  // NoConnect on n74163_1_pin5
  // NoConnect on n74163_1_pin6
  ROM #(.addrWidth(15)) rom_1 (.addr(VBUS), .data({nDRAWING, RAM_OUT}));
  _74273 u_74273_1 (
    .pin1(n74273_1_pin1), .pin2(n74273_1_pin2), .pin3(n74273_1_pin3), .pin4(MULT_BLUE[1]), .pin5(BLUE[1]),
    .pin6(BLUE[0]), .pin7(MULT_BLUE[0]), .pin8(MULT_GREEN[2]), .pin9(GREEN[2]), .pin19(RED[0]),
    .pin18(MULT_RED[0]), .pin17(MULT_RED[1]), .pin16(RED[1]), .pin15(GREEN[0]), .pin14(MULT_GREEN[0]),
    .pin13(MULT_GREEN[1]), .pin12(GREEN[1]), .pin11(nCLK4));
  _74273 #(.ShowInternalStructure("true")) u_74273_2 (
    .pin1(n74273_2_pin1), .pin2(n74273_2_pin2), .pin3(n74273_2_pin3), .pin4(n74273_2_pin4),
    .pin5(n74273_2_pin5), .pin6(n74273_2_pin6), .pin7(n74273_2_pin7), .pin8(n74273_2_pin8),
    .pin9(n74273_2_pin9), .pin19(nHRST), .pin18(MULT_nHRST), .pin17(MULT_VGA_H), .pin16(VGA_H),
    .pin15(VGA_V), .pin14(MULT_VGA_V), .pin13(MULT_nVRST), .pin12(nVRST), .pin11(nCLK4));
  T74HC590 t74hc590_1 (
    .nOE(in_1), .RCLK(CLK4), .nCLKEN(1'b0), .CCLK(CLK4), .nCCLR(nHRST), .Q_C(VBUS2[2]), .Q_D(VBUS2[3]),
    .Q_E(VBUS2[4]), .Q_F(VBUS2[5]), .Q_G(VBUS2[6]), .Q_H(VBUS2[7]), .Q_B(VBUS2[1]), .Q_A(VBUS2[0]));  // open: nRCO
  _74161 #(.ShowInternalStructure("true")) u_74161_1 (
    .pin1(nHRST), .pin2(CLK4), .pin3(n74161_1_pin3), .pin4(n74161_1_pin4), .pin5(n74161_1_pin5),
    .pin6(n74161_1_pin6), .pin7(n74161_1_pin7), .pin15(n74161_1_pin15), .pin14(VBUS[0]), .pin13(VBUS[1]),
    .pin12(VBUS[2]), .pin11(VBUS[3]), .pin10(n74161_1_pin10), .pin9(n74161_1_pin9));
  not not_2 (not_2_out, nHRST);
  _74161 #(.ShowInternalStructure("true")) u_74161_2 (
    .pin1(nHRST), .pin2(CLK4), .pin3(n74161_2_pin3), .pin4(n74161_2_pin4), .pin5(n74161_2_pin5),
    .pin6(n74161_2_pin6), .pin7(n74161_2_pin7), .pin14(VBUS[4]), .pin13(VBUS[5]), .pin12(VBUS[6]),
    .pin11(VBUS[7]), .pin10(n74161_1_pin15), .pin9(n74161_2_pin9));  // open: pin15
  T74HC590 t74hc590_2 (
    .nOE(in_1), .RCLK(CLK4), .nCLKEN(1'b0), .CCLK(not_2_out), .nCCLR(nVRST), .Q_C(VBUS2[8]), .Q_D(VBUS2[9]),
    .Q_E(VBUS2[10]), .Q_F(VBUS2[11]), .Q_G(VBUS2[12]), .Q_H(VBUS2[13]), .Q_B(Y[1]), .Q_A(Y[0]),
    .nRCO(t74hc590_2_nrco));
  not not_3 (not_3_out, nHRST);
  _74161 #(.ShowInternalStructure("true")) u_74161_3 (
    .pin1(nVRST), .pin2(CLK4), .pin3(n74161_3_pin3), .pin4(n74161_3_pin4), .pin5(n74161_3_pin5),
    .pin6(n74161_3_pin6), .pin7(n74161_3_pin7), .pin15(n74161_3_pin15), .pin12(VBUS[8]), .pin11(VBUS[9]),
    .pin10(not_3_out), .pin9(n74161_3_pin9));  // open: pin14, pin13
  T74HC590 t74hc590_3 (
    .nOE(in_1), .RCLK(CLK4), .nCLKEN(t74hc590_2_nrco), .CCLK(not_2_out), .nCCLR(nVRST), .Q_A(VBUS2[14]));  // open: Q_C, Q_D, Q_E, Q_F, Q_G, Q_H, Q_B, nRCO
  _74161 #(.ShowInternalStructure("true")) u_74161_4 (
    .pin1(nVRST), .pin2(CLK4), .pin3(n74161_4_pin3), .pin4(n74161_4_pin4), .pin5(n74161_4_pin5),
    .pin6(n74161_4_pin6), .pin7(n74161_4_pin7), .pin15(n74161_4_pin15), .pin14(VBUS[10]), .pin13(VBUS[11]),
    .pin12(VBUS[12]), .pin11(VBUS[13]), .pin10(n74161_3_pin15), .pin9(n74161_4_pin9));
  _74161 #(.ShowInternalStructure("true")) u_74161_5 (
    .pin1(nVRST), .pin2(CLK4), .pin3(n74161_5_pin3), .pin4(n74161_5_pin4), .pin5(n74161_5_pin5),
    .pin6(n74161_5_pin6), .pin7(n74161_5_pin7), .pin14(VBUS[14]), .pin10(n74161_4_pin15), .pin9(n74161_5_pin9));  // open: pin15, pin13, pin12, pin11
  // Probe on VBUS[14:8]
  Multiplexer #(.width(2)) multiplexer_1 (.in0(RAM_OUT[6:5]), .in1({2{VGA_H}}), .out(MULT_BLUE), .sel(nDRAWING));
  Multiplexer #(.width(3)) multiplexer_2 (.in0(RAM_OUT[4:2]), .in1(3'b000), .out(MULT_GREEN), .sel(nDRAWING));
  Multiplexer #(.width(2)) multiplexer_3 (.in0(RAM_OUT[1:0]), .in1({2{VGA_V}}), .out(MULT_RED), .sel(nDRAWING));
  Multiplexer multiplexer_4 (.in0(1'b0), .in1(RAM_OUT[3]), .out(multiplexer_4_out), .sel(nDRAWING));
  Multiplexer multiplexer_5 (.in0(1'b0), .in1(RAM_OUT[2]), .out(MULT_VGA_H), .sel(nDRAWING));
  Multiplexer multiplexer_6 (.in0(1'b0), .in1(RAM_OUT[1]), .out(MULT_VGA_V), .sel(nDRAWING));
  Multiplexer multiplexer_7 (.in0(1'b0), .in1(RAM_OUT[0]), .out(multiplexer_7_out), .sel(nDRAWING));
  not not_4 (MULT_nHRST, multiplexer_4_out);
  not not_5 (MULT_nVRST, multiplexer_7_out);
  not not_6 (not_6_out, nHRST);
  T74HC590 t74hc590_4 (
    .nOE(in_1), .RCLK(CLK4), .nCLKEN(1'b0), .CCLK(CLK4), .nCCLR(nHRST), .Q_C(VBUS1[2]), .Q_D(VBUS1[3]),
    .Q_E(VBUS1[4]), .Q_F(VBUS1[5]), .Q_G(VBUS1[6]), .Q_H(VBUS1[7]), .Q_B(VBUS1[1]), .Q_A(VBUS1[0]));  // open: nRCO
  _74157 #(.ShowInternalStructure("true")) u_74157_1 ();  // open: pin1, pin2, pin3, pin4, pin5, pin6, pin7, pin15, pin14, pin13, pin12, pin11, pin10, pin9
  Counter #(.max('h3ff), .width(10)) counter_1 (
    .count(1'b1), .Q(X), .clk(CLK1), .clr(not_7_out));  // open: load, D, carry, up
  not not_7 (not_7_out, nHRST);
  T74HC590 t74hc590_5 (
    .nOE(in_1), .RCLK(CLK4), .nCLKEN(1'b0), .CCLK(not_6_out), .nCCLR(nVRST), .Q_C(VBUS1[8]), .Q_D(VBUS1[9]),
    .Q_E(VBUS1[10]), .Q_F(VBUS1[11]), .Q_G(VBUS1[12]), .Q_H(VBUS1[13]), .nRCO(t74hc590_5_nrco));  // open: Q_B, Q_A
  // RGB_Video #(.height(500), .scale(1), .width(800)) rgb_video_1: pin names not known; wires that end beside it: 1'b0, CLK1, 1'b1, X, {VBUS[14:8], Y}, {RED, 3'b000, GREEN, 3'b000, BLUE, 3'b000}
  // Probe on {VBUS[14:8], Y}
  T74HC590 t74hc590_6 (
    .nOE(in_1), .RCLK(CLK4), .nCLKEN(t74hc590_5_nrco), .CCLK(not_6_out), .nCCLR(nVRST), .Q_A(VBUS1[14]));  // open: Q_C, Q_D, Q_E, Q_F, Q_G, Q_H, Q_B, nRCO
  // Probe on {RED, 3'b000, GREEN, 3'b000, BLUE, 3'b000}
  // also tied to GND on the sheet: {n74161_1_pin3, n74161_1_pin4, n74161_1_pin5, n74161_1_pin6, n74161_2_pin3, n74161_2_pin4, n74161_2_pin5, n74161_2_pin6, n74161_3_pin3, n74161_3_pin4, n74161_3_pin5, n74161_3_pin6, n74161_4_pin3, n74161_4_pin4, n74161_4_pin5, n74161_4_pin6, n74161_5_pin3, n74161_5_pin4, n74161_5_pin5, n74161_5_pin6}
  // also tied to VCC on the sheet: {n74163_1_pin1, n74163_1_pin10, n74163_1_pin7, n74273_1_pin1, n74273_2_pin1, n74161_1_pin10, n74161_1_pin7, n74161_1_pin9, n74161_2_pin7, n74161_2_pin9, n74161_3_pin7, n74161_3_pin9, n74161_4_pin7, n74161_4_pin9, n74161_5_pin7, n74161_5_pin9}

  // Other names for the same wires on the sheet: nOE = in_1; RAM_OUT[7] = nDRAWING; Y[8:2] = VBUS[14:8]

  // Notes on the sheet:
  //   contents of rom_1 (hex, n*v repeats v):
  //   2d 29 2d 2d 29 2d 29 2d 29 2d 2d 2a 2d 2d 29 2e 2d 29 2d 29 2d 29 2d 29 2d 29 29 2d 7*29 d 29 2d 29
  //   29 2d 5*29 28 29 9 5*29 28 5*29 9 29 28 29 29 9 9*29 2d 29 9 29 2c 9 29 2d 8 29 2d 29 29 28 2d 29 29
  //   29 28 29 29 2d 29 2d 29 29 2d 29 29 2d 29 2d 29 2d 29 2d 29 2d 29 2d 29 4d 29 2d 4d 29 2d 29 2d 29
  //   2d 2d 29 2d 29 29 2d 29 2d 2d 29 29 2d 49 29 2d 49 29 2c 29 29 29 2d 29 29 2d 29 29 2d 29 29 2d 49
  //   2d 29 4*80 24*84 12*80 88 55*80 2d 2d 29 2d 29 2d 2d 29 4d 2d 29 2d 29 2d 29 2d 29 2d 29 2d 29 2d 29
  //   2d 29 2d 2d 29 2d 29 2d 29 2d 29 2d 29 29 29 2d 5*29 2c 9 29 29 28 29 29 29 8 29 29 9 29 29 8 4*29 9
  //   29 29 29 8 29 29 2c 29 29 8 29 29 29 2d 5*29 2d 29 29 29 2d 29 29 2d 29 2d 29 2d 29 29 2d 29 2d 29
  //   2d 29 2d 29 2d 29 2d 29 2d 29 2d 29 2d 29 2d 29 2d 29 2d 29 2d 2d 2d 49 2d 49 2d 29 4d 29 2c 29 2d
  //   29 49 2d 29 28 2d 29 28 2d 49 29 2d 4c 29 29 2c 29 2d 29 2d 28 4d 29 2c 29 2d 4*80 24*84 12*80 88
  //   55*80 29 4d 29 2d 4d 29 2d 2d 2a 2d 2d 49 2d 2d 49 2d 2d 2e 2d 2d 29 2d 29 2d 29 29 29 2d 29 2d 29
  //   2d 4*29 2d 29 29 29 2d 29 2d 7*29 9 4*29 28 4*29 28 29 29 29 28 4*29 9 29 29 29 2d 29 9 4*29 2d 4*29
  //   2d 28 9 29 2d 29 29 29 d 29 2d 29 29 29 2d 29 29 2d 29 2d 29 2d 29 2d 2d 49 2d 2d 29 4d 29 2d 29 4d
  //   29 2d 49 2d 29 2d 29 2d 29 2d 2d 29 2d 49 2d 29 2d 29 2d 2d 29 2d 29 2d 29 2d 29 29 2d 29 4d 29 2d
  //   48 2d 29 2d 29 29 2d 29 4*80 24*84 12*80 88 55*80 4*2d 29 2d 2d 29 2d 2d 29 2d 2d 29 2e 2d 29 29 29
  //   4d 2a 2d 2d 29 2d 2d 2d 29 2d 29 29 29 2d 29 2d 29 29 29 2d 9*29 2d 28 29 29 28 29 29 29 9 29 29 9
  //   29 29 9 29 29 29 9 29 29 28 29 29 9 4*29 28 2d 9 29 29 8 2d 4*29 2d 29 29 29 2d 29 29 29 2d 29 2d 29
  //   29 2d 29 2d 29 2d 29 2d 29 2d 29 2d 29 2d 2d 29 2d 2d 29 2d 2d 2d 29 2d 49 2d 2d 28 4d 29 2d 29 2d
  //   29 2d 29 2c 29 29 49 29 2d 29 2d 29 2c 29 2d 29 2d 29 29 2d 29 29 2d 29 2d 49 2d 4*80 24*84 12*80 88
  //   55*80 2d 29 2d 29 2e 29 4d 2d 29 4d 2e 29 2d 2d 29 2d 4d 2d 2d 29 2d 29 2d 29 2d 29 29 2d 29 2d 29
  //   2d 29 29 2d 29 2d 29 29 2d 29 2d 2e 32 2d 5a 55 55 52 55 31 2d 29 9 29 28 29 28 4*29 28 29 d 29 28
  //   29 2d 29 9 29 28 29 29 29 2d 29 29 29 2d 29 2d 29 29 2d 29 2d 29 29 2d 29 29 2d 29 2d 29 29 2d 29 2d
  //   29 2d 29 2d 29 2d 29 4d 29 2d 29 4d 29 2d 29 4d 29 2d 29 49 2d 29 2d 2d 29 4d 29 2d 29 2d 29 2d 28
  //   2d 49 2d 29 2d 2c 29 2d 28 49 2d 29 49 29 2c 29 2d 29 2d 29 4d 28 29 2d 28 29 4*80 24*84 12*80 88
  //   55*80 29 4d 2d 29 4d 2d 29 2e 2d 29 2d 2d 4a 2d 2d 29 2d 29 2d 2d 29 4d 2d 29 2d 29 2d 29 29 2d 29
  //   2d 29 2d 29 29 29 2d 29 2e 32 2f 2f 2b 2a 56 7a 7e 5a 7a 5a 5a 36 31 2d 29 29 29 2d 28 9 2d 6*29 9
  //   29 29 2d 29 29 2c 29 9 6*29 2d 4*29 2d 29 29 2c 29 29 2d 29 29 2d 29 2d 29 2d 29 2d 29 2d 29 2d 2d
  //   29 2d 2d 29 2d 29 2d 29 2d 29 2d 2d 2d 49 2d 49 2d 29 2d 29 4d 29 2d 49 2d 29 2d 29 2d 29 29 2d 29
  //   29 2d 29 2d 29 2d 29 29 4d 29 28 2d 29 2d 29 2d 29 2d 4*80 24*84 12*80 88 55*80 2d 2d 2a 2d 2d 29 2d
  //   29 2d 2d 2d 29 2d 2d 29 2e 2d 29 2e 29 2d 29 2d 2d 29 2d 29 2d 29 2d 29 29 2d 29 2d 29 2d 2a 2e b b
  //   7 a 7 6 4*7a 5a 7a 3a 5a 36 3a 11 2d 6*29 9 8*29 9 4*29 2d 29 2c 29 2d 29 29 29 2d 29 29 29 2d 29 29
  //   2d 29 29 2d 29 29 2d 28 29 2d 29 2d 29 2d 29 2d 29 2d 29 2d 29 2d 49 2d 2d 29 4d 2d 29 2d 2d 29 2d
  //   2d 29 2d 2d 29 2c 29 2d 29 2d 29 4d 29 2d 49 2d 29 2d 29 2c 29 2d 29 2d 29 28 2d 29 29 2d 29 4d 29
  //   2d 29 4*80 24*84 12*80 88 55*80 29 2d 2d 4d 29 2d 2d 2d 4d 29 2d 4d 29 2d 2d 4d 29 2d 4d 2d 2d 2d 2a
  //   2d 49 2d 29 2d 29 2d 29 2d 29 29 29 2d 2e 2a 7 7 26 6 7 6 29 5a 7a 5e 7a 7a 5a 56 39 36 35 36 16 2d
  //   9 5*29 28 29 9 29 2c 29 29 28 2d 29 29 2d 7*29 2d 29 29 2c 29 2d 29 29 2d 29 29 2d 29 29 2d 29 29 2d
  //   29 2d 29 2d 29 4d 29 2d 4d 29 2d 49 2d 29 2d 29 2d 29 2d 29 2d 49 2d 29 4d 29 4d 29 2d 49 2d 29 2d
  //   49 2d 29 2c 29 2d 29 2c 29 4d 29 29 29 4c 29 2d 29 2d 29 4d 28 29 2d 28 29 2d 4*80 24*84 12*80 88
  //   55*80 2d 4d 29 2d 2d 4e 29 2d 2a 2d 2d 2d 2e 49 2d 29 2d 2d 29 29 2d 29 2d 29 2d 29 2d 29 2d 29 2d
  //   29 2d 2d 2d 2f 7 6 6 6 7 b 6 6 4d 7a 7a 7a 5a 5a 59 36 5a 36 1a 15 36 36 31 2d 8 29 2d 29 29 2d 29
  //   29 29 9 5*29 9 29 2d 29 2d 29 2d 29 28 29 2d 29 29 29 2d 29 29 2d 29 29 2c 29 2d 29 2d 29 2d 29 2d
  //   29 2d 29 2d 29 2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
  //   done for visualization
endmodule

module T74HC590 (
  input  nOE,
  input  RCLK,
  input  nCLKEN,
  input  CCLK,
  input  nCCLR,
  output Q_B,
  output Q_C,
  output Q_A,
  output Q_D,
  output Q_E,
  output Q_F,
  output Q_G,
  output Q_H,
  output nRCO
);

  wire counter_1_carry, not_1_out, not_2_out, not_4_out;
  wire [7:0] counter_1_q, register_1_q;

  not not_1 (not_1_out, nCLKEN);
  not not_2 (not_2_out, nCCLR);
  not not_3 (nRCO, counter_1_carry);
  Counter counter_1 (
    .load(1'b0), .count(not_1_out), .Q(counter_1_q), .carry(counter_1_carry), .up(1'b1), .clk(CCLK),
    .clr(not_2_out));  // open: D
  Register register_1 (.D(counter_1_q), .en(1'b1), .clk(RCLK), .Q(register_1_q), .clr(not_2_out));
  not not_4 (not_4_out, nOE);
  assign {Q_H, Q_G, Q_F, Q_E, Q_D, Q_C, Q_B, Q_A} = not_4_out ? register_1_q : 8'bz;  // Controlled_Buffer controlled_buffer_1

  // Notes on the sheet:
  //   output enable
  //   count carry
  //   count enable
  //   clear signal
  //   register clock - output updates on rise
  //   counter clock - counts on rise (count carry into here)
endmodule

module simple_vga_display (
);

  wire CLK1, CLK2, CLK4, n74157_1_pin4, n74157_1_pin7, n74157_1_pin9, n74157_1_pin12, n74157_1_pin15,
       n74157_2_pin3, n74157_2_pin4, n74157_2_pin6, n74157_2_pin7, n74157_2_pin9, n74157_2_pin11,
       n74157_2_pin12, n74157_2_pin13, n74157_2_pin15, n74157_3_pin2, n74157_3_pin4, n74157_3_pin5,
       n74157_3_pin7, n74157_3_pin12, n74157_3_pin14, n74157_3_pin15, n74161_1_pin3, n74161_1_pin4,
       n74161_1_pin5, n74161_1_pin6, n74161_1_pin7, n74161_1_pin9, n74161_1_pin10, n74161_1_pin15,
       n74161_2_pin3, n74161_2_pin4, n74161_2_pin5, n74161_2_pin6, n74161_2_pin7, n74161_2_pin9,
       n74161_3_pin3, n74161_3_pin4, n74161_3_pin5, n74161_3_pin6, n74161_3_pin7, n74161_3_pin9,
       n74161_3_pin15, n74161_4_pin3, n74161_4_pin4, n74161_4_pin5, n74161_4_pin6, n74161_4_pin7,
       n74161_4_pin9, n74161_4_pin15, n74161_5_pin3, n74161_5_pin4, n74161_5_pin5, n74161_5_pin6,
       n74161_5_pin7, n74161_5_pin9, n74163_1_pin1, n74163_1_pin3, n74163_1_pin4, n74163_1_pin5,
       n74163_1_pin6, n74163_1_pin7, n74163_1_pin10, n74163_1_pin11, n74163_1_pin12, n74163_1_pin15,
       n74273_1_pin1, n74273_1_pin3, n74273_2_pin1, n74273_2_pin3, n74273_2_pin4, n74273_2_pin7,
       n74273_2_pin8, nCLK4, nDRAWING, nHRST, not_2_out, not_3_out, nVRST, VGA_H, VGA_V;
  wire [1:0] Y;
  wire [1:1] GREEN;
  wire [6:0] n74273_1_pin19, RAM_OUT;
  wire [9:0] X;
  wire [14:0] VBUS;

  _74161 #(.ShowInternalStructure("true")) u_74161_1 (
    .pin1(nHRST), .pin2(CLK4), .pin3(n74161_1_pin3), .pin4(n74161_1_pin4), .pin5(n74161_1_pin5),
    .pin6(n74161_1_pin6), .pin7(n74161_1_pin7), .pin15(n74161_1_pin15), .pin14(VBUS[0]), .pin13(VBUS[1]),
    .pin12(VBUS[2]), .pin11(VBUS[3]), .pin10(n74161_1_pin10), .pin9(n74161_1_pin9));
  // Probe on VBUS
  // Probe on VBUS
  ROM #(.addrWidth(15)) rom_1 (.addr(VBUS), .data({nDRAWING, RAM_OUT}));
  _74161 #(.ShowInternalStructure("true")) u_74161_2 (
    .pin1(nHRST), .pin2(CLK4), .pin3(n74161_2_pin3), .pin4(n74161_2_pin4), .pin5(n74161_2_pin5),
    .pin6(n74161_2_pin6), .pin7(n74161_2_pin7), .pin14(VBUS[4]), .pin13(VBUS[5]), .pin12(VBUS[6]),
    .pin11(VBUS[7]), .pin10(n74161_1_pin15), .pin9(n74161_2_pin9));  // open: pin15
  _74163 #(.ShowInternalStructure("true")) u_74163_1 (
    .pin1(n74163_1_pin1), .pin2(CLK1), .pin3(n74163_1_pin3), .pin4(n74163_1_pin4), .pin5(n74163_1_pin5),
    .pin6(n74163_1_pin6), .pin7(n74163_1_pin7), .pin15(n74163_1_pin15), .pin14(CLK2), .pin13(CLK4),
    .pin12(n74163_1_pin12), .pin11(n74163_1_pin11), .pin10(n74163_1_pin10), .pin9(n74163_1_pin10));
  Clock clock_1 (.out(CLK1));
  // NoConnect on n74163_1_pin15
  // NoConnect on n74163_1_pin12
  // NoConnect on n74163_1_pin3
  // NoConnect on n74163_1_pin4
  // NoConnect on n74163_1_pin5
  not not_1 (nCLK4, CLK4);
  // NoConnect on n74163_1_pin11
  // NoConnect on n74163_1_pin6
  not not_2 (not_2_out, nHRST);
  _74161 #(.ShowInternalStructure("true")) u_74161_3 (
    .pin1(nVRST), .pin2(CLK4), .pin3(n74161_3_pin3), .pin4(n74161_3_pin4), .pin5(n74161_3_pin5),
    .pin6(n74161_3_pin6), .pin7(n74161_3_pin7), .pin15(n74161_3_pin15), .pin14(Y[0]), .pin13(Y[1]),
    .pin12(VBUS[8]), .pin11(VBUS[9]), .pin10(not_2_out), .pin9(n74161_3_pin9));
  _74157 #(.ShowInternalStructure("true")) u_74157_1 (
    .pin1(nDRAWING), .pin2(RAM_OUT[0]), .pin3(VGA_H), .pin4(n74157_1_pin4), .pin5(RAM_OUT[1]), .pin6(VGA_H),
    .pin7(n74157_1_pin7), .pin15(n74157_1_pin15), .pin14(RAM_OUT[5]), .pin13(VGA_V), .pin12(n74157_1_pin12),
    .pin11(RAM_OUT[6]), .pin10(VGA_V), .pin9(n74157_1_pin9));
  _74161 #(.ShowInternalStructure("true")) u_74161_4 (
    .pin1(nVRST), .pin2(CLK4), .pin3(n74161_4_pin3), .pin4(n74161_4_pin4), .pin5(n74161_4_pin5),
    .pin6(n74161_4_pin6), .pin7(n74161_4_pin7), .pin15(n74161_4_pin15), .pin14(VBUS[10]), .pin13(VBUS[11]),
    .pin12(VBUS[12]), .pin11(VBUS[13]), .pin10(n74161_3_pin15), .pin9(n74161_4_pin9));
  _74161 #(.ShowInternalStructure("true")) u_74161_5 (
    .pin1(nVRST), .pin2(CLK4), .pin3(n74161_5_pin3), .pin4(n74161_5_pin4), .pin5(n74161_5_pin5),
    .pin6(n74161_5_pin6), .pin7(n74161_5_pin7), .pin14(VBUS[14]), .pin10(n74161_4_pin15), .pin9(n74161_5_pin9));  // open: pin15, pin13, pin12, pin11
  _74157 #(.ShowInternalStructure("true")) u_74157_2 (
    .pin1(nDRAWING), .pin2(RAM_OUT[2]), .pin3(n74157_2_pin3), .pin4(n74157_2_pin4), .pin5(RAM_OUT[3]),
    .pin6(n74157_2_pin6), .pin7(n74157_2_pin7), .pin15(n74157_2_pin15), .pin14(RAM_OUT[4]),
    .pin13(n74157_2_pin13), .pin12(n74157_2_pin12), .pin11(n74157_2_pin11), .pin10(RAM_OUT[0]),
    .pin9(n74157_2_pin9));
  _74157 #(.ShowInternalStructure("true")) u_74157_3 (
    .pin1(nDRAWING), .pin2(n74157_3_pin2), .pin3(RAM_OUT[1]), .pin4(n74157_3_pin4), .pin5(n74157_3_pin5),
    .pin6(RAM_OUT[2]), .pin7(n74157_3_pin7), .pin15(n74157_3_pin15), .pin14(n74157_3_pin14),
    .pin13(RAM_OUT[3]), .pin12(n74157_3_pin12));  // open: pin11, pin10, pin9
  _74273 u_74273_1 (
    .pin1(n74273_1_pin1), .pin3(n74273_1_pin3), .pin4(n74157_1_pin9), .pin5(n74273_1_pin19[6]),
    .pin6(n74273_1_pin19[5]), .pin7(n74157_1_pin12), .pin8(n74157_2_pin12), .pin9(n74273_1_pin19[4]),
    .pin19(n74273_1_pin19[0]), .pin18(n74157_1_pin4), .pin17(n74157_1_pin7), .pin16(n74273_1_pin19[1]),
    .pin15(n74273_1_pin19[2]), .pin14(n74157_2_pin4), .pin13(n74157_2_pin7), .pin12(GREEN[1]), .pin11(nCLK4));  // open: pin2
  Counter #(.max('h3ff), .width(10)) counter_1 (
    .count(1'b1), .Q(X), .clk(CLK1), .clr(not_3_out));  // open: load, D, carry, up
  not not_3 (not_3_out, nHRST);
  // Probe on VBUS[14:8]
  _74273 #(.ShowInternalStructure("true")) u_74273_2 (
    .pin1(n74273_2_pin1), .pin3(n74273_2_pin3), .pin4(n74273_2_pin4), .pin7(n74273_2_pin7),
    .pin8(n74273_2_pin8), .pin19(nHRST), .pin18(n74157_3_pin12), .pin17(n74157_3_pin7), .pin16(VGA_H),
    .pin15(VGA_V), .pin14(n74157_3_pin4), .pin13(n74157_2_pin9), .pin12(nVRST), .pin11(nCLK4));  // open: pin2, pin5, pin6, pin9
  // RGB_Video #(.height(500), .scale(1), .width(800)) rgb_video_1: pin names not known; wires that end beside it: 1'b0, CLK1, 1'b1, X, {VBUS[14:8], Y}, {{6{1'b0}}, GREEN[1], {9{1'b0}}}
  // Probe on {VBUS[14:8], Y}
  // Probe on X
  // Probe on {{6{1'b0}}, GREEN[1], {9{1'b0}}}
  // also tied to GND on the sheet: {n74161_1_pin3, n74161_1_pin4, n74161_1_pin5, n74161_1_pin6, n74161_2_pin3, n74161_2_pin4, n74161_2_pin5, n74161_2_pin6, n74161_3_pin3, n74161_3_pin4, n74161_3_pin5, n74161_3_pin6, n74157_1_pin15, n74161_4_pin3, n74161_4_pin4, n74161_4_pin5, n74161_4_pin6, n74161_5_pin3, n74161_5_pin4, n74161_5_pin5, n74161_5_pin6, n74157_2_pin15, n74157_2_pin3, n74157_2_pin13, n74157_2_pin6, n74157_3_pin15, n74157_3_pin2, n74157_3_pin5, n74273_2_pin3, n74273_2_pin4, n74273_2_pin7, n74273_2_pin8}
  // also tied to VCC on the sheet: {n74161_1_pin10, n74161_1_pin7, n74161_1_pin9, n74163_1_pin1, n74161_2_pin7, n74161_2_pin9, n74163_1_pin10, n74163_1_pin7, n74161_3_pin7, n74161_3_pin9, n74161_4_pin7, n74161_4_pin9, n74161_5_pin7, n74161_5_pin9, n74157_2_pin11, n74273_1_pin1, n74157_3_pin14, n74273_1_pin3, n74273_2_pin1}

  // Other names for the same wires on the sheet: RAM_OUT[7] = nDRAWING; Y[8:2] = VBUS[14:8]

  // Notes on the sheet:
  //   contents of rom_1 (hex, n*v repeats v):
  //   2d 29 2d 2d 29 2d 29 2d 29 2d 2d 2a 2d 2d 29 2e 2d 29 2d 29 2d 29 2d 29 2d 29 29 2d 7*29 d 29 2d 29
  //   29 2d 5*29 28 29 9 5*29 28 5*29 9 29 28 29 29 9 9*29 2d 29 9 29 2c 9 29 2d 8 29 2d 29 29 28 2d 29 29
  //   29 28 29 29 2d 29 2d 29 29 2d 29 29 2d 29 2d 29 2d 29 2d 29 2d 29 2d 29 4d 29 2d 4d 29 2d 29 2d 29
  //   2d 2d 29 2d 29 29 2d 29 2d 2d 29 29 2d 49 29 2d 49 29 2c 29 29 29 2d 29 29 2d 29 29 2d 29 29 2d 49
  //   2d 29 4*89 24*8d 12*89 81 55*89 2d 2d 29 2d 29 2d 2d 29 4d 2d 29 2d 29 2d 29 2d 29 2d 29 2d 29 2d 29
  //   2d 29 2d 2d 29 2d 29 2d 29 2d 29 2d 29 29 29 2d 5*29 2c 9 29 29 28 29 29 29 8 29 29 9 29 29 8 4*29 9
  //   29 29 29 8 29 29 2c 29 29 8 29 29 29 2d 5*29 2d 29 29 29 2d 29 29 2d 29 2d 29 2d 29 29 2d 29 2d 29
  //   2d 29 2d 29 2d 29 2d 29 2d 29 2d 29 2d 29 2d 29 2d 29 2d 29 2d 2d 2d 49 2d 49 2d 29 4d 29 2c 29 2d
  //   29 49 2d 29 28 2d 29 28 2d 49 29 2d 4c 29 29 2c 29 2d 29 2d 28 4d 29 2c 29 2d 4*89 24*8d 12*89 81
  //   55*89 29 4d 29 2d 4d 29 2d 2d 2a 2d 2d 49 2d 2d 49 2d 2d 2e 2d 2d 29 2d 29 2d 29 29 29 2d 29 2d 29
  //   2d 4*29 2d 29 29 29 2d 29 2d 7*29 9 4*29 28 4*29 28 29 29 29 28 4*29 9 29 29 29 2d 29 9 4*29 2d 4*29
  //   2d 28 9 29 2d 29 29 29 d 29 2d 29 29 29 2d 29 29 2d 29 2d 29 2d 29 2d 2d 49 2d 2d 29 4d 29 2d 29 4d
  //   29 2d 49 2d 29 2d 29 2d 29 2d 2d 29 2d 49 2d 29 2d 29 2d 2d 29 2d 29 2d 29 2d 29 29 2d 29 4d 29 2d
  //   48 2d 29 2d 29 29 2d 29 4*89 24*8d 12*89 81 55*89 4*2d 29 2d 2d 29 2d 2d 29 2d 2d 29 2e 2d 29 29 29
  //   4d 2a 2d 2d 29 2d 2d 2d 29 2d 29 29 29 2d 29 2d 29 29 29 2d 9*29 2d 28 29 29 28 29 29 29 9 29 29 9
  //   29 29 9 29 29 29 9 29 29 28 29 29 9 4*29 28 2d 9 29 29 8 2d 4*29 2d 29 29 29 2d 29 29 29 2d 29 2d 29
  //   29 2d 29 2d 29 2d 29 2d 29 2d 29 2d 29 2d 2d 29 2d 2d 29 2d 2d 2d 29 2d 49 2d 2d 28 4d 29 2d 29 2d
  //   29 2d 29 2c 29 29 49 29 2d 29 2d 29 2c 29 2d 29 2d 29 29 2d 29 29 2d 29 2d 49 2d 4*89 24*8d 12*89 81
  //   55*89 2d 29 2d 29 2e 29 4d 2d 29 4d 2e 29 2d 2d 29 2d 4d 2d 2d 29 2d 29 2d 29 2d 29 29 2d 29 2d 29
  //   2d 29 29 2d 29 2d 29 29 2d 29 2d 2e 32 2d 5a 55 55 52 55 31 2d 29 9 29 28 29 28 4*29 28 29 d 29 28
  //   29 2d 29 9 29 28 29 29 29 2d 29 29 29 2d 29 2d 29 29 2d 29 2d 29 29 2d 29 29 2d 29 2d 29 29 2d 29 2d
  //   29 2d 29 2d 29 2d 29 4d 29 2d 29 4d 29 2d 29 4d 29 2d 29 49 2d 29 2d 2d 29 4d 29 2d 29 2d 29 2d 28
  //   2d 49 2d 29 2d 2c 29 2d 28 49 2d 29 49 29 2c 29 2d 29 2d 29 4d 28 29 2d 28 29 4*89 24*8d 12*89 81
  //   55*89 29 4d 2d 29 4d 2d 29 2e 2d 29 2d 2d 4a 2d 2d 29 2d 29 2d 2d 29 4d 2d 29 2d 29 2d 29 29 2d 29
  //   2d 29 2d 29 29 29 2d 29 2e 32 2f 2f 2b 2a 56 7a 7e 5a 7a 5a 5a 36 31 2d 29 29 29 2d 28 9 2d 6*29 9
  //   29 29 2d 29 29 2c 29 9 6*29 2d 4*29 2d 29 29 2c 29 29 2d 29 29 2d 29 2d 29 2d 29 2d 29 2d 29 2d 2d
  //   29 2d 2d 29 2d 29 2d 29 2d 29 2d 2d 2d 49 2d 49 2d 29 2d 29 4d 29 2d 49 2d 29 2d 29 2d 29 29 2d 29
  //   29 2d 29 2d 29 2d 29 29 4d 29 28 2d 29 2d 29 2d 29 2d 4*89 24*8d 12*89 81 55*89 2d 2d 2a 2d 2d 29 2d
  //   29 2d 2d 2d 29 2d 2d 29 2e 2d 29 2e 29 2d 29 2d 2d 29 2d 29 2d 29 2d 29 29 2d 29 2d 29 2d 2a 2e b b
  //   7 a 7 6 4*7a 5a 7a 3a 5a 36 3a 11 2d 6*29 9 8*29 9 4*29 2d 29 2c 29 2d 29 29 29 2d 29 29 29 2d 29 29
  //   2d 29 29 2d 29 29 2d 28 29 2d 29 2d 29 2d 29 2d 29 2d 29 2d 29 2d 49 2d 2d 29 4d 2d 29 2d 2d 29 2d
  //   2d 29 2d 2d 29 2c 29 2d 29 2d 29 4d 29 2d 49 2d 29 2d 29 2c 29 2d 29 2d 29 28 2d 29 29 2d 29 4d 29
  //   2d 29 4*89 24*8d 12*89 81 55*89 29 2d 2d 4d 29 2d 2d 2d 4d 29 2d 4d 29 2d 2d 4d 29 2d 4d 2d 2d 2d 2a
  //   2d 49 2d 29 2d 29 2d 29 2d 29 29 29 2d 2e 2a 7 7 26 6 7 6 29 5a 7a 5e 7a 7a 5a 56 39 36 35 36 16 2d
  //   9 5*29 28 29 9 29 2c 29 29 28 2d 29 29 2d 7*29 2d 29 29 2c 29 2d 29 29 2d 29 29 2d 29 29 2d 29 29 2d
  //   29 2d 29 2d 29 4d 29 2d 4d 29 2d 49 2d 29 2d 29 2d 29 2d 29 2d 49 2d 29 4d 29 4d 29 2d 49 2d 29 2d
  //   49 2d 29 2c 29 2d 29 2c 29 4d 29 29 29 4c 29 2d 29 2d 29 4d 28 29 2d 28 29 2d 4*89 24*8d 12*89 81
  //   55*89 2d 4d 29 2d 2d 4e 29 2d 2a 2d 2d 2d 2e 49 2d 29 2d 2d 29 29 2d 29 2d 29 2d 29 2d 29 2d 29 2d
  //   29 2d 2d 2d 2f 7 6 6 6 7 b 6 6 4d 7a 7a 7a 5a 5a 59 36 5a 36 1a 15 36 36 31 2d 8 29 2d 29 29 2d 29
  //   29 29 9 5*29 9 29 2d 29 2d 29 2d 29 28 29 2d 29 29 29 2d 29 29 2d 29 29 2c 29 2d 29 2d 29 2d 29 2d
  //   29 2d 29 2d 29 2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
  //   blue
  //   red
  //   green
  //   nVRST
  //   nHRST
  //   VGA_V
  //   VGA_H
endmodule

module simplest_vga_display (
);

  wire and_1_out, and_2_out, and_3_out, CLK1, CLK2, CLK4, DRAWING_BIT, n74157_1_pin4, n74157_1_pin6,
       n74157_1_pin7, n74157_1_pin9, n74157_1_pin12, n74157_1_pin13, n74157_1_pin15, n74157_2_pin3,
       n74157_2_pin4, n74157_2_pin9, n74157_2_pin10, n74157_2_pin12, n74157_2_pin13, n74157_2_pin15,
       n74157_3_pin2, n74157_3_pin4, n74157_3_pin5, n74157_3_pin7, n74157_3_pin9, n74157_3_pin11,
       n74157_3_pin12, n74157_3_pin14, n74157_3_pin15, n74161_1_pin3, n74161_1_pin4, n74161_1_pin5,
       n74161_1_pin6, n74161_1_pin7, n74161_1_pin9, n74161_1_pin10, n74161_1_pin15, n74161_2_pin3,
       n74161_2_pin4, n74161_2_pin5, n74161_2_pin6, n74161_2_pin7, n74161_2_pin9, n74161_3_pin3,
       n74161_3_pin4, n74161_3_pin5, n74161_3_pin6, n74161_3_pin7, n74161_3_pin9, n74161_3_pin10,
       n74161_3_pin15, n74161_4_pin3, n74161_4_pin4, n74161_4_pin5, n74161_4_pin6, n74161_4_pin7,
       n74161_4_pin9, n74161_4_pin15, n74161_5_pin3, n74161_5_pin4, n74161_5_pin5, n74161_5_pin6,
       n74161_5_pin7, n74161_5_pin9, n74163_1_pin1, n74163_1_pin3, n74163_1_pin4, n74163_1_pin5,
       n74163_1_pin6, n74163_1_pin7, n74163_1_pin10, n74163_1_pin11, n74163_1_pin12, n74163_1_pin15,
       n74273_1_pin1, n74273_2_pin1, n74273_2_pin4, n74273_2_pin7, n74273_2_pin8, n74273_2_pin13,
       n74273_2_pin14, n74273_2_pin16, nand_1_out, nand_2_out, nand_3_out, nand_4_out, nand_5_out,
       nand_6_out, nCLK4, nHRST, not_3_out, not_4_out, not_5_out, nVRST, nVRST_BUFFERED, or_3_out, VGA_H,
       VGA_V;
  wire [1:0] BLUE, RED;
  wire [2:0] GREEN;
  wire [7:0] RAM_OUT;
  wire [9:0] X, Y;
  wire [14:0] VBUS;

  // Probe on VBUS
  // Probe on VBUS
  ROM #(.addrWidth(15)) rom_1 (.addr(VBUS), .data(RAM_OUT));
  // NoConnect on n74163_1_pin15
  _74163 #(.ShowInternalStructure("true")) u_74163_1 (
    .pin1(n74163_1_pin1), .pin2(CLK1), .pin3(n74163_1_pin3), .pin4(n74163_1_pin4), .pin5(n74163_1_pin5),
    .pin6(n74163_1_pin6), .pin7(n74163_1_pin7), .pin15(n74163_1_pin15), .pin14(CLK2), .pin13(CLK4),
    .pin12(n74163_1_pin12), .pin11(n74163_1_pin11), .pin10(n74163_1_pin10), .pin9(n74163_1_pin10));
  // NoConnect on n74163_1_pin3
  Clock clock_1 (.out(CLK1));
  not not_1 (nCLK4, CLK4);
  // NoConnect on n74163_1_pin12
  // NoConnect on n74163_1_pin11
  // NoConnect on n74163_1_pin4
  // NoConnect on n74163_1_pin5
  // NoConnect on n74163_1_pin6
  _74161 #(.ShowInternalStructure("true")) u_74161_1 (
    .pin1(nHRST), .pin2(CLK4), .pin3(n74161_1_pin3), .pin4(n74161_1_pin4), .pin5(n74161_1_pin5),
    .pin6(n74161_1_pin6), .pin7(n74161_1_pin7), .pin15(n74161_1_pin15), .pin14(VBUS[0]), .pin13(VBUS[1]),
    .pin12(VBUS[2]), .pin11(VBUS[3]), .pin10(n74161_1_pin10), .pin9(n74161_1_pin9));
  _74161 #(.ShowInternalStructure("true")) u_74161_2 (
    .pin1(nHRST), .pin2(CLK4), .pin3(n74161_2_pin3), .pin4(n74161_2_pin4), .pin5(n74161_2_pin5),
    .pin6(n74161_2_pin6), .pin7(n74161_2_pin7), .pin14(VBUS[4]), .pin13(VBUS[5]), .pin12(VBUS[6]),
    .pin11(VBUS[7]), .pin10(n74161_1_pin15), .pin9(n74161_2_pin9));  // open: pin15
  _74157 #(.ShowInternalStructure("true")) u_74157_1 (
    .pin1(DRAWING_BIT), .pin2(RAM_OUT[1]), .pin3(VGA_H), .pin4(n74157_1_pin4), .pin5(RAM_OUT[0]),
    .pin6(n74157_1_pin6), .pin7(n74157_1_pin7), .pin15(n74157_1_pin15), .pin14(RAM_OUT[3]),
    .pin13(n74157_1_pin13), .pin12(n74157_1_pin12), .pin11(RAM_OUT[4]), .pin10(VGA_V), .pin9(n74157_1_pin9));
  _74161 #(.ShowInternalStructure("true")) u_74161_3 (
    .pin1(nVRST), .pin2(CLK4), .pin3(n74161_3_pin3), .pin4(n74161_3_pin4), .pin5(n74161_3_pin5),
    .pin6(n74161_3_pin6), .pin7(n74161_3_pin7), .pin15(n74161_3_pin15), .pin14(Y[0]), .pin13(Y[1]),
    .pin12(VBUS[8]), .pin11(VBUS[9]), .pin10(n74161_3_pin10), .pin9(n74161_3_pin9));
  not not_2 (n74161_3_pin10, nHRST);
  _74157 #(.ShowInternalStructure("true")) u_74157_2 (
    .pin1(DRAWING_BIT), .pin2(RAM_OUT[5]), .pin3(n74157_2_pin3), .pin4(n74157_2_pin4),
    .pin15(n74157_2_pin15), .pin14(RAM_OUT[6]), .pin13(n74157_2_pin13), .pin12(n74157_2_pin12),
    .pin11(RAM_OUT[7]), .pin10(n74157_2_pin10), .pin9(n74157_2_pin9));  // open: pin5, pin6, pin7
  _74161 #(.ShowInternalStructure("true")) u_74161_4 (
    .pin1(nVRST), .pin2(CLK4), .pin3(n74161_4_pin3), .pin4(n74161_4_pin4), .pin5(n74161_4_pin5),
    .pin6(n74161_4_pin6), .pin7(n74161_4_pin7), .pin15(n74161_4_pin15), .pin14(VBUS[10]), .pin13(VBUS[11]),
    .pin12(VBUS[12]), .pin11(VBUS[13]), .pin10(n74161_3_pin15), .pin9(n74161_4_pin9));
  and and_1 (and_1_out, Y[0], Y[9]);
  nand nand_1 (nand_1_out, Y[0], Y[9]);
  nand nand_2 (nand_2_out, VBUS[8], VBUS[9]);
  nand nand_3 (nand_3_out, Y[0], Y[9]);
  nand nand_4 (nand_4_out, VBUS[8], VBUS[9]);
  and and_2 (and_2_out, and_1_out, VBUS[8]);
  nand nand_5 (nand_5_out, nand_3_out, nand_3_out);
  nand nand_6 (nand_6_out, nand_4_out, nand_4_out);
  _7404 #(.ShowInternalStructure("true")) u_7404_1 ();  // open: pin1, pin2, pin3, pin4, pin5, pin6, pin13, pin12, pin11, pin10, pin9, pin8
  _7400 #(.ShowInternalStructure("true")) u_7400_1 ();  // open: pin1, pin2, pin3, pin4, pin5, pin6, pin13, pin12, pin11, pin10, pin9, pin8
  _7432 #(.ShowInternalStructure("true")) u_7432_1 ();  // open: pin1, pin2, pin3, pin4, pin5, pin6, pin13, pin12, pin11, pin10, pin9, pin8
  _74157 #(.ShowInternalStructure("true")) u_74157_3 (
    .pin1(RAM_OUT[2]), .pin2(n74157_3_pin2), .pin3(RAM_OUT[0]), .pin4(n74157_3_pin4), .pin5(n74157_3_pin5),
    .pin6(RAM_OUT[5]), .pin7(n74157_3_pin7), .pin15(n74157_3_pin15), .pin14(n74157_3_pin14),
    .pin13(RAM_OUT[6]), .pin12(n74157_3_pin12), .pin11(n74157_3_pin11), .pin10(RAM_OUT[7]),
    .pin9(n74157_3_pin9));
  not not_3 (not_3_out, and_3_out);
  and and_3 (and_3_out, and_2_out, VBUS[9]);
  // OR_Gate or_1 has open pins: in0=nand_1_out, in1=nand_2_out, out=open
  _74161 #(.ShowInternalStructure("true")) u_74161_5 (
    .pin1(nVRST), .pin2(CLK4), .pin3(n74161_5_pin3), .pin4(n74161_5_pin4), .pin5(n74161_5_pin5),
    .pin6(n74161_5_pin6), .pin7(n74161_5_pin7), .pin14(VBUS[14]), .pin13(Y[9]), .pin10(n74161_4_pin15),
    .pin9(n74161_5_pin9));  // open: pin15, pin12, pin11
  nand nand_7 (nVRST_BUFFERED, nand_5_out, nand_6_out);
  _74273 u_74273_1 (
    .pin1(n74273_1_pin1), .pin2(RED[1]), .pin3(n74157_1_pin4), .pin4(n74157_1_pin7), .pin5(RED[0]),
    .pin6(nVRST), .pin7(nVRST_BUFFERED), .pin8(n74157_3_pin4), .pin9(nHRST), .pin19(BLUE[1]),
    .pin18(n74157_1_pin9), .pin17(n74157_1_pin12), .pin16(BLUE[0]), .pin15(GREEN[2]), .pin14(n74157_2_pin9),
    .pin13(n74157_2_pin12), .pin12(GREEN[1]), .pin11(nCLK4));
  _74273 u_74273_2 (
    .pin1(n74273_2_pin1), .pin2(GREEN[0]), .pin3(n74157_2_pin4), .pin4(n74273_2_pin4), .pin7(n74273_2_pin7),
    .pin8(n74273_2_pin8), .pin19(VGA_H), .pin18(n74157_3_pin9), .pin17(n74157_3_pin12),
    .pin16(n74273_2_pin16), .pin14(n74273_2_pin14), .pin13(n74273_2_pin13), .pin11(nCLK4));  // open: pin5, pin6, pin9, pin15, pin12
  Counter #(.max('h3ff), .width(10)) counter_1 (
    .count(1'b1), .Q(X), .clk(CLK1), .clr(not_4_out));  // open: load, D, carry, up
  not not_4 (not_4_out, nHRST);
  // Probe on VBUS[14:8]
  // Probe on VBUS[14:8]
  or or_2 (DRAWING_BIT, RAM_OUT[2], Y[9]);
  // RGB_Video #(.height(530), .scale(1), .width(801)) rgb_video_1: pin names not known; wires that end beside it: 1'b0, CLK1, 1'b1, X, {Y[9], VBUS[14:8], Y[1:0]}, {RED, 3'b000, GREEN, 3'b000, BLUE, 3'b000}
  // Probe on X
  // Probe on {Y[9], VBUS[14:8], Y[1:0]}
  or or_3 (or_3_out, n74273_2_pin16, not_5_out);
  not not_5 (not_5_out, Y[1]);
  nand nand_8 (VGA_V, n74273_2_pin16, Y[1]);
  // Probe on {RED, 3'b000, GREEN, 3'b000, BLUE, 3'b000}
  // also tied to GND on the sheet: {n74161_1_pin3, n74161_1_pin4, n74161_1_pin5, n74161_1_pin6, n74161_2_pin3, n74161_2_pin4, n74161_2_pin5, n74161_2_pin6, n74157_1_pin15, n74157_1_pin13, n74157_1_pin6, n74161_3_pin3, n74161_3_pin4, n74161_3_pin5, n74161_3_pin6, n74157_2_pin15, n74157_2_pin3, n74157_2_pin13, n74161_4_pin3, n74161_4_pin4, n74157_2_pin10, n74161_4_pin5, n74161_4_pin6, n74157_3_pin15, n74157_3_pin14, n74161_5_pin3, n74161_5_pin4, n74161_5_pin5, n74161_5_pin6}
  // also tied to VCC on the sheet: {n74163_1_pin1, n74163_1_pin10, n74163_1_pin7, n74161_1_pin10, n74161_1_pin7, n74161_1_pin9, n74161_2_pin7, n74161_2_pin9, n74161_3_pin7, n74161_3_pin9, n74161_4_pin7, n74157_3_pin2, n74161_4_pin9, n74157_3_pin5, n74157_3_pin11, n74161_5_pin7, n74161_5_pin9, n74273_1_pin1, n74273_2_pin1, n74273_2_pin4, n74273_2_pin14, n74273_2_pin7, n74273_2_pin13, n74273_2_pin8}

  // Other names for the same wires on the sheet: ROM_DRAWING_BIT = RAM_OUT[2]; Y[8:2] = VBUS[14:8]; Y2 = VBUS[8];
  //   Y3 = VBUS[9]

  // Notes on the sheet:
  //   contents of rom_1 (hex, n*v repeats v):
  //   49 49 49 69 49 49 69 49 49 69 49 49 69 49 49 69 49 49 69 87*49 69 49 49 49 69 49 49 69 49 69 49 69
  //   49 69 49 69 49 69 49 69 49 69 49 69 49 49 69 49 69 49 69 49 49 69 49 69 49 49 69 49 49 69 49 69 49
  //   69 49 69 49 69 49 69 49 69 4*85 24*5 11*85 57*84 69 49 69 49 49 69 49 49 69 49 49 69 49 49 69 49 49
  //   69 49 69 49 69 69 49 69 49 49 69 5*49 41 49 49 41 49 49 41 49 49 41 49 40 49 41 49 40 49 49 41 48 41
  //   49 40 49 41 49 41 49 49 41 49 49 40 49 41 49 49 41 49 41 49 49 41 49 49 41 49 41 49 41 49 49 41 49
  //   49 49 41 49 69 49 69 49 69 49 69 49 69 49 69 49 69 69 49 49 69 49 69 49 49 69 49 69 49 69 49 69 49
  //   69 49 69 49 69 49 69 49 69 49 49 69 49 49 69 49 49 69 49 69 49 69 49 69 49 49 69 49 69 49 49 49 69
  //   49 69 51 69 49 71 49 4*85 24*5 11*85 57*84 49 49 49 69 49 49 69 49 49 69 49 69 49 69 49 69 49 69 49
  //   49 69 4*49 69 49 41 49 69 41 49 49 49 48 49 49 48 49 49 48 5*49 48 49 49 49 40 6*49 48 49 48 49 40
  //   5*49 48 49 40 49 49 48 49 49 48 49 41 49 49 48 4*49 69 49 61 49 69 49 49 41 9*49 69 49 49 69 49 49
  //   49 69 49 69 49 69 49 49 69 49 69 49 69 49 69 49 49 69 49 69 49 69 49 69 49 69 48 69 49 49 68 49 51
  //   68 49 69 50 69 49 50 49 69 70 49 71 48 69 49 68 49 69 49 4*85 24*5 11*85 57*84 49 69 49 69 49 69 49
  //   69 49 69 49 69 49 69 49 69 49 69 49 69 49 49 69 49 69 49 49 69 4*49 69 49 49 61 49 49 49 41 49 49 41
  //   48 49 41 49 49 41 4*49 40 49 49 41 49 49 41 4*49 40 49 49 41 5*49 41 49 41 49 48 5*49 68 41 49 48 49
  //   49 48 49 49 69 49 69 49 69 49 61 49 69 49 49 69 49 49 69 49 69 49 49 69 49 69 49 69 49 69 49 69 49
  //   71 49 69 71 49 69 51 69 49 71 48 69 51 49 49 69 51 49 69 49 69 49 49 69 49 69 49 69 4*49 69 49 71 49
  //   69 51 69 4*85 24*5 11*85 57*84 69 49 69 49 49 69 49 69 49 69 49 69 49 69 49 69 49 69 49 49 69 49 69
  //   49 49 49 69 49 49 69 49 48 41 8*49 48 49 49 49 48 49 49 48 49 49 41 49 49 49 48 6*49 40 6*49 41 8*49
  //   41 69 41 49 41 6*49 61 4*49 41 49 49 69 48 49 49 69 49 49 48 69 49 69 49 69 49 69 49 69 49 69 51 69
  //   49 69 49 69 49 69 49 69 49 69 49 69 49 69 49 69 69 49 68 49 69 49 69 49 71 48 49 69 49 68 49 69 69
  //   68 49 69 49 69 49 68 49 69 4*85 24*5 11*85 57*84 49 49 69 49 69 49 69 49 69 49 69 49 69 49 69 49 69
  //   49 69 69 49 69 49 69 49 69 4*49 69 49 49 69 49 49 49 61 48 49 41 49 49 41 49 41 49 41 49 41 49 49 48
  //   49 49 49 41 49 40 49 40 4*49 41 49 41 48 49 49 40 49 41 48 49 41 4*49 69 49 49 49 69 41 69 4*49 61
  //   49 68 49 69 49 49 69 49 41 69 49 69 49 49 49 68 49 69 49 69 49 69 49 69 69 49 71 49 69 69 51 69 48
  //   69 49 69 49 69 49 69 49 49 69 49 49 68 49 49 48 69 49 69 48 71 49 69 51 49 49 71 49 69 50 69 49 71
  //   49 4*85 24*5 11*85 57*84 69 49 69 49 69 49 69 49 69 49 69 49 69 49 69 49 69 49 69 49 69 49 69 49 69
  //   49 49 69 41 5*49 41 48 8*49 48 49 49 48 49 49 48 41 49 41 49 49 48 6*49 41 48 49 48 8*49 69 49 48 49
  //   49 48 49 49 69 41 4*49 69 8*49 69 49 49 69 49 49 49 69 69 49 69 49 49 69 49 69 49 69 49 49 69 49 69
  //   49 69 49 69 51 69 49 71 49 49 71 49 69 50 49 69 49 49 71 69 49 49 69 49 49 49 69 49 68 49 69 49 69
  //   49 69 49 69 49 69 4*85 24*5 11*85 57*84 49 69 49 69 49 69 49 69 49 69 49 69 49 69 69 49 69 49 69 49
  //   69 49 49 69 49 49 69 49 49 69 49 69 49 69 49 49 69 49 49 49 69 41 48 5*49 41 5*49 40 49 49 41 49 49
  //   49 41 48 4*49 41 49 49 41 49 49 49 41 49 49 41 49 61 49 49 41 48 49 49 48 69 49 41 48 49 69 49 69 49
  //   69 49 49 69 49 48 69 49 69 49 49 49 69 49 69 49 69 49 69 51 69 69 51 69 69 49 71 69 49 69 49 69 49
  //   69 69 49 69 49 69 49 69 49 69 49 49 49 71 49 49 71 69 49 49 69 49 69 49 50 69 49 69 51 69 49 4*85
  //   24*5 11*85 57*84 69 49 69 49 69 49 69 49 69 49 69 49 69 49 69 49 69 49 69 49 69 49 69 49 69 49 69 49
  //   69 49 49 41 49 49 49 69 49 49 69 49 48 49 49 41 49 48 41 49 48 49 49 49 48 5*49 48 41 4*49 41 49 49
  //   49 48 49 48 49 61 48 49 49 49 69 49 49 49 69 49 49 69 4*49 69 49 69 49 49 41 49 69 49 69 49 49 69 49
  //   49 69 49 69 69 49 69 49 69 49 69 49 69 49 69 49 69 51 69 49 69 69 51 69 49 69 48 49 69 49 69 49 49
  //   71 48 49 69 48 69 48 69 49 48 49 71 49 51 69 49 69 49 69 50 69 49 68 51 4*85 24*5 11*85 57*84 69 49
  //   69 49 69 49 69 49 69 69 49 69 69 49 69 69 49 69 69 49 69 49 69 49 69 49 69 49 49 69 49 69 49 69 4*49
  //   41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
  //   blue
  //   red
  //   6.29375
  //   green0
  //   green1
  //   green2
  //   blue
  //   VSYNC
  //   nHRST
  //   HSYNC
  //   nVRST
  //   red
  //   green2
  //   nVRST
  //   green1
  //   HSYNC
  //   green0
  //   nHRST
  //   VSYNC
endmodule

module XYZ_regs (
  input  CLOCK,
  input  [7:0] BIN,
  input  X_WE,
  input  nX_BOUT,
  input  Y_WE,
  input  nY_BOUT,
  input  Z_WE,
  input  nZ_BOUT,
  input  nRESET,
  output [7:0] BOUT
);

  wire BOUT_CONNECT, n74299_1_pin11, n74299_1_pin18, n74299_2_pin11, n74299_2_pin18, n74299_3_pin11,
       n74299_3_pin18;

  assign BOUT = BOUT_CONNECT ? ~BIN : 8'bz;  // Controlled_Inverter controlled_inverter_1
  _74299 #(.ShowInternalStructure("true")) u_74299_1 (
    .pin1(X_WE), .pin2(nX_BOUT), .pin3(nX_BOUT), .pin4(BIN[6]), .pin5(BIN[4]), .pin6(BIN[2]), .pin7(BIN[0]),
    .pin9(nRESET), .pin19(X_WE), .pin18(n74299_1_pin18), .pin16(BIN[7]), .pin15(BIN[5]), .pin14(BIN[3]),
    .pin13(BIN[1]), .pin12(CLOCK), .pin11(n74299_1_pin11));  // open: pin8, pin17
  _74299 #(.ShowInternalStructure("true")) u_74299_2 (
    .pin1(Y_WE), .pin2(nY_BOUT), .pin3(nY_BOUT), .pin4(BIN[6]), .pin5(BIN[4]), .pin6(BIN[2]), .pin7(BIN[0]),
    .pin9(nRESET), .pin19(Y_WE), .pin18(n74299_2_pin18), .pin16(BIN[7]), .pin15(BIN[5]), .pin14(BIN[3]),
    .pin13(BIN[1]), .pin12(CLOCK), .pin11(n74299_2_pin11));  // open: pin8, pin17
  nand nand_1 (BOUT_CONNECT, nX_BOUT, nY_BOUT, nZ_BOUT);
  _74299 #(.ShowInternalStructure("true")) u_74299_3 (
    .pin1(Z_WE), .pin2(nZ_BOUT), .pin3(nZ_BOUT), .pin4(BIN[6]), .pin5(BIN[4]), .pin6(BIN[2]), .pin7(BIN[0]),
    .pin9(nRESET), .pin19(Z_WE), .pin18(n74299_3_pin18), .pin16(BIN[7]), .pin15(BIN[5]), .pin14(BIN[3]),
    .pin13(BIN[1]), .pin12(CLOCK), .pin11(n74299_3_pin11));  // open: pin8, pin17
  // also tied to GND on the sheet: {n74299_1_pin18, n74299_1_pin11, n74299_2_pin18, n74299_2_pin11, n74299_3_pin18, n74299_3_pin11}

  // Notes on the sheet:
  //   nX_BOUT: initial=0x1
  //   nY_BOUT: initial=0x1
  //   nZ_BOUT: initial=0x1
  //   reqired as workaround for logisim weirdness
endmodule

module T74HC173 (
  input  M,
  input  N,
  input  nCLR,
  input  D1,
  input  D2,
  input  D3,
  input  D4,
  input  CLK,
  input  nG2,
  input  nG1,
  output Q1,
  output Q2,
  output Q3,
  output Q4
);

  wire and_1_out, and_2_out, not_1_out, not_2_out, not_3_out, not_4_out, not_5_out;
  wire [3:0] register_1_q;

  not not_1 (not_1_out, nG2);
  and and_1 (and_1_out, not_1_out, not_2_out);
  not not_2 (not_2_out, nG1);
  Register #(.width(4)) register_1 (.D({D4, D3, D2, D1}), .en(and_1_out), .clk(CLK), .Q(register_1_q), .clr(not_3_out));
  not not_3 (not_3_out, nCLR);
  not not_4 (not_4_out, M);
  and and_2 (and_2_out, not_4_out, not_5_out);
  not not_5 (not_5_out, N);
  assign {Q4, Q3, Q2, Q1} = and_2_out ? register_1_q : 4'bz;  // Controlled_Buffer controlled_buffer_1

  // Other names for the same wires on the sheet: D[3:0] = {D4, D3, D2, D1}; Q[3:0] = {Q4, Q3, Q2, Q1}
endmodule

module gp_register_16 (
  input  [15:0] inn
);

  gp_register gp_register_1 ();  // open: nWE, CLOCK, BIN, nBOUT_EN, BOUT, Q
  gp_register gp_register_2 (.BIN(inn[15:8]));  // open: nWE, CLOCK, nBOUT_EN, BOUT, Q
endmodule

module T74HC238 (
  input  A,
  input  B,
  input  C,
  input  nG2A,
  input  nG2B,
  input  G1,
  output Y0,
  output Y1,
  output Y2,
  output Y3,
  output Y4,
  output Y5,
  output Y6,
  output Y7
);

  wire n74138_1_pin7, n74138_1_pin9, n74138_1_pin10, n74138_1_pin11, n74138_1_pin12, n74138_1_pin13,
       n74138_1_pin14, n74138_1_pin15;

  _74138 #(.ShowInternalStructure("true")) u_74138_1 (
    .pin1(A), .pin2(B), .pin3(C), .pin4(nG2A), .pin5(nG2B), .pin6(G1), .pin7(n74138_1_pin7),
    .pin15(n74138_1_pin15), .pin14(n74138_1_pin14), .pin13(n74138_1_pin13), .pin12(n74138_1_pin12),
    .pin11(n74138_1_pin11), .pin10(n74138_1_pin10), .pin9(n74138_1_pin9));
  not not_1 (Y0, n74138_1_pin15);
  not not_2 (Y1, n74138_1_pin14);
  not not_3 (Y2, n74138_1_pin13);
  not not_4 (Y3, n74138_1_pin12);
  not not_5 (Y4, n74138_1_pin11);
  not not_6 (Y5, n74138_1_pin10);
  not not_7 (Y6, n74138_1_pin9);
  not not_8 (Y7, n74138_1_pin7);
endmodule

module CY7C199 (
  input  A0,
  input  A1,
  input  A2,
  input  A3,
  input  A4,
  input  A5,
  input  A6,
  input  A7,
  input  A8,
  input  A9,
  input  A10,
  input  A11,
  input  A12,
  input  A13,
  input  A14,
  input  I0,
  input  I1,
  input  I2,
  input  I3,
  input  I4,
  input  I5,
  input  I6,
  input  I7,
  input  nWE,
  input  nOE,
  input  nCE,
  output O0,
  output O1,
  output O2,
  output O3,
  output O4,
  output O5,
  output O6,
  output O7
);

  wire and_1_out, and_2_out, not_1_out, not_2_out, not_3_out;
  wire [7:0] ram_1_dout;

  not not_1 (not_1_out, nCE);
  not not_2 (not_2_out, nWE);
  and and_1 (and_1_out, not_1_out, not_2_out);
  RAM #(.addrWidth(15), .trigger("high"), .\type ("nonvolatile")) ram_1 (
    .addr({A14, A13, A12, A11, A10, A9, A8, A7, A6, A5, A4, A3, A2, A1, A0}), .we(and_1_out), .oe(1'b1),
    .din({I7, I6, I5, I4, I3, I2, I1, I0}), .dout(ram_1_dout));
  not not_3 (not_3_out, nOE);
  and and_2 (and_2_out, not_3_out, nWE, not_1_out);
  assign {O7, O6, O5, O4, O3, O2, O1, O0} = and_2_out ? ram_1_dout : 8'bz;  // Controlled_Buffer controlled_buffer_1

  // Other names for the same wires on the sheet: ADDR[14:0] = {A14, A13, A12, A11, A10, A9, A8, A7, A6, A5, A4, A3, A2, A1, A0}

  // Notes on the sheet:
  //   nWE: initial=0x1
  //   nOE: initial=0x1
  //   nCE: initial=0x1
endmodule

module SST39SF010A (
  input  A0,
  input  A1,
  input  A2,
  input  A3,
  input  A4,
  input  A5,
  input  A6,
  input  A7,
  input  A8,
  input  A9,
  input  A10,
  input  A11,
  input  A12,
  input  A13,
  input  A14,
  input  A15,
  input  A16,
  input  nOE,
  input  nCE,
  input  [1:0] ROM_SELECT,
  output O0,
  output O1,
  output O2,
  output O3,
  output O4,
  output O5,
  output O6,
  output O7
);

  wire and_1_out, and_2_out, and_3_out, and_4_out, not_1_out, not_2_out, not_3_out, not_4_out, not_5_out,
       not_6_out, not_7_out, not_8_out;
  wire [3:0] bit_extender_1_out;
  wire [7:0] controlled_buffer_1_out, controlled_buffer_2_out, controlled_buffer_3_out,
       controlled_buffer_4_out, MEM_ROM_data, rom_1_data, UCODE_ROM0_data, UCODE_ROM1_data;

  ROM #(.addrWidth(17)) UCODE_ROM1 (
    .addr({A16, A15, A14, A13, A12, A11, A10, A9, A8, A7, A6, A5, A4, A3, A2, A1, A0}), .data(UCODE_ROM1_data));
  ROM #(.addrWidth(17)) MEM_ROM (
    .addr({A16, A15, A14, A13, A12, A11, A10, A9, A8, A7, A6, A5, A4, A3, A2, A1, A0}), .data(MEM_ROM_data));
  ROM #(.addrWidth(17)) rom_1 (
    .addr({A16, A15, A14, A13, A12, A11, A10, A9, A8, A7, A6, A5, A4, A3, A2, A1, A0}), .data(rom_1_data));
  ROM #(.addrWidth(17)) UCODE_ROM0 (
    .addr({A16, A15, A14, A13, A12, A11, A10, A9, A8, A7, A6, A5, A4, A3, A2, A1, A0}), .data(UCODE_ROM0_data));
  not not_1 (not_1_out, nOE);
  and and_1 (and_1_out, not_1_out, not_2_out);
  not not_2 (not_2_out, nCE);
  not not_3 (not_3_out, nOE);
  and and_2 (and_2_out, not_3_out, not_4_out);
  not not_4 (not_4_out, nCE);
  not not_5 (not_5_out, nOE);
  and and_3 (and_3_out, not_5_out, not_6_out);
  not not_6 (not_6_out, nCE);
  not not_7 (not_7_out, nOE);
  and and_4 (and_4_out, not_7_out, not_8_out);
  not not_8 (not_8_out, nCE);
  assign controlled_buffer_1_out = and_1_out ? UCODE_ROM0_data : 8'bz;  // Controlled_Buffer controlled_buffer_1
  assign controlled_buffer_2_out = and_2_out ? UCODE_ROM1_data : 8'bz;  // Controlled_Buffer controlled_buffer_2
  assign controlled_buffer_3_out = and_3_out ? MEM_ROM_data : 8'bz;  // Controlled_Buffer controlled_buffer_3
  assign controlled_buffer_4_out = and_4_out ? rom_1_data : 8'bz;  // Controlled_Buffer controlled_buffer_4
  Hex_Digit_Display L4 (.value(bit_extender_1_out));  // open: dp
  Hex_Digit_Display L3 (.value({A15, A14, A13, A12}));  // open: dp
  assign bit_extender_1_out = {{3{1'b0}}, A16};  // Bit_Extender bit_extender_1
  Hex_Digit_Display L2 (.value({A11, A10, A9, A8}));  // open: dp
  Hex_Digit_Display L1 (.value({A7, A6, A5, A4}));  // open: dp
  Hex_Digit_Display L0 (.value({A3, A2, A1, A0}));  // open: dp
  Multiplexer #(.select(2), .width(8)) multiplexer_1 (
    .in0(controlled_buffer_1_out), .in1(controlled_buffer_2_out), .in2(controlled_buffer_3_out),
    .in3(controlled_buffer_4_out), .out({O7, O6, O5, O4, O3, O2, O1, O0}), .sel(ROM_SELECT));

  // Other names for the same wires on the sheet: ADDR[16:0] = {A16, A15, A14, A13, A12, A11, A10, A9, A8, A7, A6, A5, A4, A3, A2, A1, A0}

  // Notes on the sheet:
  //   nOE: initial=0x1
  //   nCE: initial=0x1
  //   control rom 1
  //   control rom 0
  //   memory rom
  //   video control rom
  //   contents of UCODE_ROM1 (hex, n*v repeats v):
  //   704*1 64*0 192*1 32*0 3680*1 64*0 192*1 32*0 3232*1 480*80 32*82 32*8a 32*80 32*8a 32*80 32*8a 32*80
  //   64*0 160*80 32*88 32*0 256*80 32*82 224*80 32*82 224*80 32*82 224*80 32*82 32*83 32*82 32*83 32*4e
  //   32*83 32*88 32*83 32*4e 32*84 160*80 32*82 32*80 256*88 32*8a 32*80 32*8a 32*80 32*8a 32*80 32*8a 25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
  //   contents of MEM_ROM (hex, n*v repeats v):
  //   3f ff e0 38 0 38 a 5c 1 26 38 0 38 11 5c 1 a8 a 7 3f 44 cf 3e 32 f 95 2 74 3d bd 40 ae 0 48 4c 9a 1
  //   5f 0 16 a 7 3f 44 d0 3e 30 77 95 2 74 3d bd 40 ae 0 48 4c 9a 1 5f 0 2d a 7 3f 44 d1 3e 30 af 95 2 74
  //   3d bd 40 ae 0 48 4c 9a 1 5f 0 44 a 7 3f 44 d2 3e 30 af 95 2 74 3d bd 40 ae 0 48 4c 9a 1 5f 0 5b a 7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
  //   contents of rom_1 (hex, n*v repeats v):
  //   39*78 6c 7c 6*7e 7c 78 7c 39*78 64 7c 6*7e 7c 78 7c 39*78 6c 7c 6*7e 7c 78 7c 39*78 64 7c 6*7e 7c 78
  //   7c 39*78 6c 7c 6*7e 7c 78 7c 39*78 64 7c 6*7e 7c 78 7c 39*78 6c 7c 6*7e 7c 78 7c 39*78 64 7c 6*7e 7c
  //   78 7c 39*78 6c 7c 6*7e 7c 78 7c 39*78 64 7c 6*7e 7c 78 7c 39*78 6c 7c 6*7e 7c 78 7c 39*78 64 7c 6*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
  //   contents of UCODE_ROM0 (hex, n*v repeats v):
  //   704*f1 64*5 192*f1 32*5 3680*f1 64*5 192*f1 32*5 3232*f1 288*0 32*88 32*0 32*8f 32*0 32*8d 32*0
  //   32*83 32*68 32*0 32*6f 32*0 32*6d 32*0 64*5 96*7 32*0 32*7 32*4 32*5 64*0 32*88 32*0 32*8f 32*0
  //   32*8d 32*0 32*83 32*0 32*88 32*0 32*8f 32*0 32*8d 32*0 32*83 32*0 32*88 32*0 32*8f 32*0 32*8d 32*0
  //   32*83 32*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
endmodule

module T74HC191 (
  input  A,
  input  B,
  input  C,
  input  D,
  input  nCLKEN,
  input  D_nU,
  input  CLK,
  input  nLOAD,
  output Qa,
  output Qb,
  output Qc,
  output Qd,
  output MAX_MIN,
  output nRCO
);

  wire not_1_out, not_2_out, not_3_out, not_4_out, not_5_out;

  not not_1 (not_1_out, nCLKEN);
  not not_2 (not_2_out, nCLKEN);
  not not_3 (not_3_out, CLK);
  not not_4 (not_4_out, D_nU);
  not not_5 (not_5_out, nLOAD);
  Counter #(.max('hf), .width(4)) counter_1 (
    .load(not_5_out), .D({D, C, B, A}), .count(not_1_out), .Q({Qd, Qc, Qb, Qa}), .carry(MAX_MIN),
    .up(not_4_out), .clk(CLK), .clr(1'b0));
  nand nand_1 (nRCO, MAX_MIN, not_2_out, not_3_out);

  // Other names for the same wires on the sheet: D_t[3:0] = {D, C, B, A}; Q[3:0] = {Qd, Qc, Qb, Qa}
endmodule

module T74HC574 (
  input  D0,
  input  D1,
  input  D2,
  input  D3,
  input  D4,
  input  D5,
  input  D6,
  input  D7,
  input  nOE,
  input  CLK,
  output O0,
  output O1,
  output O2,
  output O3,
  output O4,
  output O5,
  output O6,
  output O7
);

  wire not_1_out;
  wire [7:0] register_1_q;

  Register register_1 (.D({D7, D6, D5, D4, D3, D2, D1, D0}), .en(1'b1), .clk(CLK), .Q(register_1_q), .clr(1'b0));
  not not_1 (not_1_out, nOE);
  assign {O7, O6, O5, O4, O3, O2, O1, O0} = not_1_out ? register_1_q : 8'bz;  // Controlled_Buffer controlled_buffer_1
  Hex_Digit_Display L1 (.value({D7, D6, D5, D4}));  // open: dp
  Hex_Digit_Display L0 (.value({D3, D2, D1, D0}));  // open: dp

  // Other names for the same wires on the sheet: Q[7:0] = {O7, O6, O5, O4, O3, O2, O1, O0}

  // Notes on the sheet:
  //   nOE: initial=0x1
endmodule
